// Logisim project ALUpj3.circ as structural Verilog: 14 circuits, main circuit main
module main (
  input  [31:0] Instruccion,
  input  in_2,
  input  in_3
);

  wire decoder_1_load_store, decoder_1_tipo_b, decoder_1_tipo_i, decoder_1_tipo_r;
  wire [23:0] bit_extender_1_out;
  wire [31:0] program_counter_1_output;

  Program_Counter program_counter_1 (
    .offset_mux(in_2), .clear(in_3), .OUTPUT(program_counter_1_output));  // open: Inmediato
  Bit_Extender #(.in_width(32), .out_width(24)) bit_extender_1 (
    .in(program_counter_1_output), .out(bit_extender_1_out));
  Memory_Manager_Instrucciones memory_manager_instrucciones_1 (
    .address_high(bit_extender_1_out), .str_high(1'b1), .data_low(Instruccion));
  Decoder decoder_1 (
    .instruction(Instruccion), .Tipo_B(decoder_1_tipo_b), .Load_Store(decoder_1_load_store),
    .Tipo_R(decoder_1_tipo_r), .Tipo_I(decoder_1_tipo_i));
  ALU alu_1 ();  // open: Input_high, Input_low, Input_high_2, Input_low_2, Output_high, Output_low, Offset_shift, control
endmodule

module ALU (
  input  [31:0] Input_high,
  input  [31:0] Input_low,
  input  [31:0] Input_high_2,
  input  [31:0] Input_low_2,
  input  [31:0] Offset_shift,
  input  [3:0] control,
  output [31:0] Output_high,
  output [31:0] Output_low
);

  wire adder_2_cout, subtractor_2_bout;
  wire [31:0] adder_1_out, adder_2_out, and_1_out, and_2_out, or_1_out, or_2_out, shift_left_1_salida_high,
       shift_left_1_salida_low, shift_right_1_salida_high, shift_right_1_salida_low, shifter_1_out,
       shifter_2_out, shifter_3_out, shifter_4_out, subtractor_1_out, subtractor_2_out, xor_1_out, xor_2_out;

  Adder #(.width(32)) adder_1 (.a(Input_high), .b(Input_high_2), .out(adder_1_out), .cin(adder_2_cout));  // open: cout
  Subtractor #(.width(32)) subtractor_1 (
    .a(Input_high), .b(Input_high_2), .out(subtractor_1_out), .bin(subtractor_2_bout));  // open: bout
  assign and_1_out = Input_high & Input_high_2;  // AND_Gate and_1, 32 bits wide
  assign or_1_out = Input_high | Input_high_2;  // OR_Gate or_1, 32 bits wide
  assign xor_1_out = Input_high ^ Input_high_2;  // XOR_Gate xor_1, 32 bits wide
  Shift_Left shift_left_1 (
    .High(Input_high), .Corrimiento(Offset_shift), .Low(Input_low_2), .Salida_high(shift_left_1_salida_high),
    .Salida_low(shift_left_1_salida_low));
  Shift_right shift_right_1 (
    .High(Input_high), .Corrimiento(Offset_shift), .Low(Input_low), .Salida_high(shift_right_1_salida_high),
    .Salida_Low(shift_right_1_salida_low));
  Shifter #(.width(32), .shift("ar")) shifter_1 (.out(shifter_1_out));  // open: in, dist
  Shifter #(.width(32), .shift("rr")) shifter_2 (.out(shifter_2_out));  // open: in, dist
  Adder #(.width(32)) adder_2 (.a(Input_low), .b(Input_low_2), .out(adder_2_out), .cout(adder_2_cout));  // open: cin
  Subtractor #(.width(32)) subtractor_2 (
    .a(Input_low), .b(Input_low_2), .out(subtractor_2_out), .bout(subtractor_2_bout));  // open: bin
  assign and_2_out = Input_low & Input_low_2;  // AND_Gate and_2, 32 bits wide
  assign or_2_out = Input_low | Input_low_2;  // OR_Gate or_2, 32 bits wide
  assign xor_2_out = Input_low ^ Input_low_2;  // XOR_Gate xor_2, 32 bits wide
  Shifter #(.width(32), .shift("ar")) shifter_3 (.out(shifter_3_out));  // open: in, dist
  Shifter #(.width(32), .shift("rr")) shifter_4 (.out(shifter_4_out));  // open: in, dist
  Multiplexer #(.select(4), .width(32)) multiplexer_1 (
    .in0(adder_1_out), .in1(subtractor_1_out), .in2(and_1_out), .in3(or_1_out), .in4(xor_1_out),
    .in5(shift_left_1_salida_high), .in6(shift_right_1_salida_high), .in7(shifter_1_out),
    .in8(shifter_2_out), .in9({32{1'b0}}), .in10({32{1'b0}}), .in11({32{1'b0}}), .in12({32{1'b0}}),
    .in13({32{1'b0}}), .in14({32{1'b0}}), .in15({32{1'b0}}), .out(Output_high), .sel(control), .en(1'b1));
  Multiplexer #(.select(4), .width(32)) multiplexer_2 (
    .in0(adder_2_out), .in1(subtractor_2_out), .in2(and_2_out), .in3(or_2_out), .in4(xor_2_out),
    .in5(shift_left_1_salida_low), .in6(shift_right_1_salida_low), .in7(shifter_3_out), .in8(shifter_4_out),
    .in9({32{1'b0}}), .in10({32{1'b0}}), .in11({32{1'b0}}), .in12({32{1'b0}}), .in13({32{1'b0}}),
    .in14({32{1'b0}}), .in15({32{1'b0}}), .out(Output_low), .sel(control), .en(1'b1));

  // Other names for the same wires on the sheet: Input_High_1[31:0] = Input_high; Input_low_1[31:0] = Input_low
endmodule

module Memory_Manager_Instrucciones (
  input  [23:0] address_high,
  input  [31:0] data_low,
  input  str_high
);

  ROM #(.addrWidth(24), .dataWidth(32)) rom_1 (.addr(address_high), .data(data_low), .sel(str_high));
endmodule

module Memory_Manager_Datos (
  input  [23:0] address_high,
  input  [31:0] data_high,
  input  set_high,
  input  clear,
  input  ld_high
);

  wire ckl;

  Clock clock_1 (.out(ckl));
  RAM #(.addrWidth(24), .dataWidth(32)) ram_1 (
    .addr(address_high), .data(data_high), .sel(set_high), .clk(ckl), .ld(ld_high), .clr(clear));
endmodule

module Register_File (
  input  _4,
  input  _3,
  input  _2,
  input  _1,
  input  _0,
  input  [31:0] Input_high,
  input  _4_2,
  input  _3_2,
  input  _2_2,
  input  _1_2,
  input  _0_2,
  input  [31:0] Input_low,
  output [31:0] Output_high,
  output [31:0] Output_low
);

  wire and_1_out, and_2_out, and_3_out, and_4_out, and_5_out, and_6_out, and_7_out, and_8_out, and_9_out,
       and_10_out, and_11_out, and_12_out, and_13_out, and_14_out, and_15_out, and_16_out, and_17_out,
       and_18_out, and_19_out, and_20_out, and_21_out, and_22_out, and_23_out, and_24_out, and_25_out,
       and_26_out, and_27_out, and_28_out, and_29_out, and_30_out, and_31_out, and_32_out, and_33_out,
       and_34_out, and_35_out, and_36_out, and_37_out, and_38_out, and_39_out, and_40_out, and_41_out,
       and_42_out, and_43_out, and_44_out, and_45_out, and_46_out, and_47_out, and_48_out, and_49_out,
       and_50_out, and_51_out, and_52_out, and_53_out, and_54_out, and_55_out, and_56_out, and_57_out,
       and_58_out, and_59_out, and_60_out, and_61_out, and_62_out, and_63_out, and_64_out, clock, not_1_out,
       not_2_out, not_3_out, not_4_out, not_5_out, not_6_out, not_7_out, not_8_out, not_9_out, not_10_out,
       not_11_out, not_12_out, not_13_out, not_14_out, not_15_out, not_16_out, not_17_out, not_18_out,
       not_19_out, not_20_out, not_21_out, not_22_out, not_23_out, not_24_out, not_25_out, not_26_out,
       not_27_out, not_28_out, not_29_out, not_30_out, not_31_out, not_32_out, not_33_out, not_34_out,
       not_35_out, not_36_out, not_37_out, not_38_out, not_39_out, not_40_out, not_41_out, not_42_out,
       not_43_out, not_44_out, not_45_out, not_46_out, not_47_out, not_48_out, not_49_out, not_50_out,
       not_51_out, not_52_out, not_53_out, not_54_out, not_55_out, not_56_out, not_57_out, not_58_out,
       not_59_out, not_60_out, not_61_out, not_62_out, not_63_out, not_64_out, not_65_out, not_66_out,
       not_67_out, not_68_out, not_69_out, not_70_out, not_71_out, not_72_out, not_73_out, not_74_out,
       not_75_out, not_76_out, not_77_out, not_78_out, not_79_out, not_80_out, not_81_out, not_82_out,
       not_83_out, not_84_out, not_85_out, not_86_out, not_87_out, not_88_out, not_89_out, not_90_out,
       not_91_out, not_92_out, not_93_out, not_94_out, not_95_out, not_96_out, not_97_out, not_98_out,
       not_99_out, not_100_out, not_101_out, not_102_out, not_103_out, not_104_out, not_105_out, not_106_out,
       not_107_out, not_108_out, not_109_out, not_110_out, not_111_out, not_112_out, not_113_out,
       not_114_out, not_115_out, not_116_out, not_117_out, not_118_out, not_119_out, not_120_out,
       not_121_out, not_122_out, not_123_out, not_124_out, not_125_out, not_126_out, not_127_out,
       not_128_out, not_129_out, not_130_out, not_131_out, not_132_out, not_133_out, not_134_out,
       not_135_out, not_136_out, not_137_out, not_138_out, not_139_out, not_140_out, not_141_out,
       not_142_out, not_143_out, not_144_out, not_145_out, not_146_out, not_147_out, not_148_out,
       not_149_out, not_150_out, not_151_out, not_152_out, not_153_out, not_154_out, not_155_out,
       not_156_out, not_157_out, not_158_out, not_159_out, not_160_out;
  wire [31:0] undriven, undriven_2, undriven_3, undriven_4, undriven_5, undriven_6, undriven_7, undriven_8,
       undriven_9, undriven_10, x0_2_q, x0_q, x1_2_q, x1_q, x3_2_q, x3_q, x4_2_q, x4_3_q, x4_4_q, x4_5_q,
       x4_6_q, x4_q, x6_2_q, x6_q, x7_2_q, x7_q, x8_2_q, x8_q, x9_2_q, x9_3_q, x9_4_q, x9_q, x11_2_q, x11_q,
       x12_2_q, x12_q, x13_2_q, x13_q, x14_2_q, x14_q, x15_2_q, x15_q, x16_2_q, x16_q, x17_2_q, x17_q,
       x18_2_q, x18_q, x19_2_q, x19_q, x20_2_q, x20_q, x21_2_q, x21_3_q, x21_4_q, x21_q, x23_2_q, x23_3_q,
       x23_4_q, x23_q, x25_2_q, x25_q, x26_2_q, x26_q, x27_2_q, x27_q, x28_2_q, x28_q, x29_2_q, x29_q,
       x30_2_q, x30_q, x31_2_q, x31_q;

  not not_1 (not_1_out, _1);
  not not_2 (not_2_out, _2);
  not not_3 (not_3_out, _3);
  not not_4 (not_4_out, _4);
  not not_5 (not_5_out, _0);
  not not_6 (not_6_out, _2);
  not not_7 (not_7_out, _3);
  not not_8 (not_8_out, _4);
  not not_9 (not_9_out, _2);
  not not_10 (not_10_out, _3);
  not not_11 (not_11_out, _4);
  not not_12 (not_12_out, _0);
  not not_13 (not_13_out, _1);
  not not_14 (not_14_out, _3);
  not not_15 (not_15_out, _4);
  not not_16 (not_16_out, _1);
  not not_17 (not_17_out, _3);
  not not_18 (not_18_out, _4);
  not not_19 (not_19_out, _0);
  not not_20 (not_20_out, _3);
  not not_21 (not_21_out, _4);
  not not_22 (not_22_out, _3);
  not not_23 (not_23_out, _4);
  not not_24 (not_24_out, _0);
  not not_25 (not_25_out, _1);
  not not_26 (not_26_out, _2);
  not not_27 (not_27_out, _4);
  not not_28 (not_28_out, _1);
  not not_29 (not_29_out, _2);
  not not_30 (not_30_out, _4);
  not not_31 (not_31_out, _0);
  not not_32 (not_32_out, _2);
  not not_33 (not_33_out, _4);
  not not_34 (not_34_out, _2);
  not not_35 (not_35_out, _4);
  not not_36 (not_36_out, _0);
  not not_37 (not_37_out, _1);
  not not_38 (not_38_out, _4);
  not not_39 (not_39_out, _1);
  not not_40 (not_40_out, _4);
  not not_41 (not_41_out, _0);
  not not_42 (not_42_out, _4);
  not not_43 (not_43_out, _4);
  not not_44 (not_44_out, _0);
  not not_45 (not_45_out, _1);
  not not_46 (not_46_out, _2);
  not not_47 (not_47_out, _3);
  not not_48 (not_48_out, _1);
  not not_49 (not_49_out, _2);
  not not_50 (not_50_out, _3);
  not not_51 (not_51_out, _0);
  not not_52 (not_52_out, _2);
  not not_53 (not_53_out, _3);
  not not_54 (not_54_out, _2);
  not not_55 (not_55_out, _3);
  not not_56 (not_56_out, _0);
  not not_57 (not_57_out, _1);
  not not_58 (not_58_out, _3);
  not not_59 (not_59_out, _1);
  not not_60 (not_60_out, _3);
  not not_61 (not_61_out, _0);
  not not_62 (not_62_out, _3);
  not not_63 (not_63_out, _3);
  not not_64 (not_64_out, _0);
  not not_65 (not_65_out, _1);
  not not_66 (not_66_out, _2);
  not not_67 (not_67_out, _1);
  not not_68 (not_68_out, _2);
  not not_69 (not_69_out, _0);
  not not_70 (not_70_out, _2);
  not not_71 (not_71_out, _2);
  not not_72 (not_72_out, _0);
  not not_73 (not_73_out, _1);
  not not_74 (not_74_out, _1);
  not not_75 (not_75_out, _0);
  not not_76 (not_76_out, _0);
  not not_77 (not_77_out, _1);
  not not_78 (not_78_out, _2);
  not not_79 (not_79_out, _3);
  not not_80 (not_80_out, _4);
  not not_81 (not_81_out, _1_2);
  not not_82 (not_82_out, _2_2);
  not not_83 (not_83_out, _3_2);
  not not_84 (not_84_out, _4_2);
  not not_85 (not_85_out, _0_2);
  not not_86 (not_86_out, _2_2);
  not not_87 (not_87_out, _3_2);
  not not_88 (not_88_out, _4_2);
  not not_89 (not_89_out, _2_2);
  not not_90 (not_90_out, _3_2);
  not not_91 (not_91_out, _4_2);
  not not_92 (not_92_out, _0_2);
  not not_93 (not_93_out, _1_2);
  not not_94 (not_94_out, _3_2);
  not not_95 (not_95_out, _4_2);
  not not_96 (not_96_out, _1_2);
  not not_97 (not_97_out, _3_2);
  not not_98 (not_98_out, _4_2);
  not not_99 (not_99_out, _0_2);
  not not_100 (not_100_out, _3_2);
  not not_101 (not_101_out, _4_2);
  not not_102 (not_102_out, _3_2);
  not not_103 (not_103_out, _4_2);
  not not_104 (not_104_out, _0_2);
  not not_105 (not_105_out, _1_2);
  not not_106 (not_106_out, _2_2);
  not not_107 (not_107_out, _4_2);
  not not_108 (not_108_out, _1_2);
  not not_109 (not_109_out, _2_2);
  not not_110 (not_110_out, _4_2);
  not not_111 (not_111_out, _0_2);
  not not_112 (not_112_out, _2_2);
  not not_113 (not_113_out, _4_2);
  not not_114 (not_114_out, _2_2);
  not not_115 (not_115_out, _4_2);
  not not_116 (not_116_out, _0_2);
  not not_117 (not_117_out, _1_2);
  not not_118 (not_118_out, _4_2);
  not not_119 (not_119_out, _1_2);
  not not_120 (not_120_out, _4_2);
  not not_121 (not_121_out, _0_2);
  not not_122 (not_122_out, _4_2);
  not not_123 (not_123_out, _4_2);
  not not_124 (not_124_out, _0_2);
  not not_125 (not_125_out, _1_2);
  not not_126 (not_126_out, _2_2);
  not not_127 (not_127_out, _3_2);
  not not_128 (not_128_out, _1_2);
  not not_129 (not_129_out, _2_2);
  not not_130 (not_130_out, _3_2);
  not not_131 (not_131_out, _0_2);
  not not_132 (not_132_out, _2_2);
  not not_133 (not_133_out, _3_2);
  not not_134 (not_134_out, _2_2);
  not not_135 (not_135_out, _3_2);
  not not_136 (not_136_out, _0_2);
  not not_137 (not_137_out, _1_2);
  not not_138 (not_138_out, _3_2);
  not not_139 (not_139_out, _1_2);
  not not_140 (not_140_out, _3_2);
  not not_141 (not_141_out, _0_2);
  not not_142 (not_142_out, _3_2);
  not not_143 (not_143_out, _3_2);
  not not_144 (not_144_out, _0_2);
  not not_145 (not_145_out, _1_2);
  not not_146 (not_146_out, _2_2);
  not not_147 (not_147_out, _1_2);
  not not_148 (not_148_out, _2_2);
  not not_149 (not_149_out, _0_2);
  not not_150 (not_150_out, _2_2);
  not not_151 (not_151_out, _2_2);
  not not_152 (not_152_out, _0_2);
  not not_153 (not_153_out, _1_2);
  not not_154 (not_154_out, _1_2);
  not not_155 (not_155_out, _0_2);
  not not_156 (not_156_out, _0_2);
  not not_157 (not_157_out, _1_2);
  not not_158 (not_158_out, _2_2);
  not not_159 (not_159_out, _3_2);
  not not_160 (not_160_out, _4_2);
  and and_1 (and_1_out, _0, not_1_out, not_2_out, not_3_out, not_4_out);
  and and_2 (and_2_out, not_5_out, _1, not_6_out, not_7_out, not_8_out);
  and and_3 (and_3_out, _0, _1, not_9_out, not_10_out, not_11_out);
  and and_4 (and_4_out, not_12_out, not_13_out, _2, not_14_out, not_15_out);
  and and_5 (and_5_out, _0, not_16_out, _2, not_17_out, not_18_out);
  and and_6 (and_6_out, not_19_out, _1, _2, not_20_out, not_21_out);
  and and_7 (and_7_out, _0, _1, _2, not_22_out, not_23_out);
  and and_8 (and_8_out, not_24_out, not_25_out, not_26_out, _3, not_27_out);
  and and_9 (and_9_out, _0, not_28_out, not_29_out, _3, not_30_out);
  and and_10 (and_10_out, not_31_out, _1, not_32_out, _3, not_33_out);
  and and_11 (and_11_out, _0, _1, not_34_out, _3, not_35_out);
  and and_12 (and_12_out, not_36_out, not_37_out, _2, _3, not_38_out);
  and and_13 (and_13_out, _0, not_39_out, _2, _3, not_40_out);
  and and_14 (and_14_out, not_41_out, _1, _2, _3, not_42_out);
  and and_15 (and_15_out, _0, _1, _2, _3, not_43_out);
  and and_16 (and_16_out, not_44_out, not_45_out, not_46_out, not_47_out, _4);
  and and_17 (and_17_out, _0, not_48_out, not_49_out, not_50_out, _4);
  and and_18 (and_18_out, not_51_out, _1, not_52_out, not_53_out, _4);
  and and_19 (and_19_out, _0, _1, not_54_out, not_55_out, _4);
  and and_20 (and_20_out, not_56_out, not_57_out, _2, not_58_out, _4);
  and and_21 (and_21_out, _0, not_59_out, _2, not_60_out, _4);
  and and_22 (and_22_out, not_61_out, _1, _2, not_62_out, _4);
  and and_23 (and_23_out, _0, _1, _2, not_63_out, _4);
  and and_24 (and_24_out, not_64_out, not_65_out, not_66_out, _3, _4);
  and and_25 (and_25_out, _0, not_67_out, not_68_out, _3, _4);
  and and_26 (and_26_out, not_69_out, _1, not_70_out, _3, _4);
  and and_27 (and_27_out, _0, _1, not_71_out, _3, _4);
  and and_28 (and_28_out, not_72_out, not_73_out, _2, _3, _4);
  and and_29 (and_29_out, _0, not_74_out, _2, _3, _4);
  and and_30 (and_30_out, not_75_out, _1, _2, _3, _4);
  and and_31 (and_31_out, _0, _1, _2, _3, _4);
  and and_32 (and_32_out, not_76_out, not_77_out, not_78_out, not_79_out, not_80_out);
  and and_33 (and_33_out, _0_2, not_81_out, not_82_out, not_83_out, not_84_out);
  and and_34 (and_34_out, not_85_out, _1_2, not_86_out, not_87_out, not_88_out);
  and and_35 (and_35_out, _0_2, _1_2, not_89_out, not_90_out, not_91_out);
  and and_36 (and_36_out, not_92_out, not_93_out, _2_2, not_94_out, not_95_out);
  and and_37 (and_37_out, _0_2, not_96_out, _2_2, not_97_out, not_98_out);
  and and_38 (and_38_out, not_99_out, _1_2, _2_2, not_100_out, not_101_out);
  and and_39 (and_39_out, _0_2, _1_2, _2_2, not_102_out, not_103_out);
  and and_40 (and_40_out, not_104_out, not_105_out, not_106_out, _3_2, not_107_out);
  and and_41 (and_41_out, _0_2, not_108_out, not_109_out, _3_2, not_110_out);
  and and_42 (and_42_out, not_111_out, _1_2, not_112_out, _3_2, not_113_out);
  and and_43 (and_43_out, _0_2, _1_2, not_114_out, _3_2, not_115_out);
  and and_44 (and_44_out, not_116_out, not_117_out, _2_2, _3_2, not_118_out);
  and and_45 (and_45_out, _0_2, not_119_out, _2_2, _3_2, not_120_out);
  and and_46 (and_46_out, not_121_out, _1_2, _2_2, _3_2, not_122_out);
  and and_47 (and_47_out, _0_2, _1_2, _2_2, _3_2, not_123_out);
  and and_48 (and_48_out, not_124_out, not_125_out, not_126_out, not_127_out, _4_2);
  and and_49 (and_49_out, _0_2, not_128_out, not_129_out, not_130_out, _4_2);
  and and_50 (and_50_out, not_131_out, _1_2, not_132_out, not_133_out, _4_2);
  and and_51 (and_51_out, _0_2, _1_2, not_134_out, not_135_out, _4_2);
  and and_52 (and_52_out, not_136_out, not_137_out, _2_2, not_138_out, _4_2);
  and and_53 (and_53_out, _0_2, not_139_out, _2_2, not_140_out, _4_2);
  and and_54 (and_54_out, not_141_out, _1_2, _2_2, not_142_out, _4_2);
  and and_55 (and_55_out, _0_2, _1_2, _2_2, not_143_out, _4_2);
  and and_56 (and_56_out, not_144_out, not_145_out, not_146_out, _3_2, _4_2);
  and and_57 (and_57_out, _0_2, not_147_out, not_148_out, _3_2, _4_2);
  and and_58 (and_58_out, not_149_out, _1_2, not_150_out, _3_2, _4_2);
  and and_59 (and_59_out, _0_2, _1_2, not_151_out, _3_2, _4_2);
  and and_60 (and_60_out, not_152_out, not_153_out, _2_2, _3_2, _4_2);
  and and_61 (and_61_out, _0_2, not_154_out, _2_2, _3_2, _4_2);
  and and_62 (and_62_out, not_155_out, _1_2, _2_2, _3_2, _4_2);
  and and_63 (and_63_out, _0_2, _1_2, _2_2, _3_2, _4_2);
  and and_64 (and_64_out, not_156_out, not_157_out, not_158_out, not_159_out, not_160_out);
  Register #(.width(32)) x1 (.D(Input_high), .en(and_1_out), .Q(x1_q), .clk(clock));  // open: clr
  Register #(.width(32)) x4 (.D(Input_high), .en(and_2_out), .Q(x4_q), .clk(clock));  // open: clr
  Register #(.width(32)) x3 (.D(Input_high), .en(and_3_out), .Q(x3_q), .clk(clock));  // open: clr
  Register #(.width(32)) x4_2 (.D(Input_high), .en(and_4_out), .Q(x4_2_q), .clk(clock));  // open: clr
  Register #(.width(32)) x4_3 (.D(Input_high), .en(and_5_out), .Q(x4_3_q), .clk(clock));  // open: clr
  Register #(.width(32)) x6 (.D(Input_high), .en(and_6_out), .Q(x6_q), .clk(clock));  // open: clr
  Register #(.width(32)) x7 (.D(Input_high), .en(and_7_out), .Q(x7_q), .clk(clock));  // open: clr
  Register #(.width(32)) x8 (.D(Input_high), .en(and_8_out), .Q(x8_q), .clk(clock));  // open: clr
  Register #(.width(32)) x9 (.D(Input_high), .en(and_9_out), .Q(x9_q), .clk(clock));  // open: clr
  Register #(.width(32)) x9_2 (.D(Input_high), .en(and_10_out), .Q(x9_2_q), .clk(clock));  // open: clr
  Register #(.width(32)) x11 (.D(Input_high), .en(and_11_out), .Q(x11_q), .clk(clock));  // open: clr
  Register #(.width(32)) x12 (.D(Input_high), .en(and_12_out), .Q(x12_q), .clk(clock));  // open: clr
  Register #(.width(32)) x13 (.D(Input_high), .en(and_13_out), .Q(x13_q), .clk(clock));  // open: clr
  Register #(.width(32)) x14 (.D(Input_high), .en(and_14_out), .Q(x14_q), .clk(clock));  // open: clr
  Register #(.width(32)) x15 (.D(Input_high), .en(and_15_out), .Q(x15_q), .clk(clock));  // open: clr
  Register #(.width(32)) x16 (.D(undriven_2), .en(and_16_out), .Q(x16_q), .clk(clock));  // open: clr
  Register #(.width(32)) x17 (.D(undriven), .en(and_17_out), .Q(x17_q), .clk(clock));  // open: clr
  Register #(.width(32)) x18 (.D(Input_high), .en(and_18_out), .Q(x18_q), .clk(clock));  // open: clr
  Register #(.width(32)) x19 (.D(Input_high), .en(and_19_out), .Q(x19_q), .clk(clock));  // open: clr
  Register #(.width(32)) x20 (.D(Input_high), .en(and_20_out), .Q(x20_q), .clk(clock));  // open: clr
  Register #(.width(32)) x21 (.D(Input_high), .en(and_21_out), .Q(x21_q), .clk(clock));  // open: clr
  Register #(.width(32)) x21_2 (.D(Input_high), .en(and_22_out), .Q(x21_2_q), .clk(clock));  // open: clr
  Register #(.width(32)) x23 (.D(Input_high), .en(and_23_out), .Q(x23_q), .clk(clock));  // open: clr
  Register #(.width(32)) x23_2 (.D(Input_high), .en(and_24_out), .Q(x23_2_q), .clk(clock));  // open: clr
  Register #(.width(32)) x25 (.D(Input_high), .en(and_25_out), .Q(x25_q), .clk(clock));  // open: clr
  Register #(.width(32)) x26 (.D(Input_high), .en(and_26_out), .Q(x26_q), .clk(clock));  // open: clr
  Register #(.width(32)) x27 (.D(Input_high), .en(and_27_out), .Q(x27_q), .clk(clock));  // open: clr
  Register #(.width(32)) x28 (.D(Input_high), .en(and_28_out), .Q(x28_q), .clk(clock));  // open: clr
  Register #(.width(32)) x29 (.D(Input_high), .en(and_29_out), .Q(x29_q), .clk(clock));  // open: clr
  Register #(.width(32)) x30 (.D(Input_high), .en(and_30_out), .Q(x30_q), .clk(clock));  // open: clr
  Register #(.width(32)) x31 (.D(Input_high), .en(and_31_out), .Q(x31_q), .clk(clock));  // open: clr
  Register #(.width(32)) x0 (.D(Input_high), .en(and_32_out), .Q(x0_q), .clk(clock));  // open: clr
  Register #(.width(32)) x1_2 (.D(Input_low), .en(and_33_out), .Q(x1_2_q), .clk(clock));  // open: clr
  Register #(.width(32)) x4_4 (.D(Input_low), .en(and_34_out), .Q(x4_4_q), .clk(clock));  // open: clr
  Register #(.width(32)) x3_2 (.D(Input_low), .en(and_35_out), .Q(x3_2_q), .clk(clock));  // open: clr
  Register #(.width(32)) x4_5 (.D(Input_low), .en(and_36_out), .Q(x4_5_q), .clk(clock));  // open: clr
  Register #(.width(32)) x4_6 (.D(Input_low), .en(and_37_out), .Q(x4_6_q), .clk(clock));  // open: clr
  Register #(.width(32)) x6_2 (.D(Input_low), .en(and_38_out), .Q(x6_2_q), .clk(clock));  // open: clr
  Register #(.width(32)) x7_2 (.D(Input_low), .en(and_39_out), .Q(x7_2_q), .clk(clock));  // open: clr
  Register #(.width(32)) x8_2 (.D(Input_low), .en(and_40_out), .Q(x8_2_q), .clk(clock));  // open: clr
  Register #(.width(32)) x9_3 (.D(Input_low), .en(and_41_out), .Q(x9_3_q), .clk(clock));  // open: clr
  Register #(.width(32)) x9_4 (.D(Input_low), .en(and_42_out), .Q(x9_4_q), .clk(clock));  // open: clr
  Register #(.width(32)) x11_2 (.D(Input_low), .en(and_43_out), .Q(x11_2_q), .clk(clock));  // open: clr
  Register #(.width(32)) x12_2 (.D(Input_low), .en(and_44_out), .Q(x12_2_q), .clk(clock));  // open: clr
  Register #(.width(32)) x13_2 (.D(Input_low), .en(and_45_out), .Q(x13_2_q), .clk(clock));  // open: clr
  Register #(.width(32)) x14_2 (.D(Input_low), .en(and_46_out), .Q(x14_2_q), .clk(clock));  // open: clr
  Register #(.width(32)) x15_2 (.D(Input_low), .en(and_47_out), .Q(x15_2_q), .clk(clock));  // open: clr
  Register #(.width(32)) x16_2 (.D(undriven_4), .en(and_48_out), .Q(x16_2_q), .clk(clock));  // open: clr
  Register #(.width(32)) x17_2 (.D(undriven_3), .en(and_49_out), .Q(x17_2_q), .clk(clock));  // open: clr
  Register #(.width(32)) x18_2 (.D(Input_low), .en(and_50_out), .Q(x18_2_q), .clk(clock));  // open: clr
  Register #(.width(32)) x19_2 (.D(Input_low), .en(and_51_out), .Q(x19_2_q), .clk(clock));  // open: clr
  Register #(.width(32)) x20_2 (.D(Input_low), .en(and_52_out), .Q(x20_2_q), .clk(clock));  // open: clr
  Register #(.width(32)) x21_3 (.D(Input_low), .en(and_53_out), .Q(x21_3_q), .clk(clock));  // open: clr
  Register #(.width(32)) x21_4 (.D(Input_low), .en(and_54_out), .Q(x21_4_q), .clk(clock));  // open: clr
  Register #(.width(32)) x23_3 (.D(Input_low), .en(and_55_out), .Q(x23_3_q), .clk(clock));  // open: clr
  Register #(.width(32)) x23_4 (.D(Input_low), .en(and_56_out), .Q(x23_4_q), .clk(clock));  // open: clr
  Register #(.width(32)) x25_2 (.D(Input_low), .en(and_57_out), .Q(x25_2_q), .clk(clock));  // open: clr
  Register #(.width(32)) x26_2 (.D(Input_low), .en(and_58_out), .Q(x26_2_q), .clk(clock));  // open: clr
  Register #(.width(32)) x27_2 (.D(Input_low), .en(and_59_out), .Q(x27_2_q), .clk(clock));  // open: clr
  Register #(.width(32)) x28_2 (.D(Input_low), .en(and_60_out), .Q(x28_2_q), .clk(clock));  // open: clr
  Register #(.width(32)) x29_2 (.D(Input_low), .en(and_61_out), .Q(x29_2_q), .clk(clock));  // open: clr
  Register #(.width(32)) x30_2 (.D(Input_low), .en(and_62_out), .Q(x30_2_q), .clk(clock));  // open: clr
  Register #(.width(32)) x31_2 (.D(Input_low), .en(and_63_out), .Q(x31_2_q), .clk(clock));  // open: clr
  Register #(.width(32)) x0_2 (.D(Input_low), .en(and_64_out), .Q(x0_2_q), .clk(clock));  // open: clr
  Multiplexer #(.select(5), .width(32)) multiplexer_1 (
    .in0(x0_q), .in1(x1_q), .in2(undriven_7), .in3(undriven_8), .in4(x4_2_q), .in5(x4_3_q), .in6(x6_q),
    .in7(undriven_5), .in8(x8_q), .in9(x9_q), .in10(x9_2_q), .in11(x11_q), .in12(x12_q), .in13(x13_q),
    .in14(x14_q), .in15(x15_q), .in16(x16_q), .in17(x17_q), .in18(x18_q), .in19(x19_q), .in20(x20_q),
    .in21(x21_q), .in22(x21_2_q), .in23(x23_q), .in24(x23_2_q), .in25(x25_q), .in26(x26_q), .in27(x27_q),
    .in28(x28_q), .in29(x29_q), .in30(x30_q), .in31(x31_q), .out(Output_high), .sel({_4, _3, _2, _1, _0}));  // open: en
  Multiplexer #(.select(5), .width(32)) multiplexer_2 (
    .in0(x0_2_q), .in1(x1_2_q), .in2(undriven_9), .in3(undriven_10), .in4(x4_5_q), .in5(x4_6_q),
    .in6(x6_2_q), .in7(undriven_6), .in8(x8_2_q), .in9(x9_3_q), .in10(x9_4_q), .in11(x11_2_q),
    .in12(x12_2_q), .in13(x13_2_q), .in14(x14_2_q), .in15(x15_2_q), .in16(x16_2_q), .in17(x17_2_q),
    .in18(x18_2_q), .in19(x19_2_q), .in20(x20_2_q), .in21(x21_3_q), .in22(x21_4_q), .in23(x23_3_q),
    .in24(x23_4_q), .in25(x25_2_q), .in26(x26_2_q), .in27(x27_2_q), .in28(x28_2_q), .in29(x29_2_q),
    .in30(x30_2_q), .in31(x31_2_q), .out(Output_low), .sel({_4_2, _3_2, _2_2, _1_2, _0_2}));  // open: en
  Clock u_Clock (.out(clock));
endmodule

module Program_Counter (
  input  [31:0] Inmediato,
  input  offset_mux,
  input  clear,
  output [31:0] OUTPUT
);

  wire clock_out;
  wire [31:0] adder_1_out, adder_2_out, multiplexer_1_out;

  Adder #(.width(32)) adder_1 (.a(OUTPUT), .b(32'h1), .out(adder_1_out));  // open: cin, cout
  Adder #(.width(32)) adder_2 (.a(Inmediato), .b(OUTPUT), .out(adder_2_out));  // open: cin, cout
  Multiplexer #(.width(32), .enable("false")) multiplexer_1 (
    .in0(adder_1_out), .in1(adder_2_out), .out(multiplexer_1_out), .sel(offset_mux));
  Register #(.width(32)) PC (.D(multiplexer_1_out), .Q(OUTPUT), .clk(clock_out), .clr(clear));  // open: en
  Clock clock (.out(clock_out));
endmodule

module Decoder (
  input  [31:0] instruction,
  output Tipo_B,
  output Load_Store,
  output Tipo_R,
  output Tipo_I
);

  wire B__BL_out, B_cond_out, CBZ_out, I_Add__etc_out, not_1_out, not_2_out, not_3_out, not_4_out, not_5_out,
       not_6_out, not_7_out, not_8_out, not_9_out, not_10_out, not_11_out, not_12_out, not_13_out,
       not_14_out, not_15_out, not_16_out, not_17_out, not_18_out, not_19_out, not_20_out, not_21_out,
       not_22_out, not_23_out, not_24_out, not_25_out, not_26_out, not_27_out, not_28_out, not_29_out,
       not_30_out, R_add__etc_out, R_and__etc_out, R_load_out, R_mov_out, R_shifts_out, R_STR_out;

  not not_1 (not_1_out, instruction[27]);
  not not_2 (not_2_out, instruction[26]);
  not not_3 (not_3_out, instruction[25]);
  and I_Add__etc (I_Add__etc_out, instruction[28], not_1_out, not_2_out, not_3_out, instruction[24]);
  or or_1 (Tipo_I, I_Add__etc_out, CBZ_out);
  not not_4 (not_4_out, instruction[26]);
  not not_5 (not_5_out, instruction[28]);
  and R_add__etc (R_add__etc_out, not_5_out, instruction[27], not_4_out, instruction[25], instruction[24]);
  not not_6 (not_6_out, instruction[26]);
  not not_7 (not_7_out, instruction[24]);
  not not_8 (not_8_out, instruction[28]);
  and R_and__etc (R_and__etc_out, not_8_out, instruction[27], not_6_out, instruction[25], not_7_out);
  or or_2 (Tipo_R, R_add__etc_out, R_and__etc_out, R_shifts_out, R_mov_out);
  not not_9 (not_9_out, instruction[26]);
  and R_shifts (R_shifts_out, instruction[28], instruction[27], not_9_out, instruction[25], not_10_out);
  not not_10 (not_10_out, instruction[24]);
  not not_11 (not_11_out, instruction[24]);
  not not_12 (not_12_out, instruction[26]);
  not not_13 (not_13_out, instruction[27]);
  and R_mov (R_mov_out, instruction[28], not_13_out, not_12_out, instruction[25], not_11_out);
  not not_14 (not_14_out, instruction[26]);
  not not_15 (not_15_out, instruction[22]);
  not not_16 (not_16_out, instruction[25]);
  not not_17 (not_17_out, instruction[23]);
  and R_STR (R_STR_out, instruction[31], instruction[30], instruction[29], instruction[28], instruction[27], not_14_out, not_16_out, instruction[24], not_17_out, not_15_out);
  or or_3 (Load_Store, R_STR_out, R_load_out);
  not not_18 (not_18_out, instruction[30]);
  not not_19 (not_19_out, instruction[25]);
  not not_20 (not_20_out, instruction[31]);
  not not_21 (not_21_out, instruction[27]);
  and CBZ (CBZ_out, not_18_out, instruction[29], instruction[28], not_21_out, instruction[26], not_19_out);
  not not_22 (not_22_out, instruction[25]);
  not not_23 (not_23_out, instruction[27]);
  not not_24 (not_24_out, instruction[29]);
  and B_cond (B_cond_out, not_20_out, instruction[30], not_24_out, instruction[28], not_23_out, instruction[26], not_22_out);
  or or_4 (Tipo_B, B_cond_out, B__BL_out);
  not not_25 (not_25_out, instruction[27]);
  not not_26 (not_26_out, instruction[30]);
  not not_27 (not_27_out, instruction[29]);
  and B__BL (B__BL_out, not_26_out, not_27_out, instruction[28], not_25_out, instruction[26]);
  not not_28 (not_28_out, instruction[26]);
  and R_load (R_load_out, instruction[31], instruction[30], instruction[29], instruction[28], instruction[27], not_28_out, not_30_out, instruction[24], not_29_out, instruction[22]);
  not not_29 (not_29_out, instruction[23]);
  not not_30 (not_30_out, instruction[25]);
endmodule

module Jump_Controller (
  input  [3:0] in_1,
  output out_2
);

  wire not_1_out, not_2_out;

  and and_1 (out_2, in_1[3], in_1[2], not_1_out, not_2_out);
  not not_1 (not_1_out, in_1[1]);
  not not_2 (not_2_out, in_1[0]);
endmodule

module Shift_Left (
  input  [31:0] High,
  input  [31:0] Corrimiento,
  input  [31:0] Low,
  output [31:0] Salida_high,
  output [31:0] Salida_low
);

  wire [4:0] bit_extender_1_out, subtractor_1_out;
  wire [31:0] or_1_out, shifter_1_out, shifter_2_out;

  Bit_Extender #(.in_width(32), .out_width(5)) bit_extender_1 (.in(Corrimiento), .out(bit_extender_1_out));
  Subtractor #(.width(5)) subtractor_1 (
    .a({5{1'b1}}), .b(bit_extender_1_out), .out(subtractor_1_out));  // open: bin, bout
  Shifter #(.width(32)) shifter_1 (.in(High), .\dist (bit_extender_1_out), .out(shifter_1_out));
  assign or_1_out = Low | {32{1'b0}};  // OR_Gate or_1, 32 bits wide
  Shifter #(.width(32), .shift("lr")) shifter_2 (.in(or_1_out), .\dist (subtractor_1_out), .out(shifter_2_out));
  assign Salida_high = shifter_1_out | shifter_2_out;  // OR_Gate or_2, 32 bits wide
  Shifter #(.width(32)) shifter_3 (.in(Low), .\dist (bit_extender_1_out), .out(Salida_low));
endmodule

module Shift_right (
  input  [31:0] High,
  input  [31:0] Corrimiento,
  input  [31:0] Low,
  output [31:0] Salida_high,
  output [31:0] Salida_Low
);

  wire [4:0] bit_extender_1_out, subtractor_1_out;
  wire [31:0] or_1_out, shifter_1_out, shifter_3_out;

  Bit_Extender #(.in_width(32), .out_width(5)) bit_extender_1 (.in(Corrimiento), .out(bit_extender_1_out));
  Subtractor #(.width(5)) subtractor_1 (
    .a({5{1'b1}}), .b(bit_extender_1_out), .out(subtractor_1_out));  // open: bin, bout
  assign or_1_out = High | {32{1'b0}};  // OR_Gate or_1, 32 bits wide
  Shifter #(.width(32), .shift("lr")) shifter_1 (.in(Low), .\dist (bit_extender_1_out), .out(shifter_1_out));
  Shifter #(.width(32), .shift("lr")) shifter_2 (.in(High), .\dist (bit_extender_1_out), .out(Salida_high));
  Shifter #(.width(32)) shifter_3 (.in(or_1_out), .\dist (subtractor_1_out), .out(shifter_3_out));
  assign Salida_Low = shifter_3_out | shifter_1_out;  // OR_Gate or_2, 32 bits wide
endmodule

module Prueba_registro (
  input  [3:0] in_1,
  input  in_2,
  output [3:0] out_3
);

  Register #(.width(4)) register_1 (.D(in_1), .Q(out_3), .clk(in_2));  // open: en, clr
endmodule

module Decodept2 (
  input  [31:0] instruction,
  output ADD_R,
  output ADDS_R,
  output SUB_R,
  output SUBS_R,
  output AND_R,
  output ORR_R,
  output EOR_R,
  output ANDS_R,
  output LSLV_R,
  output LSRV_R,
  output ASRV_R,
  output RORV_R,
  output ADD_I,
  output ADDS_I,
  output SUB_I,
  output SUBS_I,
  output MOVN_I,
  output MOV_I,
  output MOVK_I,
  output CBZ_B,
  output CBNZ_B,
  output B__EQ_B,
  output B__NE_B,
  output B__HS_B,
  output B__LO_B,
  output B__MI_B,
  output B__PL_B,
  output B__VS_B,
  output B__VC_B,
  output B__HI_B,
  output B__LS_B,
  output B__GE_B,
  output B__LT_B,
  output B__GT_B,
  output B__LE_B,
  output B,
  output BL,
  output STR,
  output LDR,
  output RET
);

  wire not_1_out, not_2_out, not_3_out, not_4_out, not_5_out, not_6_out, not_7_out, not_8_out, not_9_out,
       not_10_out, not_11_out, not_12_out, not_13_out, not_14_out, not_15_out, not_16_out, not_17_out,
       not_18_out, not_19_out, not_20_out, not_21_out, not_22_out, not_23_out, not_24_out, not_25_out,
       not_26_out, not_27_out, not_28_out, not_29_out, not_30_out, not_31_out, not_32_out, not_33_out,
       not_34_out, not_35_out, not_36_out, not_37_out, not_38_out, not_39_out, not_40_out, not_41_out,
       not_42_out, not_43_out, not_44_out, not_45_out, not_46_out, not_47_out, not_48_out, not_49_out,
       not_50_out, not_51_out, not_52_out, not_53_out, not_54_out, not_55_out, not_56_out, not_57_out,
       not_58_out, not_59_out, not_60_out, not_61_out, not_62_out, not_63_out, not_64_out, not_65_out,
       not_66_out, not_67_out, not_68_out, not_69_out, not_70_out, not_71_out, not_72_out, not_73_out,
       not_74_out, not_75_out, not_76_out, not_77_out, not_78_out, not_79_out, not_80_out, not_81_out,
       not_82_out, not_83_out, not_84_out, not_85_out, not_86_out, not_87_out, not_88_out, not_89_out,
       not_90_out, not_91_out, not_92_out, not_93_out, not_94_out, not_95_out, not_96_out, not_97_out,
       not_98_out, not_99_out, not_100_out, not_101_out, not_102_out, not_103_out, not_104_out, not_105_out,
       not_106_out, not_107_out, not_108_out, not_109_out, not_110_out, not_111_out, not_112_out,
       not_113_out, not_114_out, not_116_out, not_117_out, not_118_out, not_119_out, not_120_out,
       not_121_out, not_122_out, not_123_out, not_125_out, not_126_out, not_127_out, not_128_out,
       not_130_out, not_131_out, not_132_out, not_133_out, not_134_out, not_135_out, not_136_out,
       not_137_out, not_138_out, not_139_out, not_140_out, not_141_out, not_142_out, not_143_out,
       not_144_out, not_145_out, not_146_out, not_147_out, not_148_out, not_149_out, not_150_out,
       not_151_out, not_152_out, not_153_out, not_154_out, not_155_out, not_156_out, not_157_out,
       not_158_out, not_159_out, not_160_out, not_161_out, not_162_out, not_163_out, not_164_out,
       not_165_out, not_166_out, not_167_out, not_168_out, not_169_out, not_170_out, not_171_out,
       not_172_out, not_173_out, not_174_out, not_175_out, not_176_out, not_177_out, not_178_out,
       not_179_out, not_180_out, not_181_out, not_182_out, not_183_out, not_184_out, not_185_out,
       not_186_out, not_187_out, not_188_out, not_189_out, not_190_out, not_191_out, not_192_out,
       not_193_out, not_194_out, not_195_out, not_196_out, not_197_out, not_198_out, not_199_out,
       not_200_out, not_201_out, not_202_out, not_203_out, not_204_out, not_205_out, not_206_out,
       not_207_out, not_208_out, not_209_out, not_210_out, not_211_out, not_212_out, not_213_out,
       not_214_out, not_215_out, not_216_out, not_217_out, not_218_out, not_219_out, not_220_out,
       not_221_out, not_222_out, not_223_out, not_224_out, not_225_out, not_226_out, not_227_out,
       not_228_out, not_229_out, not_230_out, not_231_out, not_232_out, not_233_out, not_234_out,
       not_235_out, not_236_out, not_237_out, not_238_out, not_239_out, not_240_out, not_241_out,
       not_242_out, not_243_out, not_244_out, not_245_out, not_246_out, not_247_out, not_248_out,
       not_249_out, not_250_out, not_251_out, not_252_out, not_253_out, not_254_out, not_255_out,
       not_256_out, not_257_out, not_258_out, not_259_out, not_260_out, not_261_out, not_262_out,
       not_263_out, not_264_out, not_265_out, not_266_out, not_267_out, not_268_out, not_269_out,
       not_270_out, not_271_out, not_272_out, not_273_out, not_274_out, not_275_out, not_276_out,
       not_277_out, not_278_out, not_279_out, not_280_out, not_281_out, not_282_out, not_283_out;

  not not_1 (not_1_out, instruction[29]);
  not not_2 (not_2_out, instruction[30]);
  not not_3 (not_3_out, instruction[21]);
  not not_4 (not_4_out, instruction[28]);
  not not_5 (not_5_out, instruction[26]);
  not not_6 (not_6_out, instruction[23]);
  not not_7 (not_7_out, instruction[22]);
  and and_1 (ADD_R, instruction[31], not_2_out, not_1_out, not_4_out, instruction[27], not_5_out, instruction[25], instruction[24], not_6_out, not_7_out, not_3_out);
  not not_8 (not_8_out, instruction[28]);
  not not_9 (not_9_out, instruction[30]);
  not not_10 (not_10_out, instruction[26]);
  and and_2 (ADDS_R, instruction[31], not_9_out, instruction[29], not_8_out, instruction[27], not_10_out, instruction[25], instruction[24], not_14_out, not_13_out, not_11_out);
  not not_11 (not_11_out, instruction[21]);
  not not_12 (not_12_out, instruction[29]);
  not not_13 (not_13_out, instruction[22]);
  not not_14 (not_14_out, instruction[23]);
  not not_15 (not_15_out, instruction[23]);
  not not_16 (not_16_out, instruction[28]);
  not not_17 (not_17_out, instruction[22]);
  not not_18 (not_18_out, instruction[21]);
  not not_19 (not_19_out, instruction[26]);
  and and_3 (SUB_R, instruction[31], instruction[30], not_12_out, not_16_out, instruction[27], not_19_out, instruction[25], instruction[24], not_15_out, not_17_out, not_18_out);
  not not_20 (not_20_out, instruction[28]);
  not not_21 (not_21_out, instruction[26]);
  and and_4 (SUBS_R, instruction[31], instruction[30], instruction[29], not_20_out, instruction[27], not_21_out, instruction[25], instruction[24], not_23_out, not_25_out, not_24_out);
  not not_22 (not_22_out, instruction[29]);
  not not_23 (not_23_out, instruction[23]);
  not not_24 (not_24_out, instruction[21]);
  not not_25 (not_25_out, instruction[22]);
  not not_26 (not_26_out, instruction[30]);
  not not_27 (not_27_out, instruction[24]);
  not not_28 (not_28_out, instruction[23]);
  not not_29 (not_29_out, instruction[28]);
  not not_30 (not_30_out, instruction[22]);
  not not_31 (not_31_out, instruction[21]);
  not not_32 (not_32_out, instruction[26]);
  and and_5 (AND_R, instruction[31], not_26_out, not_22_out, not_29_out, instruction[27], not_32_out, instruction[25], not_27_out, not_28_out, not_30_out, not_31_out);
  not not_33 (not_33_out, instruction[26]);
  not not_34 (not_34_out, instruction[28]);
  not not_35 (not_35_out, instruction[30]);
  and and_6 (ORR_R, instruction[31], not_35_out, instruction[29], not_34_out, instruction[27], not_33_out, instruction[25], not_38_out, not_39_out, not_37_out, not_40_out);
  not not_36 (not_36_out, instruction[29]);
  not not_37 (not_37_out, instruction[22]);
  not not_38 (not_38_out, instruction[24]);
  not not_39 (not_39_out, instruction[23]);
  not not_40 (not_40_out, instruction[21]);
  not not_41 (not_41_out, instruction[24]);
  not not_42 (not_42_out, instruction[23]);
  not not_43 (not_43_out, instruction[28]);
  not not_44 (not_44_out, instruction[26]);
  not not_45 (not_45_out, instruction[22]);
  not not_46 (not_46_out, instruction[21]);
  and and_7 (EOR_R, instruction[31], instruction[30], not_36_out, not_43_out, instruction[27], not_44_out, instruction[25], not_41_out, not_42_out, not_45_out, not_46_out);
  not not_47 (not_47_out, instruction[28]);
  not not_48 (not_48_out, instruction[26]);
  and and_8 (ANDS_R, instruction[31], instruction[30], instruction[29], not_47_out, instruction[27], not_48_out, instruction[25], not_50_out, not_51_out, not_53_out, not_49_out);
  not not_49 (not_49_out, instruction[21]);
  not not_50 (not_50_out, instruction[24]);
  not not_51 (not_51_out, instruction[23]);
  not not_52 (not_52_out, instruction[29]);
  not not_53 (not_53_out, instruction[22]);
  not not_54 (not_54_out, instruction[30]);
  not not_55 (not_55_out, instruction[24]);
  not not_56 (not_56_out, instruction[26]);
  not not_57 (not_57_out, instruction[21]);
  and and_9 (LSLV_R, instruction[31], not_54_out, not_52_out, instruction[28], instruction[27], not_56_out, instruction[25], not_55_out, instruction[23], instruction[22], not_57_out, not_60_out, not_58_out, instruction[13], not_62_out, not_59_out, not_61_out);
  not not_58 (not_58_out, instruction[14]);
  not not_59 (not_59_out, instruction[11]);
  not not_60 (not_60_out, instruction[15]);
  not not_61 (not_61_out, instruction[10]);
  not not_62 (not_62_out, instruction[12]);
  not not_63 (not_63_out, instruction[24]);
  not not_64 (not_64_out, instruction[26]);
  not not_65 (not_65_out, instruction[30]);
  not not_66 (not_66_out, instruction[29]);
  and and_10 (LSRV_R, instruction[31], not_65_out, not_66_out, instruction[28], instruction[27], not_64_out, instruction[25], not_63_out, instruction[23], instruction[22], not_70_out, not_69_out, not_68_out, instruction[13], not_71_out, not_67_out, instruction[10]);
  not not_67 (not_67_out, instruction[11]);
  not not_68 (not_68_out, instruction[14]);
  not not_69 (not_69_out, instruction[15]);
  not not_70 (not_70_out, instruction[21]);
  not not_71 (not_71_out, instruction[12]);
  not not_72 (not_72_out, instruction[29]);
  not not_73 (not_73_out, instruction[30]);
  not not_74 (not_74_out, instruction[26]);
  not not_75 (not_75_out, instruction[14]);
  not not_76 (not_76_out, instruction[15]);
  not not_77 (not_77_out, instruction[24]);
  not not_78 (not_78_out, instruction[12]);
  not not_79 (not_79_out, instruction[21]);
  and and_11 (ASRV_R, instruction[31], not_73_out, not_72_out, instruction[28], instruction[27], not_74_out, instruction[25], not_77_out, instruction[23], instruction[22], not_79_out, not_76_out, not_75_out, instruction[13], not_78_out, instruction[11], not_80_out);
  not not_80 (not_80_out, instruction[10]);
  not not_81 (not_81_out, instruction[29]);
  not not_82 (not_82_out, instruction[30]);
  not not_83 (not_83_out, instruction[24]);
  not not_84 (not_84_out, instruction[14]);
  not not_85 (not_85_out, instruction[26]);
  not not_86 (not_86_out, instruction[15]);
  not not_87 (not_87_out, instruction[21]);
  and and_12 (RORV_R, instruction[31], not_82_out, not_81_out, instruction[28], instruction[27], not_85_out, instruction[25], not_83_out, instruction[23], instruction[22], not_87_out, not_86_out, not_84_out, instruction[13], not_88_out, instruction[11], instruction[10]);
  not not_88 (not_88_out, instruction[12]);
  not not_89 (not_89_out, instruction[30]);
  not not_90 (not_90_out, instruction[29]);
  not not_91 (not_91_out, instruction[26]);
  not not_92 (not_92_out, instruction[27]);
  not not_93 (not_93_out, instruction[23]);
  not not_94 (not_94_out, instruction[22]);
  not not_95 (not_95_out, instruction[25]);
  and and_13 (ADD_I, instruction[31], not_89_out, not_90_out, instruction[28], not_92_out, not_91_out, not_95_out, instruction[24], not_93_out, not_94_out);
  not not_96 (not_96_out, instruction[27]);
  not not_97 (not_97_out, instruction[26]);
  not not_98 (not_98_out, instruction[30]);
  and and_14 (ADDS_I, instruction[31], not_98_out, instruction[29], instruction[28], not_96_out, not_97_out, not_99_out, instruction[24], not_101_out, not_102_out);
  not not_99 (not_99_out, instruction[25]);
  not not_100 (not_100_out, instruction[29]);
  not not_101 (not_101_out, instruction[23]);
  not not_102 (not_102_out, instruction[22]);
  not not_103 (not_103_out, instruction[23]);
  not not_104 (not_104_out, instruction[22]);
  not not_105 (not_105_out, instruction[27]);
  not not_106 (not_106_out, instruction[26]);
  not not_107 (not_107_out, instruction[25]);
  and and_15 (SUB_I, instruction[31], instruction[30], not_100_out, instruction[28], not_105_out, not_106_out, not_107_out, instruction[24], not_103_out, not_104_out);
  not not_108 (not_108_out, instruction[27]);
  not not_109 (not_109_out, instruction[26]);
  and and_16 (SUBS_I, instruction[31], instruction[30], instruction[29], instruction[28], not_108_out, not_109_out, not_112_out, instruction[24], not_113_out, not_111_out);
  not not_110 (not_110_out, instruction[29]);
  not not_111 (not_111_out, instruction[22]);
  not not_112 (not_112_out, instruction[25]);
  not not_113 (not_113_out, instruction[23]);
  not not_114 (not_114_out, instruction[30]);
  // NOT_Gate not_115 has open pins: in=instruction[21], out=open
  not not_116 (not_116_out, instruction[22]);
  not not_117 (not_117_out, instruction[26]);
  not not_118 (not_118_out, instruction[24]);
  not not_119 (not_119_out, instruction[27]);
  and and_17 (MOVN_I, instruction[31], not_114_out, not_110_out, instruction[28], not_119_out, not_117_out, instruction[25], not_118_out, instruction[23], not_116_out);
  not not_120 (not_120_out, instruction[27]);
  not not_121 (not_121_out, instruction[26]);
  not not_122 (not_122_out, instruction[29]);
  and and_18 (MOV_I, instruction[31], instruction[30], not_122_out, instruction[28], not_120_out, not_121_out, instruction[25], not_125_out, instruction[23], not_123_out);
  not not_123 (not_123_out, instruction[22]);
  // NOT_Gate not_124 has open pins: in=instruction[21], out=open
  not not_125 (not_125_out, instruction[24]);
  not not_126 (not_126_out, instruction[26]);
  not not_127 (not_127_out, instruction[22]);
  not not_128 (not_128_out, instruction[24]);
  // NOT_Gate not_129 has open pins: in=instruction[21], out=open
  not not_130 (not_130_out, instruction[27]);
  and and_19 (MOVK_I, instruction[31], instruction[30], instruction[29], instruction[28], not_130_out, not_126_out, instruction[25], not_128_out, instruction[23], not_127_out);
  not not_131 (not_131_out, instruction[27]);
  not not_132 (not_132_out, instruction[30]);
  and and_20 (CBZ_B, instruction[31], not_132_out, instruction[29], instruction[28], not_131_out, instruction[26], not_135_out, not_134_out);
  not not_133 (not_133_out, instruction[30]);
  not not_134 (not_134_out, instruction[24]);
  not not_135 (not_135_out, instruction[25]);
  and and_21 (CBNZ_B, instruction[31], not_133_out, instruction[29], instruction[28], not_137_out, instruction[26], not_136_out, instruction[24]);
  not not_136 (not_136_out, instruction[25]);
  not not_137 (not_137_out, instruction[27]);
  not not_138 (not_138_out, instruction[29]);
  not not_139 (not_139_out, instruction[31]);
  not not_140 (not_140_out, instruction[4]);
  not not_141 (not_141_out, instruction[3]);
  not not_142 (not_142_out, instruction[24]);
  not not_143 (not_143_out, instruction[2]);
  not not_144 (not_144_out, instruction[25]);
  not not_145 (not_145_out, instruction[27]);
  and and_22 (B__EQ_B, not_139_out, instruction[30], not_138_out, instruction[28], not_145_out, instruction[26], not_144_out, not_142_out, not_140_out, not_141_out, not_143_out, not_150_out, not_146_out);
  not not_146 (not_146_out, instruction[0]);
  not not_147 (not_147_out, instruction[31]);
  not not_148 (not_148_out, instruction[27]);
  not not_149 (not_149_out, instruction[29]);
  not not_150 (not_150_out, instruction[1]);
  not not_151 (not_151_out, instruction[1]);
  not not_152 (not_152_out, instruction[2]);
  not not_153 (not_153_out, instruction[25]);
  not not_154 (not_154_out, instruction[24]);
  not not_155 (not_155_out, instruction[4]);
  not not_156 (not_156_out, instruction[3]);
  and and_23 (B__NE_B, not_147_out, instruction[30], not_149_out, instruction[28], not_148_out, instruction[26], not_153_out, not_154_out, not_155_out, not_156_out, not_152_out, not_151_out, instruction[0]);
  not not_157 (not_157_out, instruction[29]);
  not not_158 (not_158_out, instruction[27]);
  not not_159 (not_159_out, instruction[25]);
  not not_160 (not_160_out, instruction[31]);
  and and_24 (B__HS_B, not_160_out, instruction[30], not_157_out, instruction[28], not_158_out, instruction[26], not_159_out, not_166_out, not_165_out, not_162_out, not_161_out, instruction[1], not_164_out);
  not not_161 (not_161_out, instruction[2]);
  not not_162 (not_162_out, instruction[3]);
  not not_163 (not_163_out, instruction[31]);
  not not_164 (not_164_out, instruction[0]);
  not not_165 (not_165_out, instruction[4]);
  not not_166 (not_166_out, instruction[24]);
  not not_167 (not_167_out, instruction[29]);
  not not_168 (not_168_out, instruction[25]);
  not not_169 (not_169_out, instruction[27]);
  not not_170 (not_170_out, instruction[4]);
  not not_171 (not_171_out, instruction[24]);
  and and_25 (B__LO_B, not_163_out, instruction[30], not_167_out, instruction[28], not_169_out, instruction[26], not_168_out, not_171_out, not_170_out, not_175_out, not_173_out, instruction[1], instruction[0]);
  not not_172 (not_172_out, instruction[31]);
  not not_173 (not_173_out, instruction[2]);
  not not_174 (not_174_out, instruction[29]);
  not not_175 (not_175_out, instruction[3]);
  not not_176 (not_176_out, instruction[3]);
  not not_177 (not_177_out, instruction[25]);
  not not_178 (not_178_out, instruction[27]);
  not not_179 (not_179_out, instruction[24]);
  not not_180 (not_180_out, instruction[4]);
  and and_26 (B__MI_B, not_172_out, instruction[30], not_174_out, instruction[28], not_178_out, instruction[26], not_177_out, not_179_out, not_180_out, not_176_out, instruction[2], not_184_out, not_182_out);
  not not_181 (not_181_out, instruction[31]);
  not not_182 (not_182_out, instruction[0]);
  not not_183 (not_183_out, instruction[29]);
  not not_184 (not_184_out, instruction[1]);
  not not_185 (not_185_out, instruction[27]);
  not not_186 (not_186_out, instruction[25]);
  not not_187 (not_187_out, instruction[1]);
  not not_188 (not_188_out, instruction[24]);
  not not_189 (not_189_out, instruction[4]);
  not not_190 (not_190_out, instruction[3]);
  and and_27 (B__PL_B, not_181_out, instruction[30], not_183_out, instruction[28], not_185_out, instruction[26], not_186_out, not_188_out, not_189_out, not_190_out, instruction[2], not_187_out, instruction[0]);
  not not_191 (not_191_out, instruction[25]);
  not not_192 (not_192_out, instruction[27]);
  not not_193 (not_193_out, instruction[29]);
  not not_194 (not_194_out, instruction[31]);
  and and_28 (B__VS_B, not_194_out, instruction[30], not_193_out, instruction[28], not_192_out, instruction[26], not_191_out, not_196_out, not_195_out, not_198_out, instruction[2], instruction[1], not_197_out);
  not not_195 (not_195_out, instruction[4]);
  not not_196 (not_196_out, instruction[24]);
  not not_197 (not_197_out, instruction[0]);
  not not_198 (not_198_out, instruction[3]);
  not not_199 (not_199_out, instruction[31]);
  not not_200 (not_200_out, instruction[24]);
  not not_201 (not_201_out, instruction[25]);
  not not_202 (not_202_out, instruction[4]);
  not not_203 (not_203_out, instruction[29]);
  not not_204 (not_204_out, instruction[27]);
  and and_29 (B__VC_B, not_199_out, instruction[30], not_203_out, instruction[28], not_204_out, instruction[26], not_201_out, not_200_out, not_202_out, not_207_out, instruction[2], instruction[1], instruction[0]);
  not not_205 (not_205_out, instruction[29]);
  not not_206 (not_206_out, instruction[31]);
  not not_207 (not_207_out, instruction[3]);
  not not_208 (not_208_out, instruction[25]);
  not not_209 (not_209_out, instruction[4]);
  not not_210 (not_210_out, instruction[24]);
  not not_211 (not_211_out, instruction[2]);
  not not_212 (not_212_out, instruction[27]);
  and and_30 (B__HI_B, not_206_out, instruction[30], not_205_out, instruction[28], not_212_out, instruction[26], not_208_out, not_210_out, not_209_out, instruction[3], not_211_out, not_216_out, not_217_out);
  not not_213 (not_213_out, instruction[31]);
  not not_214 (not_214_out, instruction[29]);
  not not_215 (not_215_out, instruction[27]);
  not not_216 (not_216_out, instruction[1]);
  not not_217 (not_217_out, instruction[0]);
  not not_218 (not_218_out, instruction[24]);
  not not_219 (not_219_out, instruction[4]);
  not not_220 (not_220_out, instruction[1]);
  not not_221 (not_221_out, instruction[25]);
  not not_222 (not_222_out, instruction[2]);
  and and_31 (B__LS_B, not_213_out, instruction[30], not_214_out, instruction[28], not_215_out, instruction[26], not_221_out, not_218_out, not_219_out, instruction[3], not_222_out, not_220_out, instruction[0]);
  not not_223 (not_223_out, instruction[29]);
  not not_224 (not_224_out, instruction[27]);
  not not_225 (not_225_out, instruction[25]);
  not not_226 (not_226_out, instruction[31]);
  and and_32 (B__GE_B, not_226_out, instruction[30], not_223_out, instruction[28], not_224_out, instruction[26], not_225_out, not_230_out, not_227_out, instruction[3], not_229_out, instruction[1], not_228_out);
  not not_227 (not_227_out, instruction[4]);
  not not_228 (not_228_out, instruction[0]);
  not not_229 (not_229_out, instruction[2]);
  not not_230 (not_230_out, instruction[24]);
  not not_231 (not_231_out, instruction[31]);
  not not_232 (not_232_out, instruction[25]);
  not not_233 (not_233_out, instruction[24]);
  not not_234 (not_234_out, instruction[4]);
  not not_235 (not_235_out, instruction[29]);
  not not_236 (not_236_out, instruction[27]);
  and and_33 (B__LT_B, not_231_out, instruction[30], not_235_out, instruction[28], not_236_out, instruction[26], not_232_out, not_233_out, not_234_out, instruction[3], not_238_out, instruction[1], instruction[0]);
  not not_237 (not_237_out, instruction[31]);
  not not_238 (not_238_out, instruction[2]);
  not not_239 (not_239_out, instruction[29]);
  not not_240 (not_240_out, instruction[4]);
  not not_241 (not_241_out, instruction[24]);
  not not_242 (not_242_out, instruction[25]);
  not not_243 (not_243_out, instruction[27]);
  and and_34 (B__GT_B, not_237_out, instruction[30], not_239_out, instruction[28], not_243_out, instruction[26], not_242_out, not_241_out, not_240_out, instruction[3], instruction[2], not_246_out, not_244_out);
  not not_244 (not_244_out, instruction[0]);
  not not_245 (not_245_out, instruction[29]);
  not not_246 (not_246_out, instruction[1]);
  not not_247 (not_247_out, instruction[31]);
  not not_248 (not_248_out, instruction[27]);
  not not_249 (not_249_out, instruction[4]);
  not not_250 (not_250_out, instruction[24]);
  not not_251 (not_251_out, instruction[25]);
  not not_252 (not_252_out, instruction[1]);
  and and_35 (B__LE_B, not_247_out, instruction[30], not_245_out, instruction[28], not_248_out, instruction[26], not_251_out, not_250_out, not_249_out, instruction[3], instruction[2], not_252_out, instruction[0]);
  not not_253 (not_253_out, instruction[31]);
  not not_254 (not_254_out, instruction[30]);
  not not_255 (not_255_out, instruction[29]);
  not not_256 (not_256_out, instruction[27]);
  and and_36 (B, not_253_out, not_254_out, not_255_out, instruction[28], not_256_out, instruction[26]);
  not not_257 (not_257_out, instruction[29]);
  not not_258 (not_258_out, instruction[27]);
  not not_259 (not_259_out, instruction[30]);
  and and_37 (BL, instruction[31], not_259_out, not_257_out, instruction[28], not_258_out, instruction[26]);
  not not_260 (not_260_out, instruction[26]);
  and and_38 (STR, instruction[31], instruction[30], instruction[29], instruction[28], instruction[27], not_260_out, not_262_out, instruction[24], not_261_out, not_263_out);
  not not_261 (not_261_out, instruction[23]);
  not not_262 (not_262_out, instruction[25]);
  not not_263 (not_263_out, instruction[22]);
  not not_264 (not_264_out, instruction[25]);
  not not_265 (not_265_out, instruction[23]);
  not not_266 (not_266_out, instruction[26]);
  and and_39 (LDR, instruction[31], instruction[30], instruction[29], instruction[28], instruction[27], not_266_out, not_264_out, instruction[24], not_265_out, instruction[22]);
  not not_267 (not_267_out, instruction[29]);
  not not_268 (not_268_out, instruction[27]);
  not not_269 (not_269_out, instruction[24]);
  not not_270 (not_270_out, instruction[21]);
  not not_271 (not_271_out, instruction[23]);
  not not_272 (not_272_out, instruction[13]);
  not not_273 (not_273_out, instruction[14]);
  not not_274 (not_274_out, instruction[12]);
  not not_275 (not_275_out, instruction[15]);
  not not_276 (not_276_out, instruction[10]);
  not not_277 (not_277_out, instruction[11]);
  and and_40 (RET, instruction[31], instruction[30], not_267_out, instruction[28], not_268_out, instruction[26], instruction[25], not_269_out, not_271_out, instruction[22], not_270_out, instruction[20], instruction[19], instruction[18], instruction[17], instruction[16], not_275_out, not_273_out, not_272_out, not_274_out, not_277_out, not_276_out, instruction[9], instruction[8], instruction[7], instruction[6], not_279_out, not_281_out, not_278_out, not_280_out, not_283_out, not_282_out);
  not not_278 (not_278_out, instruction[3]);
  not not_279 (not_279_out, instruction[5]);
  not not_280 (not_280_out, instruction[2]);
  not not_281 (not_281_out, instruction[4]);
  not not_282 (not_282_out, instruction[0]);
  not not_283 (not_283_out, instruction[1]);
endmodule

module xxxxxx (
  input  [31:0] instruction
);
endmodule

module Registros_orden (
  input  [4:0] xd,
  input  [4:0] xm,
  input  [4:0] xn,
  input  [31:0] Input_h,
  input  [31:0] Input_l,
  input  [31:0] output_xn_low,
  input  [31:0] output_xn_high,
  input  [31:0] output_xm_low,
  input  [31:0] output_xm_high
);

  wire clock, not_1_out, not_2_out, not_3_out, not_4_out, not_5_out, not_6_out, not_7_out, not_8_out,
       not_9_out, not_10_out, not_11_out, not_12_out, not_13_out, not_14_out, not_15_out, not_16_out,
       not_17_out, not_18_out, not_19_out, not_20_out, not_21_out, not_22_out, not_23_out, not_24_out,
       not_25_out, not_26_out, not_27_out, not_28_out, not_29_out, not_30_out, not_31_out, not_32_out,
       not_33_out, not_34_out, not_35_out, not_36_out, not_37_out, not_38_out, not_39_out, not_40_out,
       not_41_out, not_42_out, not_43_out, not_44_out, not_45_out, not_46_out, not_47_out, not_48_out,
       not_49_out, not_50_out, not_51_out, not_52_out, not_53_out, not_54_out, not_55_out, not_56_out,
       not_57_out, not_58_out, not_59_out, not_60_out, not_61_out, not_62_out, not_63_out, not_64_out,
       not_65_out, not_66_out, not_67_out, not_69_out, not_70_out, not_71_out, not_72_out, not_73_out,
       not_74_out, not_75_out, not_76_out, not_77_out, not_78_out, not_79_out, not_80_out, not_81_out, on0,
       on1, on2, on3, on4, on5, on6, on7, on8, on9, on10, on11, on12, on13, on14, on15, on16, on17, on18,
       on19, on20, on21, on22, on23, on24, on25, on26, on27, on28, on29, on30, on31;
  wire [31:0] x0, x0h, x1, x1h, x2, x2h, x3, x3h, x4, x4h, x5, x5h, x6, x6h, x7, x7h, x8, x8h, x9, x9h, x10,
       x10h, x11, x11h, x12, x12h, x13, x13h, x14, x14h, x15, x15h, x16, x16h, x17, x17h, x18, x18h, x19,
       x19h, x20, x20h, x21, x21h, x22, x22h, x23, x23h, x24, x24h, x25, x25h, x26, x26h, x27, x27h, x28,
       x28h, x29, x29h, x30, x30h, x31, x31h;

  Clock clock_1 (.out(clock));
  not not_1 (not_1_out, xd[2]);
  not not_2 (not_2_out, xd[0]);
  not not_3 (not_3_out, xd[1]);
  and and_1 (on0, not_2_out, not_3_out, not_1_out, not_7_out, not_6_out);
  not not_4 (not_4_out, xd[2]);
  not not_5 (not_5_out, xd[1]);
  not not_6 (not_6_out, xd[4]);
  not not_7 (not_7_out, xd[3]);
  not not_8 (not_8_out, xd[4]);
  not not_9 (not_9_out, xd[3]);
  and and_2 (on1, xd[0], not_5_out, not_4_out, not_9_out, not_8_out);
  Register #(.width(32)) u_x0 (.D(Input_h), .en(on0), .Q(x0h), .clk(clock));  // open: clr
  Register #(.width(32)) u_x1 (.D(Input_h), .en(on1), .Q(x1h), .clk(clock));  // open: clr
  Register #(.width(32)) u_x2 (.D(Input_h), .en(on2), .Q(x2h), .clk(clock));  // open: clr
  Register #(.width(32)) u_x3 (.D(Input_h), .en(on3), .Q(x3h), .clk(clock));  // open: clr
  Register #(.width(32)) u_x4 (.D(Input_h), .en(on4), .Q(x4h), .clk(clock));  // open: clr
  Register #(.width(32)) u_x5 (.D(Input_h), .en(on5), .Q(x5h), .clk(clock));  // open: clr
  Register #(.width(32)) u_x6 (.D(Input_h), .en(on6), .Q(x6h), .clk(clock));  // open: clr
  Register #(.width(32)) u_x7 (.D(Input_h), .en(on7), .Q(x7h), .clk(clock));  // open: clr
  not not_10 (not_10_out, xd[4]);
  not not_11 (not_11_out, xd[2]);
  not not_12 (not_12_out, xd[3]);
  not not_13 (not_13_out, xd[0]);
  and and_3 (on2, not_13_out, xd[1], not_11_out, not_12_out, not_10_out);
  not not_14 (not_14_out, xd[0]);
  not not_15 (not_15_out, xd[2]);
  not not_16 (not_16_out, xd[4]);
  not not_17 (not_17_out, xd[3]);
  not not_18 (not_18_out, xd[1]);
  and and_4 (on3, xd[0], xd[1], not_15_out, not_17_out, not_16_out);
  and and_5 (on4, not_14_out, not_18_out, xd[2], not_21_out, not_19_out);
  Register #(.width(32)) u_x8 (.D(Input_h), .en(on8), .Q(x8h));  // open: clk, clr
  Register #(.width(32)) u_x9 (.D(Input_h), .en(on9), .Q(x9h), .clk(clock));  // open: clr
  Register #(.width(32)) u_x10 (.D(Input_h), .en(on10), .Q(x10h), .clk(clock));  // open: clr
  Register #(.width(32)) u_x11 (.D(Input_h), .en(on11), .Q(x11h), .clk(clock));  // open: clr
  Register #(.width(32)) u_x12 (.D(Input_h), .en(on12), .Q(x12h), .clk(clock));  // open: clr
  Register #(.width(32)) u_x13 (.D(Input_h), .en(on13), .Q(x13h), .clk(clock));  // open: clr
  Register #(.width(32)) u_x14 (.D(Input_h), .en(on14), .Q(x14h), .clk(clock));  // open: clr
  Register #(.width(32)) u_x15 (.D(Input_h), .en(on15), .Q(x15h), .clk(clock));  // open: clr
  not not_19 (not_19_out, xd[4]);
  not not_20 (not_20_out, xd[1]);
  not not_21 (not_21_out, xd[3]);
  not not_22 (not_22_out, xd[3]);
  not not_23 (not_23_out, xd[4]);
  and and_6 (on5, xd[0], not_20_out, xd[2], not_22_out, not_23_out);
  not not_24 (not_24_out, xd[4]);
  not not_25 (not_25_out, xd[0]);
  not not_26 (not_26_out, xd[3]);
  and and_7 (on6, not_25_out, xd[1], xd[2], not_26_out, not_24_out);
  Register #(.width(32)) u_x16 (.D(Input_h), .en(on16), .Q(x16h));  // open: clk, clr
  Register #(.width(32)) u_x17 (.D(Input_h), .en(on17), .Q(x17h), .clk(clock));  // open: clr
  Register #(.width(32)) u_x18 (.D(Input_h), .en(on18), .Q(x18h), .clk(clock));  // open: clr
  Register #(.width(32)) u_x19 (.D(Input_h), .en(on19), .Q(x19h), .clk(clock));  // open: clr
  Register #(.width(32)) u_x20 (.D(Input_h), .en(on20), .Q(x20h), .clk(clock));  // open: clr
  Register #(.width(32)) u_x21 (.D(Input_h), .en(on21), .Q(x21h), .clk(clock));  // open: clr
  Register #(.width(32)) u_x22 (.D(Input_h), .en(on22), .Q(x22h), .clk(clock));  // open: clr
  Register #(.width(32)) u_x23 (.D(Input_h), .en(on23), .Q(x23h), .clk(clock));  // open: clr
  not not_27 (not_27_out, xd[0]);
  not not_28 (not_28_out, xd[4]);
  not not_29 (not_29_out, xd[3]);
  not not_30 (not_30_out, xd[2]);
  not not_31 (not_31_out, xd[1]);
  and and_8 (on8, not_27_out, not_31_out, not_30_out, xd[3], not_34_out);
  and and_9 (on7, xd[0], xd[1], xd[2], not_29_out, not_28_out);
  not not_32 (not_32_out, xd[1]);
  not not_33 (not_33_out, xd[2]);
  not not_34 (not_34_out, xd[4]);
  not not_35 (not_35_out, xd[4]);
  and and_10 (on9, xd[0], not_32_out, not_33_out, xd[3], not_35_out);
  Register #(.width(32)) u_x24 (.D(Input_h), .en(on24), .Q(x24h));  // open: clk, clr
  Register #(.width(32)) u_x25 (.D(Input_h), .en(on25), .Q(x25h), .clk(clock));  // open: clr
  Register #(.width(32)) u_x26 (.D(Input_h), .en(on26), .Q(x26h), .clk(clock));  // open: clr
  Register #(.width(32)) u_x27 (.D(Input_h), .en(on27), .Q(x27h), .clk(clock));  // open: clr
  Register #(.width(32)) u_x28 (.D(Input_h), .en(on28), .Q(x28h), .clk(clock));  // open: clr
  Register #(.width(32)) u_x29 (.D(Input_h), .en(on29), .Q(x29h), .clk(clock));  // open: clr
  Register #(.width(32)) u_x30 (.D(Input_h), .en(on30), .Q(x30h), .clk(clock));  // open: clr
  Register #(.width(32)) u_x31 (.D(Input_h), .en(on31), .Q(x31h), .clk(clock));  // open: clr
  not not_36 (not_36_out, xd[2]);
  not not_37 (not_37_out, xd[4]);
  not not_38 (not_38_out, xd[0]);
  and and_11 (on10, not_38_out, xd[1], not_36_out, xd[3], not_37_out);
  not not_39 (not_39_out, xd[1]);
  not not_40 (not_40_out, xd[0]);
  not not_41 (not_41_out, xd[2]);
  not not_42 (not_42_out, xd[4]);
  and and_12 (on12, not_40_out, not_39_out, xd[2], xd[3], not_43_out);
  and and_13 (on11, xd[0], xd[1], not_41_out, xd[3], not_42_out);
  not not_43 (not_43_out, xd[4]);
  not not_44 (not_44_out, xd[4]);
  not not_45 (not_45_out, xd[1]);
  and and_14 (on13, xd[0], not_45_out, xd[2], xd[3], not_44_out);
  not not_46 (not_46_out, xd[4]);
  not not_47 (not_47_out, xd[0]);
  and and_15 (on14, not_47_out, xd[1], xd[2], xd[3], not_46_out);
  not not_48 (not_48_out, xd[1]);
  not not_49 (not_49_out, xd[4]);
  not not_50 (not_50_out, xd[2]);
  not not_51 (not_51_out, xd[0]);
  and and_16 (on16, not_51_out, not_48_out, not_50_out, not_54_out, xd[4]);
  and and_17 (on15, xd[0], xd[1], xd[2], xd[3], not_49_out);
  Multiplexer #(.select(5), .width(32)) multiplexer_1 (
    .in0(x0h), .in1(x1h), .in2(x2h), .in3(x3h), .in4(x4h), .in5(x5h), .in6(x6h), .in7(x7h), .in8(x8h),
    .in9(x9h), .in10(x10h), .in11(x11h), .in12(x12h), .in13(x13h), .in14(x14h), .in15(x15h), .in16(x16h),
    .in17(x17h), .in18(x18h), .in19(x19h), .in20(x20h), .in21(x21h), .in22(x22h), .in23(x23h), .in24(x24h),
    .in25(x25h), .in26(x26h), .in27(x27h), .in28(x28h), .in29(x29h), .in30(x30h), .in31(x31h),
    .out(output_xn_high), .sel(xn));  // open: en
  Multiplexer #(.select(5), .width(32)) multiplexer_2 (
    .in0(x0h), .in1(x1h), .in2(x2h), .in3(x3h), .in4(x4h), .in5(x5h), .in6(x6h), .in7(x7h), .in8(x8h),
    .in9(x9h), .in10(x10h), .in11(x11h), .in12(x12h), .in13(x13h), .in14(x14h), .in15(x15h), .in16(x16h),
    .in17(x17h), .in18(x18h), .in19(x19h), .in20(x20h), .in21(x21h), .in22(x22h), .in23(x23h), .in24(x24h),
    .in25(x25h), .in26(x26h), .in27(x27h), .in28(x28h), .in29(x29h), .in30(x30h), .in31(x31h),
    .out(output_xm_high), .sel(xm));  // open: en
  not not_52 (not_52_out, xd[3]);
  not not_53 (not_53_out, xd[1]);
  not not_54 (not_54_out, xd[3]);
  not not_55 (not_55_out, xd[2]);
  and and_18 (on17, xd[0], not_53_out, not_55_out, not_52_out, xd[4]);
  not not_56 (not_56_out, xd[2]);
  not not_57 (not_57_out, xd[3]);
  not not_58 (not_58_out, xd[0]);
  and and_19 (on18, not_58_out, xd[1], not_56_out, not_57_out, xd[4]);
  not not_59 (not_59_out, xd[0]);
  not not_60 (not_60_out, xd[3]);
  not not_61 (not_61_out, xd[2]);
  not not_62 (not_62_out, xd[1]);
  and and_20 (on20, not_59_out, not_62_out, xd[2], not_64_out, xd[4]);
  and and_21 (on19, xd[0], xd[1], not_61_out, not_60_out, xd[4]);
  not not_63 (not_63_out, xd[1]);
  not not_64 (not_64_out, xd[3]);
  not not_65 (not_65_out, xd[3]);
  and and_22 (on21, xd[0], not_63_out, xd[2], not_65_out, xd[4]);
  Register #(.width(32)) x0_2 (.D(Input_l), .en(on0), .Q(x0), .clk(clock));  // open: clr
  Register #(.width(32)) x1_2 (.D(Input_l), .en(on1), .Q(x1), .clk(clock));  // open: clr
  Register #(.width(32)) x2_2 (.D(Input_l), .en(on2), .Q(x2), .clk(clock));  // open: clr
  Register #(.width(32)) x3_2 (.D(Input_l), .en(on3), .Q(x3), .clk(clock));  // open: clr
  Register #(.width(32)) x4_2 (.D(Input_l), .en(on4), .Q(x4), .clk(clock));  // open: clr
  Register #(.width(32)) x5_2 (.D(Input_l), .en(on5), .Q(x5), .clk(clock));  // open: clr
  Register #(.width(32)) x6_2 (.D(Input_l), .en(on6), .Q(x6), .clk(clock));  // open: clr
  Register #(.width(32)) x7_2 (.D(Input_l), .en(on7), .Q(x7), .clk(clock));  // open: clr
  not not_66 (not_66_out, xd[0]);
  not not_67 (not_67_out, xd[3]);
  and and_23 (on22, not_66_out, xd[1], xd[2], not_67_out, xd[4]);
  // NOT_Gate not_68 is placed but not wired
  not not_69 (not_69_out, xd[0]);
  not not_70 (not_70_out, xd[1]);
  not not_71 (not_71_out, xd[2]);
  not not_72 (not_72_out, xd[3]);
  and and_24 (on23, xd[0], xd[1], xd[2], not_72_out, xd[4]);
  and and_25 (on24, not_69_out, not_70_out, not_71_out, xd[3], xd[4]);
  Register #(.width(32)) x8_2 (.D(Input_l), .en(on8), .Q(x8), .clk(clock));  // open: clr
  Register #(.width(32)) x9_2 (.D(Input_l), .en(on9), .Q(x9), .clk(clock));  // open: clr
  Register #(.width(32)) x10_2 (.D(Input_l), .en(on10), .Q(x10), .clk(clock));  // open: clr
  Register #(.width(32)) x11_2 (.D(Input_l), .en(on11), .Q(x11), .clk(clock));  // open: clr
  Register #(.width(32)) x12_2 (.D(Input_l), .en(on12), .Q(x12), .clk(clock));  // open: clr
  Register #(.width(32)) x13_2 (.D(Input_l), .en(on13), .Q(x13), .clk(clock));  // open: clr
  Register #(.width(32)) x14_2 (.D(Input_l), .en(on14), .Q(x14), .clk(clock));  // open: clr
  Register #(.width(32)) x15_2 (.D(Input_l), .en(on15), .Q(x15), .clk(clock));  // open: clr
  not not_73 (not_73_out, xd[1]);
  not not_74 (not_74_out, xd[2]);
  and and_26 (on25, xd[0], not_73_out, not_74_out, xd[3], xd[4]);
  not not_75 (not_75_out, xd[0]);
  not not_76 (not_76_out, xd[2]);
  and and_27 (on26, not_75_out, xd[1], not_76_out, xd[3], xd[4]);
  Register #(.width(32)) x16_2 (.D(Input_l), .en(on16), .Q(x16), .clk(clock));  // open: clr
  Register #(.width(32)) x17_2 (.D(Input_l), .en(on17), .Q(x17), .clk(clock));  // open: clr
  Register #(.width(32)) x18_2 (.D(Input_l), .en(on18), .Q(x18), .clk(clock));  // open: clr
  Register #(.width(32)) x19_2 (.D(Input_l), .en(on19), .Q(x19), .clk(clock));  // open: clr
  Register #(.width(32)) x20_2 (.D(Input_l), .en(on20), .Q(x20), .clk(clock));  // open: clr
  Register #(.width(32)) x21_2 (.D(Input_l), .en(on21), .Q(x21), .clk(clock));  // open: clr
  Register #(.width(32)) x22_2 (.D(Input_l), .en(on22), .Q(x22), .clk(clock));  // open: clr
  Register #(.width(32)) x23_2 (.D(Input_l), .en(on23), .Q(x23), .clk(clock));  // open: clr
  not not_77 (not_77_out, xd[0]);
  not not_78 (not_78_out, xd[2]);
  not not_79 (not_79_out, xd[1]);
  and and_28 (on28, not_77_out, not_79_out, xd[2], xd[3], xd[4]);
  and and_29 (on27, xd[0], xd[1], not_78_out, xd[3], xd[4]);
  not not_80 (not_80_out, xd[1]);
  and and_30 (on29, xd[0], not_80_out, xd[2], xd[3], xd[4]);
  Register #(.width(32)) x24_2 (.D(Input_l), .en(on24), .Q(x24), .clk(clock));  // open: clr
  Register #(.width(32)) x25_2 (.D(Input_l), .en(on25), .Q(x25), .clk(clock));  // open: clr
  Register #(.width(32)) x26_2 (.D(Input_l), .en(on26), .Q(x26), .clk(clock));  // open: clr
  Register #(.width(32)) x27_2 (.D(Input_l), .en(on27), .Q(x27), .clk(clock));  // open: clr
  Register #(.width(32)) x28_2 (.D(Input_l), .en(on28), .Q(x28), .clk(clock));  // open: clr
  Register #(.width(32)) x29_2 (.D(Input_l), .en(on29), .Q(x29), .clk(clock));  // open: clr
  Register #(.width(32)) x30_2 (.D(Input_l), .en(on30), .Q(x30), .clk(clock));  // open: clr
  Register #(.width(32)) x31_2 (.D(Input_l), .en(on31), .Q(x31), .clk(clock));  // open: clr
  not not_81 (not_81_out, xd[0]);
  and and_31 (on30, not_81_out, xd[1], xd[2], xd[3], xd[4]);
  and and_32 (on31, xd[0], xd[1], xd[2], xd[3], xd[4]);
  Multiplexer #(.select(5), .width(32)) multiplexer_3 (
    .in0(x0), .in1(x1), .in2(x2), .in3(x3), .in4(x4), .in5(x5), .in6(x6), .in7(x7), .in8(x8), .in9(x9),
    .in10(x10), .in11(x11), .in12(x12), .in13(x13), .in14(x14), .in15(x15), .in16(x16), .in17(x17),
    .in18(x18), .in19(x19), .in20(x20), .in21(x21), .in22(x22), .in23(x23), .in24(x24), .in25(x25),
    .in26(x26), .in27(x27), .in28(x28), .in29(x29), .in30(x30), .in31(x31), .out(output_xn_low), .sel(xn));  // open: en
  Multiplexer #(.select(5), .width(32)) multiplexer_4 (
    .in0(x0), .in1(x1), .in2(x2), .in3(x3), .in4(x4), .in5(x5), .in6(x6), .in7(x7), .in8(x8), .in9(x9),
    .in10(x10), .in11(x11), .in12(x12), .in13(x13), .in14(x14), .in15(x15), .in16(x16), .in17(x17),
    .in18(x18), .in19(x19), .in20(x20), .in21(x21), .in22(x22), .in23(x23), .in24(x24), .in25(x25),
    .in26(x26), .in27(x27), .in28(x28), .in29(x29), .in30(x30), .in31(x31), .out(output_xm_low), .sel(xm));  // open: en
endmodule
