// Logisim project Proyecto04-14005476.circ as structural Verilog: 4 circuits, main circuit main
module main (
  input  in_1,
  input  in_2,
  input  RESET
);

  wire _1, _2, _3, _4, _5, _6, _7, _8, _9, _10, _11, _12, _13, _14, _15, BB, BB_eneble, CLOCK, clock_1_out,
       comparator_1_lt, comparator_2_eq, jmp_1_out_2, jr_1_out_2, nand_1_out, not_1_out, not_2_out,
       not_3_out, not_4_out, or_2_out, read_BB, Set_BB_to_0;
  wire [3:0] From_RAM, OP_Code, Rdest, Rsrc1, Rsrc2;
  wire [7:0] toRAM;
  wire [15:0] adder_1_out, adder_2_out, and_1_out, BB_FOUBU, controlled_buffer_1_out,
       controlled_buffer_2_out, demultiplexer_2_out0, multiplexer_8_out, Mux1, Mux2, or_1_out, R1, R2, R3,
       R4, R5, R6, R7, R8, R9, R10, R11, R12, R13, R14, R15, Registro_1_q, Registro_2_q, Registro_3_q,
       Registro_4_q, Registro_5_q, Registro_6_q, Registro_7_q, Registro_8_q, Registro_9_q, Registro_10_q,
       Registro_11_q, Registro_12_q, Registro_13_q, Registro_14_q, Registro_15_q, SPC, subtractor_1_out,
       xor_1_out;

  Register #(.width(16)) Registro_1 (.D(R1), .en(_1), .Q(Registro_1_q), .clk(CLOCK), .clr(RESET));
  Register #(.width(16)) Registro_2 (.D(R2), .en(_2), .Q(Registro_2_q), .clk(CLOCK), .clr(RESET));
  Register #(.width(16)) Registro_3 (.D(R3), .en(_3), .Q(Registro_3_q), .clk(CLOCK), .clr(RESET));
  Register #(.width(16)) Registro_4 (.D(R4), .en(_4), .Q(Registro_4_q), .clk(CLOCK), .clr(RESET));
  Register #(.width(16)) Registro_5 (.D(R5), .en(_5), .Q(Registro_5_q), .clk(CLOCK), .clr(RESET));
  Register #(.width(16)) Registro_6 (.D(R6), .en(_6), .Q(Registro_6_q), .clk(CLOCK), .clr(RESET));
  Register #(.width(16)) Registro_7 (.D(R7), .en(_7), .Q(Registro_7_q), .clk(CLOCK), .clr(RESET));
  Register #(.width(16)) Registro_8 (.D(R8), .en(_8), .Q(Registro_8_q), .clk(CLOCK), .clr(RESET));
  Register #(.width(16)) Registro_9 (.D(R9), .en(_9), .Q(Registro_9_q), .clk(CLOCK), .clr(RESET));
  Register #(.width(16)) Registro_10 (.D(R10), .en(_10), .Q(Registro_10_q), .clk(CLOCK), .clr(RESET));
  Register #(.width(16)) Registro_11 (.D(R11), .en(_11), .Q(Registro_11_q), .clk(CLOCK), .clr(RESET));
  Register #(.width(16)) Registro_12 (.D(R12), .en(_12), .Q(Registro_12_q), .clk(CLOCK), .clr(RESET));
  Register #(.width(16)) Registro_13 (.D(R13), .en(_13), .Q(Registro_13_q), .clk(CLOCK), .clr(RESET));
  Register #(.width(16)) Registro_14 (.D(R14), .en(_14), .Q(Registro_14_q), .clk(CLOCK), .clr(RESET));
  Register #(.width(16)) Registro_15 (.D(R15), .en(_15), .Q(Registro_15_q), .clk(CLOCK), .clr(RESET));
  Multiplexer #(.select(4)) multiplexer_1 (
    .in0(1'b0), .in1(1'b0), .in2(1'b0), .in3(1'b0), .in4(1'b0), .in5(1'b0), .in6(1'b1), .in7(1'b1),
    .in8(1'b0), .in9(1'b0), .in10(1'b0), .in11(1'b0), .in12(1'b0), .in13(1'b0), .in14(1'b0), .in15(1'b0),
    .out(BB_eneble), .sel(OP_Code), .en(nand_1_out));
  Demultiplexer #(.select(4), .enable("false")) demultiplexer_1 (
    .out1(_1), .out2(_2), .out3(_3), .out4(_4), .out5(_5), .out6(_6), .out7(_7), .out8(_8), .out9(_9),
    .out10(_10), .out11(_11), .out12(_12), .out13(_13), .out14(_14), .out15(_15), .in(1'b1), .sel(Rdest));  // open: out0
  Adder #(.width(16)) adder_1 (.a(SPC), .b(BB_FOUBU), .out(adder_1_out));  // open: cin, cout
  JMP jmp_1 (.out_2(jmp_1_out_2), .in_1(OP_Code));
  JR jr_1 (.out_2(jr_1_out_2), .in_1(OP_Code));
  not not_1 (not_1_out, jr_1_out_2);
  assign controlled_buffer_1_out = not_2_out ? adder_1_out : 16'bz;  // Controlled_Buffer controlled_buffer_1
  assign controlled_buffer_2_out = not_1_out ? controlled_buffer_1_out : 16'bz;  // Controlled_Buffer controlled_buffer_2
  not not_2 (not_2_out, jmp_1_out_2);
  assign controlled_buffer_1_out = jmp_1_out_2 ? {{8{1'b0}}, Rsrc1, Rsrc2} : 16'bz;  // Controlled_Buffer controlled_buffer_3
  Multiplexer #(.select(4), .width(16), .enable("false")) multiplexer_2 (
    .in0({16{1'b0}}), .in1(Registro_1_q), .in2(Registro_2_q), .in3(Registro_3_q), .in4(Registro_4_q),
    .in5(Registro_5_q), .in6(Registro_6_q), .in7(Registro_7_q), .in8(Registro_8_q), .in9(Registro_9_q),
    .in10(Registro_10_q), .in11(Registro_11_q), .in12(Registro_12_q), .in13(Registro_13_q),
    .in14(Registro_14_q), .in15(Registro_15_q), .out(Mux1), .sel(Rsrc1));
  Multiplexer #(.select(4), .width(16), .enable("false")) multiplexer_3 (
    .in0({16{1'b0}}), .in1(Registro_1_q), .in2(Registro_2_q), .in3(Registro_3_q), .in4(Registro_4_q),
    .in5(Registro_5_q), .in6(Registro_6_q), .in7(Registro_7_q), .in8(Registro_8_q), .in9(Registro_9_q),
    .in10(Registro_10_q), .in11(Registro_11_q), .in12(Registro_12_q), .in13(Registro_13_q),
    .in14(Registro_14_q), .in15(Registro_15_q), .out(Mux2), .sel(Rsrc2));
  Multiplexer #(.select(4), .width(8), .enable("false")) multiplexer_4 (
    .in8({Rsrc2, Rsrc1}), .out(toRAM), .sel(OP_Code));  // open: in0, in1, in2, in3, in4, in5, in6, in7, in9, in10, in11, in12, in13, in14, in15
  assign CLOCK = in_2 ? in_1 : 1'bz;  // Controlled_Buffer controlled_buffer_4
  assign controlled_buffer_2_out = jr_1_out_2 ? Mux1 : 16'bz;  // Controlled_Buffer controlled_buffer_5
  Register #(.width(16)) register_1 (.D(controlled_buffer_2_out), .Q(SPC), .clk(CLOCK), .clr(RESET));  // open: en
  assign CLOCK = not_3_out ? clock_1_out : 1'bz;  // Controlled_Buffer controlled_buffer_6
  not not_3 (not_3_out, in_2);
  Clock clock_1 (.out(clock_1_out));
  assign and_1_out = Mux1 & Mux2;  // AND_Gate and_1, 16 bits wide
  assign or_1_out = Mux1 | Mux2;  // OR_Gate or_1, 16 bits wide
  Multiplexer #(.select(4), .width(16)) multiplexer_5 (
    .in0(16'h1), .in1(16'h1), .in2(16'h1), .in3(16'h1), .in4(16'h1), .in5(16'h1), .in6(16'h1), .in7(16'h1),
    .in8(16'h1), .in9(16'h1), .in10(16'h1), .in11(16'h1), .in13(16'h1), .in15(16'h1), .out(BB_FOUBU),
    .sel(OP_Code), .en(nand_1_out));  // open: in12, in14
  Multiplexer #(.select(4), .width(16)) multiplexer_6 (
    .in0(16'h1), .in1(16'h1), .in2(16'h1), .in3(16'h1), .in4(16'h1), .in5(16'h1), .in6(16'h1), .in7(16'h1),
    .in8(16'h1), .in9(16'h1), .in10(16'h1), .in11(16'h1), .in13({Rsrc2, Rsrc1, {8{1'b0}}}), .in15(16'h1),
    .out(BB_FOUBU), .sel(OP_Code), .en(Set_BB_to_0));  // open: in12, in14
  Multiplexer #(.select(4)) multiplexer_7 (
    .in0(1'b0), .in1(1'b0), .in2(1'b0), .in3(1'b0), .in4(1'b0), .in5(1'b0), .in6(1'b1), .in7(1'b1),
    .in8(1'b0), .in9(1'b0), .in10(1'b0), .in11(1'b0), .in12(1'b0), .in13(1'b1), .in14(1'b0), .in15(1'b0),
    .out(BB_eneble), .sel(OP_Code), .en(Set_BB_to_0));
  Adder #(.width(16)) adder_2 (.a(Mux1), .b(Mux2), .out(adder_2_out));  // open: cin, cout
  Subtractor #(.width(16)) subtractor_1 (.a(Mux1), .b(Mux2), .out(subtractor_1_out));  // open: bin, bout
  assign xor_1_out = Mux1 ^ Mux2;  // XOR_Gate xor_1, 16 bits wide
  Comparator #(.width(16)) comparator_1 (.a(Mux1), .b(Mux2), .lt(comparator_1_lt));  // open: gt, eq
  assign BB = not_4_out ? or_2_out : 1'bz;  // Controlled_Buffer controlled_buffer_7
  or or_2 (or_2_out, comparator_1_lt, comparator_2_eq);
  not not_4 (not_4_out, Set_BB_to_0);
  Comparator #(.width(16)) comparator_2 (.a(Mux1), .b(Mux2), .eq(comparator_2_eq));  // open: gt, lt
  nand nand_1 (nand_1_out, read_BB, read_BB);
  and and_2 (Set_BB_to_0, read_BB, read_BB);
  assign BB = Set_BB_to_0 ? not_4_out : 1'bz;  // Controlled_Buffer controlled_buffer_8
  ROM #(.addrWidth(16), .dataWidth(16)) rom_1 (.addr(SPC), .data({OP_Code, Rdest, Rsrc1, Rsrc2}), .sel(1'b1));
  RAM #(.addrWidth(4), .dataWidth(4), .bus("separate")) ram_1 (
    .addr(toRAM[3:0]), .din(toRAM[7:4]), .data(From_RAM), .sel(1'b1), .clk(CLOCK), .clr(RESET));  // open: str, ld
  Register #(.width(1)) Branch_Bit (.D(BB), .en(BB_eneble), .Q(read_BB), .clk(CLOCK), .clr(RESET));
  Multiplexer #(.select(4), .width(16), .enable("false")) multiplexer_8 (
    .in0(adder_2_out), .in1(subtractor_1_out), .in2(and_1_out), .in3(or_1_out), .in4(xor_1_out),
    .in5({1'b0, Mux1[15:1]}), .in9({{12{1'b0}}, From_RAM}), .in10({{8{1'b0}}, Rsrc1, Rsrc2}),
    .in11({Rsrc1, Rsrc2, {8{1'b0}}}), .in15(SPC), .out(multiplexer_8_out), .sel(OP_Code));  // open: in6, in7, in8, in12, in13, in14
  Demultiplexer #(.select(4), .width(16), .enable("false")) demultiplexer_2 (
    .out0(demultiplexer_2_out0), .out1(R1), .out2(R2), .out3(R3), .out4(R4), .out5(R5), .out6(R6), .out7(R7),
    .out8(R8), .out9(R9), .out10(R10), .out11(R11), .out12(R12), .out13(R13), .out14(R14), .out15(R15),
    .in(multiplexer_8_out), .sel(Rdest));
  // also tied to GND on the sheet: {demultiplexer_2_out0[0], demultiplexer_2_out0[1], demultiplexer_2_out0[2], demultiplexer_2_out0[3], demultiplexer_2_out0[4], demultiplexer_2_out0[5], demultiplexer_2_out0[6], demultiplexer_2_out0[7], demultiplexer_2_out0[8], demultiplexer_2_out0[9], demultiplexer_2_out0[10], demultiplexer_2_out0[11], demultiplexer_2_out0[12], demultiplexer_2_out0[13], demultiplexer_2_out0[14], demultiplexer_2_out0[15]}

  // Notes on the sheet:
  //   Registro 0
  //   DeMUX que habilita la edición de los Rdest
  //   lo que hara si que cambie el Branch Bit
  //   SB
  //   BRA
  //   BRA
  //   JMP
  //   PROCESADOR
  //   ADD
  //   SUB
  //   AND
  //   OR
  //   XOR
  //   SL
  //   SLT
  //   CMP
  //   LB
  //   LI
  //   LUI
  //   JMP
  //   JR
  //   JMP
  //   JR
  //   lo que hara si que cambie el Branch Bit
  //   JR
  //   Universidad Galileo
  //   JMP
  //   BRA
  //   SPC
  //   ROM
  //   I.E.
  //   RAM
  //   contents of rom_1 (hex, n*v repeats v):
  //   a202 8032 9130
  //   SLT
  //   CMP
  //   SB
  //   BRA
  //   Diego José Bolaños Ruíz
  //   Carné: 14005476
endmodule

module JMP (
  input  [3:0] in_1,
  output out_2
);

  wire not_1_out, not_2_out;

  and and_1 (out_2, in_1[3], in_1[2], not_1_out, not_2_out);
  not not_1 (not_1_out, in_1[1]);
  not not_2 (not_2_out, in_1[0]);
endmodule

module \Será_SB_o_LB  (
  input  in_1,
  input  in_2,
  input  in_3,
  input  in_4,
  output out_5
);

  wire not_1_out, not_2_out, or_1_out;

  or or_1 (or_1_out, in_4, 1'b0);
  not not_1 (not_1_out, in_2);
  not not_2 (not_2_out, in_3);
  and Fuck_Yes (out_5, in_1, not_1_out, not_2_out, or_1_out);

  // Notes on the sheet:
  //   1 se leeran los datos, 0 se grabarán
endmodule

module JR (
  input  [3:0] in_1,
  output out_2
);

  wire not_1_out;

  and and_1 (out_2, in_1[3], in_1[2], in_1[1], not_1_out);
  not not_1 (not_1_out, in_1[0]);
endmodule
