// Logisim project proyecto.circ as structural Verilog: 23 circuits, main circuit main
module main (
  input  jump_o_no,
  input  clear,
  input  [31:0] Instruccion,
  output [31:0] PC
);

  wire C, CARRY, clock, comparator_3_gt, comparator_4_lt, comparator_5_eq, comparator_6_eq,
       decoder_1_load_store, decoder_1_tipo_b, decoder_b_1_b, decoder_b_1_b__eq_b, decoder_b_1_b__ge_b,
       decoder_b_1_b__gt_b, decoder_b_1_b__hi_b, decoder_b_1_b__hs_b, decoder_b_1_b__le_b,
       decoder_b_1_b__lo_b, decoder_b_1_b__ls_b, decoder_b_1_b__lt_b, decoder_b_1_b__mi_b,
       decoder_b_1_b__ne_b, decoder_b_1_b__pl_b, decoder_b_1_b__vc_b, decoder_b_1_b__vs_b, decoder_b_1_bl,
       decoder_b_1_cbnz_b, decoder_b_1_cbz_b, decoder_i_1_add_i, decoder_i_1_adds_i, decoder_i_1_mov_i,
       decoder_i_1_movk_i, decoder_i_1_movn_i, decoder_i_1_sub_i, decoder_i_1_subs_i, decoder_r_1_add_r,
       decoder_r_1_adds_r, decoder_r_1_and_r, decoder_r_1_ands_r, decoder_r_1_asrv_r, decoder_r_1_eor_r,
       decoder_r_1_lslv_r, decoder_r_1_lsrv_r, decoder_r_1_orr_r, decoder_r_1_rorv_r, decoder_r_1_sub_r,
       decoder_r_1_subs_r, I, N, not_1_out, not_2_out, not_3_out, not_4_out, not_5_out, not_7_out, O_C, O_N,
       O_V, O_Z, on, or_1_out, or_2_out, or_3_out, or_4_out, or_5_out, R, V, Z;
  wire [3:0] CONTROL, CONTROL_I, MOV, MOVK, MOVN;
  wire [4:0] B, B_EQ, B_GE, B_GT, B_HI, B_HS, B_LE, B_LO, B_LS, B_LT, B_MI, B_NE, B_PL, B_VC, B_VS, BL, CBNZ,
       CBZ, RD, RM, RN;
  wire [11:0] IMM;
  wire [23:0] bit_extender_1_out, bit_extender_2_out;
  wire [31:0] CARRY_OUT, controlled_buffer_1_out, controlled_buffer_3_out, controlled_buffer_4_out,
       controlled_buffer_5_out, controlled_buffer_48_out, controlled_buffer_49_out, O_HIGH, O_LOW,
       registros_orden_1_output_xm_high, registros_orden_1_output_xm_low, registros_orden_1_output_xn_high,
       registros_orden_1_output_xn_low;

  Program_Counter program_counter_1 (
    .offset_mux(jump_o_no), .clock(clock), .clear(clear), .OUTPUT(PC));  // open: Inmediato
  Bit_Extender #(.in_width(32), .out_width(24)) bit_extender_1 (.in(PC), .out(bit_extender_1_out));
  Bit_Extender #(.in_width(32), .out_width(24)) bit_extender_2 (.in(PC), .out(bit_extender_2_out));
  Memory_Manager_Instrucciones memory_manager_instrucciones_1 (
    .address(bit_extender_1_out), .str(clock), .data(Instruccion));
  Memory_Manager_Instrucciones memory_manager_instrucciones_2 (
    .address(bit_extender_2_out), .str(1'b1), .data(Instruccion));
  Decoder decoder_1 (
    .instruction(Instruccion), .Tipo_B(decoder_1_tipo_b), .Load_Store(decoder_1_load_store), .Tipo_R(R),
    .Tipo_I(I));
  assign controlled_buffer_1_out = decoder_1_tipo_b ? Instruccion : 32'bz;  // Controlled_Buffer controlled_buffer_1
  not not_1 (not_1_out, decoder_1_tipo_b);
  assign controlled_buffer_1_out = not_1_out ? {32{1'b0}} : 32'bz;  // Controlled_Buffer controlled_buffer_2
  not not_2 (not_2_out, R);
  assign controlled_buffer_3_out = not_2_out ? {32{1'b0}} : 32'bz;  // Controlled_Buffer controlled_buffer_3
  not not_3 (not_3_out, I);
  assign controlled_buffer_4_out = not_3_out ? {32{1'b0}} : 32'bz;  // Controlled_Buffer controlled_buffer_4
  assign controlled_buffer_5_out = decoder_1_load_store ? Instruccion : 32'bz;  // Controlled_Buffer controlled_buffer_5
  not not_4 (not_4_out, decoder_1_load_store);
  assign controlled_buffer_5_out = not_4_out ? {32{1'b0}} : 32'bz;  // Controlled_Buffer controlled_buffer_6
  assign controlled_buffer_3_out = R ? Instruccion : 32'bz;  // Controlled_Buffer controlled_buffer_7
  Decoder_R decoder_r_1 (
    .instruction(controlled_buffer_3_out), .ADD_R(decoder_r_1_add_r), .ADDS_R(decoder_r_1_adds_r),
    .SUB_R(decoder_r_1_sub_r), .SUBS_R(decoder_r_1_subs_r), .AND_R(decoder_r_1_and_r),
    .ORR_R(decoder_r_1_orr_r), .EOR_R(decoder_r_1_eor_r), .ANDS_R(decoder_r_1_ands_r),
    .LSLV_R(decoder_r_1_lslv_r), .LSRV_R(decoder_r_1_lsrv_r), .ASRV_R(decoder_r_1_asrv_r),
    .RORV_R(decoder_r_1_rorv_r), .RN(RN), .RM(RM), .RD(RD));
  assign controlled_buffer_4_out = I ? Instruccion : 32'bz;  // Controlled_Buffer controlled_buffer_8
  Clock clock_1 (.out(clock));
  Decoder_B decoder_b_1 (
    .instruction(controlled_buffer_1_out), .CBZ_B(decoder_b_1_cbz_b), .CBNZ_B(decoder_b_1_cbnz_b),
    .B__EQ_B(decoder_b_1_b__eq_b), .B__NE_B(decoder_b_1_b__ne_b), .B__HS_B(decoder_b_1_b__hs_b),
    .B__LO_B(decoder_b_1_b__lo_b), .B__MI_B(decoder_b_1_b__mi_b), .B__PL_B(decoder_b_1_b__pl_b),
    .B__VS_B(decoder_b_1_b__vs_b), .B__VC_B(decoder_b_1_b__vc_b), .B__HI_B(decoder_b_1_b__hi_b),
    .B__LS_B(decoder_b_1_b__ls_b), .B__GE_B(decoder_b_1_b__ge_b), .B__LT_B(decoder_b_1_b__lt_b),
    .B__GT_B(decoder_b_1_b__gt_b), .B__LE_B(decoder_b_1_b__le_b), .B(decoder_b_1_b), .BL(decoder_b_1_bl));
  Decoder_STR_o_LDR decoder_str_o_ldr_1 (.instruction(controlled_buffer_5_out));  // open: STR, LDR
  or or_1 (or_1_out, decoder_r_1_adds_r, decoder_r_1_add_r);
  Decoder_I decoder_i_1 (
    .instruction(controlled_buffer_4_out), .ADD_I(decoder_i_1_add_i), .ADDS_I(decoder_i_1_adds_i),
    .SUB_I(decoder_i_1_sub_i), .SUBS_I(decoder_i_1_subs_i), .MOVN_I(decoder_i_1_movn_i),
    .MOV_I(decoder_i_1_mov_i), .MOVK_I(decoder_i_1_movk_i), .IMM(IMM), .RN(RN), .RD(RD));
  or or_2 (or_2_out, decoder_r_1_and_r, decoder_r_1_ands_r);
  or or_3 (or_3_out, decoder_r_1_subs_r, decoder_r_1_sub_r);
  or or_4 (or_4_out, decoder_i_1_subs_i, decoder_i_1_sub_i);
  or or_5 (or_5_out, decoder_i_1_adds_i, decoder_i_1_add_i);
  Controlled_Buffer controlled_buffer_9 (.en(R));  // open: in, out
  Controlled_Buffer controlled_buffer_10 (.en(I));  // open: in, out
  assign CONTROL = or_1_out ? 4'b0000 : 4'bz;  // Controlled_Buffer controlled_buffer_11
  assign CONTROL = or_5_out ? 4'b1001 : 4'bz;  // Controlled_Buffer controlled_buffer_12
  Controlled_Buffer #(.width(5)) controlled_buffer_13 (.in(CBZ), .en(decoder_b_1_cbz_b));  // open: out
  Controlled_Buffer #(.width(5)) controlled_buffer_14 (.in(CBNZ), .en(decoder_b_1_cbnz_b));  // open: out
  assign on = decoder_r_1_adds_r ? 1'b1 : 1'bz;  // Controlled_Buffer controlled_buffer_15
  assign on = decoder_i_1_adds_i ? 1'b1 : 1'bz;  // Controlled_Buffer controlled_buffer_16
  Controlled_Buffer #(.width(5)) controlled_buffer_17 (.in(B_EQ), .en(decoder_b_1_b__eq_b));  // open: out
  Controlled_Buffer #(.width(5)) controlled_buffer_18 (.in(B_NE), .en(decoder_b_1_b__ne_b));  // open: out
  assign CONTROL = or_3_out ? 4'b0001 : 4'bz;  // Controlled_Buffer controlled_buffer_19
  assign on = decoder_r_1_subs_r ? 1'b1 : 1'bz;  // Controlled_Buffer controlled_buffer_20
  assign on = decoder_i_1_subs_i ? 1'b1 : 1'bz;  // Controlled_Buffer controlled_buffer_21
  assign CONTROL_I = or_4_out ? 4'b1010 : 4'bz;  // Controlled_Buffer controlled_buffer_22
  Controlled_Buffer #(.width(5)) controlled_buffer_23 (.in(B_HS), .en(decoder_b_1_b__hs_b));  // open: out
  Controlled_Buffer #(.width(5)) controlled_buffer_24 (.in(B_LO), .en(decoder_b_1_b__lo_b));  // open: out
  assign CONTROL = or_2_out ? 4'b0010 : 4'bz;  // Controlled_Buffer controlled_buffer_25
  assign CONTROL = decoder_r_1_orr_r ? 4'b0011 : 4'bz;  // Controlled_Buffer controlled_buffer_26
  assign CONTROL_I = decoder_i_1_movn_i ? MOVN : 4'bz;  // Controlled_Buffer controlled_buffer_27
  Registros_orden registros_orden_1 (
    .xd(RD), .xm(RM), .xn(RN), .Input_h(O_HIGH), .Input_l(O_LOW), .clock(clock),
    .output_xn_low(registros_orden_1_output_xn_low), .output_xn_high(registros_orden_1_output_xn_high),
    .output_xm_low(registros_orden_1_output_xm_low), .output_xm_high(registros_orden_1_output_xm_high));
  Controlled_Buffer #(.width(5)) controlled_buffer_28 (.in(B_MI), .en(decoder_b_1_b__mi_b));  // open: out
  Controlled_Buffer #(.width(5)) controlled_buffer_29 (.in(B_PL), .en(decoder_b_1_b__pl_b));  // open: out
  assign CONTROL = decoder_r_1_eor_r ? 4'b0100 : 4'bz;  // Controlled_Buffer controlled_buffer_30
  assign CONTROL_I = decoder_i_1_mov_i ? MOV : 4'bz;  // Controlled_Buffer controlled_buffer_31
  ALU alu_1 (
    .CARRY(CARRY), .Input_high(registros_orden_1_output_xn_high),
    .Input_low(registros_orden_1_output_xn_low), .Input_high_2(registros_orden_1_output_xm_high),
    .Input_low_2(registros_orden_1_output_xm_low), .Output_high(O_HIGH), .control(CONTROL),
    .Output_low(O_LOW), .IMM(IMM));
  Controlled_Buffer #(.width(5)) controlled_buffer_32 (.in(B_VS), .en(decoder_b_1_b__vs_b));  // open: out
  Controlled_Buffer #(.width(5)) controlled_buffer_33 (.in(B_VC), .en(decoder_b_1_b__vc_b));  // open: out
  assign on = decoder_r_1_ands_r ? 1'b1 : 1'bz;  // Controlled_Buffer controlled_buffer_34
  assign CONTROL_I = decoder_i_1_movk_i ? MOVK : 4'bz;  // Controlled_Buffer controlled_buffer_35
  Controlled_Buffer #(.width(5)) controlled_buffer_36 (.in(B_LS), .en(decoder_b_1_b__ls_b));  // open: out
  Controlled_Buffer #(.width(5)) controlled_buffer_37 (.in(B_HI), .en(decoder_b_1_b__hi_b));  // open: out
  assign CONTROL = decoder_r_1_lslv_r ? 4'b0101 : 4'bz;  // Controlled_Buffer controlled_buffer_38
  assign CONTROL = decoder_r_1_lsrv_r ? 4'b0110 : 4'bz;  // Controlled_Buffer controlled_buffer_39
  Controlled_Buffer #(.width(5)) controlled_buffer_40 (.in(B_GE), .en(decoder_b_1_b__ge_b));  // open: out
  Controlled_Buffer #(.width(5)) controlled_buffer_41 (.in(B_LT), .en(decoder_b_1_b__lt_b));  // open: out
  assign CONTROL = decoder_r_1_asrv_r ? 4'b0111 : 4'bz;  // Controlled_Buffer controlled_buffer_42
  Controlled_Buffer #(.width(5)) controlled_buffer_43 (.in(B_LE), .en(decoder_b_1_b__le_b));  // open: out
  Controlled_Buffer #(.width(5)) controlled_buffer_44 (.in(B_GT), .en(decoder_b_1_b__gt_b));  // open: out
  assign CONTROL = decoder_r_1_rorv_r ? 4'b1000 : 4'bz;  // Controlled_Buffer controlled_buffer_45
  Controlled_Buffer #(.width(5)) controlled_buffer_46 (.in(BL), .en(decoder_b_1_bl));  // open: out
  Controlled_Buffer #(.width(5)) controlled_buffer_47 (.in(B), .en(decoder_b_1_b));  // open: out
  Banderas banderas_1 (
    .input_z(Z), .input_n(N), .input_c(C), .input_v(V), .clock(clock), .on(on), .output_z(O_Z),
    .output_n(O_N), .output_c(O_C), .output_v(O_V));
  Comparator #(.width(32)) comparator_1 (.b({32{1'b0}}), .eq(Z));  // open: a, gt, lt
  Comparator #(.width(32)) comparator_2 (.b({32{1'b0}}), .lt(N));  // open: a, gt, eq
  Comparator #(.width(32)) comparator_3 (.b({32{1'b1}}), .gt(comparator_3_gt));  // open: a, eq, lt
  Comparator #(.width(32)) comparator_4 (.b({32{1'b0}}), .lt(comparator_4_lt));  // open: a, gt, eq
  assign CARRY_OUT = {{31{1'b0}}, CARRY};  // Bit_Extender bit_extender_3
  assign controlled_buffer_48_out = comparator_3_gt ? CARRY_OUT : 32'bz;  // Controlled_Buffer controlled_buffer_48
  assign controlled_buffer_49_out = comparator_4_lt ? CARRY_OUT : 32'bz;  // Controlled_Buffer controlled_buffer_49
  not not_5 (not_5_out, comparator_3_gt);
  assign controlled_buffer_48_out = not_5_out ? {32{1'b0}} : 32'bz;  // Controlled_Buffer controlled_buffer_50
  not not_6 (C, comparator_5_eq);
  Comparator #(.width(32)) comparator_5 (
    .a(controlled_buffer_48_out), .b({32{1'b0}}), .eq(comparator_5_eq));  // open: gt, lt
  not not_7 (not_7_out, comparator_4_lt);
  assign controlled_buffer_49_out = not_7_out ? {32{1'b0}} : 32'bz;  // Controlled_Buffer controlled_buffer_51
  not not_8 (V, comparator_6_eq);
  Comparator #(.width(32)) comparator_6 (
    .a(controlled_buffer_49_out), .b({32{1'b0}}), .eq(comparator_6_eq));  // open: gt, lt
endmodule

module ALU (
  input  [31:0] Input_high,
  input  [31:0] Input_low,
  input  [31:0] Input_high_2,
  input  [31:0] Input_low_2,
  input  [3:0] control,
  input  [11:0] IMM,
  output CARRY,
  output [31:0] Output_high,
  output [31:0] Output_low
);

  wire adder_3_cout, adder_4_cout, subtractor_3_bout, subtractor_4_bout;
  wire [31:0] adder_1_out, adder_2_out, adder_3_out, adder_4_out, and_1_out, and_2_out, asrv_1_highp,
       asrv_1_lowp, asrv_1_out_7, bit_extender_1_out, IMM_HIGH, IMM_LOW, or_1_out, or_2_out, rorv_1_highp,
       rorv_1_out_7, shift_left_1_salida_high, shift_left_1_salida_low, shift_right_1_salida_high,
       shift_right_1_salida_low, subtractor_1_out, subtractor_2_out, subtractor_3_out, subtractor_4_out,
       xor_1_out, xor_2_out;

  assign bit_extender_1_out = {{20{1'b0}}, IMM};  // Bit_Extender bit_extender_1
  EXTENDER_32_64 extender_32_64_1 (.INPUT(bit_extender_1_out), .LOW(IMM_LOW), .HIGH(IMM_HIGH));
  Adder #(.width(32)) adder_1 (.a(Input_high), .b(Input_high_2), .out(adder_1_out), .cin(adder_3_cout), .cout(CARRY));
  Subtractor #(.width(32)) subtractor_1 (
    .a(Input_high), .b(Input_high_2), .out(subtractor_1_out), .bin(subtractor_3_bout), .bout(CARRY));
  assign and_1_out = Input_high & Input_high_2;  // AND_Gate and_1, 32 bits wide
  assign or_1_out = Input_high | Input_high_2;  // OR_Gate or_1, 32 bits wide
  assign xor_1_out = Input_high ^ Input_high_2;  // XOR_Gate xor_1, 32 bits wide
  Shift_Left shift_left_1 (
    .High(Input_high), .Corrimiento(Input_low_2), .Low(Input_low_2), .Salida_high(shift_left_1_salida_high),
    .Salida_low(shift_left_1_salida_low));
  Shift_right shift_right_1 (
    .High(Input_high), .Corrimiento(Input_low_2), .Low(Input_low), .Salida_high(shift_right_1_salida_high),
    .Salida_Low(shift_right_1_salida_low));
  asrv asrv_1 (
    .r1h(Input_high), .rl1(Input_low_2), .rl2(Input_low_2), .r2h(Input_high_2), .HIGHP(asrv_1_highp),
    .LowP(asrv_1_lowp), .out_7(asrv_1_out_7));
  rorv rorv_1 (
    .r1h(Input_high), .rl1(Input_low), .rl2(Input_low_2), .HIGHP(rorv_1_highp), .out_5(asrv_1_lowp),
    .out_6(asrv_1_lowp), .out_7(rorv_1_out_7));
  Adder #(.width(32)) adder_2 (.a(Input_high), .b(IMM_HIGH), .out(adder_2_out), .cin(adder_4_cout));  // open: cout
  Subtractor #(.width(32)) subtractor_2 (
    .a(Input_high), .b(IMM_HIGH), .out(subtractor_2_out), .bin(subtractor_4_bout));  // open: bout
  Adder #(.width(32)) adder_3 (.a(Input_low), .b(Input_low_2), .out(adder_3_out), .cout(adder_3_cout));  // open: cin
  Subtractor #(.width(32)) subtractor_3 (
    .a(Input_low), .b(Input_low_2), .out(subtractor_3_out), .bout(subtractor_3_bout));  // open: bin
  assign and_2_out = Input_low & Input_low_2;  // AND_Gate and_2, 32 bits wide
  assign or_2_out = Input_low | Input_low_2;  // OR_Gate or_2, 32 bits wide
  assign xor_2_out = Input_low ^ Input_low_2;  // XOR_Gate xor_2, 32 bits wide
  Adder #(.width(32)) adder_4 (.a(Input_low), .b(IMM_LOW), .out(adder_4_out), .cout(adder_4_cout));  // open: cin
  Subtractor #(.width(32)) subtractor_4 (
    .a(Input_low), .b(IMM_LOW), .out(subtractor_4_out), .bout(subtractor_4_bout));  // open: bin
  Bit_Extender #(.in_width(32), .out_width(1)) bit_extender_2 (.in(asrv_1_lowp), .out(CARRY));
  Multiplexer #(.select(4), .width(32)) multiplexer_1 (
    .in0(adder_1_out), .in1(subtractor_1_out), .in2(and_1_out), .in3(or_1_out), .in4(xor_1_out),
    .in5(shift_left_1_salida_high), .in6(shift_right_1_salida_high), .in7(asrv_1_highp), .in8(rorv_1_highp),
    .in9(adder_2_out), .in10(subtractor_2_out), .in11({32{1'b0}}), .in12({32{1'b0}}), .in13({32{1'b0}}),
    .in14({32{1'b0}}), .in15({32{1'b0}}), .out(Output_high), .sel(control), .en(1'b1));
  Multiplexer #(.select(4), .width(32)) multiplexer_2 (
    .in0(adder_3_out), .in1(subtractor_3_out), .in2(and_2_out), .in3(or_2_out), .in4(xor_2_out),
    .in5(shift_left_1_salida_low), .in6(shift_right_1_salida_low), .in7(asrv_1_out_7), .in8(rorv_1_out_7),
    .in9(adder_4_out), .in10(subtractor_4_out), .in11({32{1'b0}}), .in12({32{1'b0}}), .in13({32{1'b0}}),
    .in14({32{1'b0}}), .in15({32{1'b0}}), .out(Output_low), .sel(control), .en(1'b1));

  // Other names for the same wires on the sheet: Input_High_1[31:0] = Input_high; Input_low_1[31:0] = Input_low;
  //   Offset_shift[31:0] = Input_low_2
endmodule

module Memory_Manager_Instrucciones (
  input  [23:0] address,
  input  [31:0] data,
  input  str
);

  ROM #(.addrWidth(24), .dataWidth(32)) rom_1 (.addr(address), .data(data), .sel(str));
endmodule

module Memory_Manager_Datos (
  input  clock,
  input  [23:0] address_high,
  input  [31:0] data_high,
  input  set_high,
  input  clear,
  input  ld_high
);

  RAM #(.addrWidth(24), .dataWidth(32)) ram_1 (
    .addr(address_high), .data(data_high), .sel(set_high), .clk(clock), .ld(ld_high), .clr(clear));

  // Other names for the same wires on the sheet: ckl = clock
endmodule

module Register_File (
  input  _4,
  input  _3,
  input  _2,
  input  _1,
  input  _0,
  input  [31:0] Input_high,
  input  _4_2,
  input  _3_2,
  input  _2_2,
  input  _1_2,
  input  _0_2,
  input  [31:0] Input_low,
  output [31:0] Output_high,
  output [31:0] Output_low
);

  wire and_1_out, and_2_out, and_3_out, and_4_out, and_5_out, and_6_out, and_7_out, and_8_out, and_9_out,
       and_10_out, and_11_out, and_12_out, and_13_out, and_14_out, and_15_out, and_16_out, and_17_out,
       and_18_out, and_19_out, and_20_out, and_21_out, and_22_out, and_23_out, and_24_out, and_25_out,
       and_26_out, and_27_out, and_28_out, and_29_out, and_30_out, and_31_out, and_32_out, and_33_out,
       and_34_out, and_35_out, and_36_out, and_37_out, and_38_out, and_39_out, and_40_out, and_41_out,
       and_42_out, and_43_out, and_44_out, and_45_out, and_46_out, and_47_out, and_48_out, and_49_out,
       and_50_out, and_51_out, and_52_out, and_53_out, and_54_out, and_55_out, and_56_out, and_57_out,
       and_58_out, and_59_out, and_60_out, and_61_out, and_62_out, and_63_out, and_64_out, clock, not_1_out,
       not_2_out, not_3_out, not_4_out, not_5_out, not_6_out, not_7_out, not_8_out, not_9_out, not_10_out,
       not_11_out, not_12_out, not_13_out, not_14_out, not_15_out, not_16_out, not_17_out, not_18_out,
       not_19_out, not_20_out, not_21_out, not_22_out, not_23_out, not_24_out, not_25_out, not_26_out,
       not_27_out, not_28_out, not_29_out, not_30_out, not_31_out, not_32_out, not_33_out, not_34_out,
       not_35_out, not_36_out, not_37_out, not_38_out, not_39_out, not_40_out, not_41_out, not_42_out,
       not_43_out, not_44_out, not_45_out, not_46_out, not_47_out, not_48_out, not_49_out, not_50_out,
       not_51_out, not_52_out, not_53_out, not_54_out, not_55_out, not_56_out, not_57_out, not_58_out,
       not_59_out, not_60_out, not_61_out, not_62_out, not_63_out, not_64_out, not_65_out, not_66_out,
       not_67_out, not_68_out, not_69_out, not_70_out, not_71_out, not_72_out, not_73_out, not_74_out,
       not_75_out, not_76_out, not_77_out, not_78_out, not_79_out, not_80_out, not_81_out, not_82_out,
       not_83_out, not_84_out, not_85_out, not_86_out, not_87_out, not_88_out, not_89_out, not_90_out,
       not_91_out, not_92_out, not_93_out, not_94_out, not_95_out, not_96_out, not_97_out, not_98_out,
       not_99_out, not_100_out, not_101_out, not_102_out, not_103_out, not_104_out, not_105_out, not_106_out,
       not_107_out, not_108_out, not_109_out, not_110_out, not_111_out, not_112_out, not_113_out,
       not_114_out, not_115_out, not_116_out, not_117_out, not_118_out, not_119_out, not_120_out,
       not_121_out, not_122_out, not_123_out, not_124_out, not_125_out, not_126_out, not_127_out,
       not_128_out, not_129_out, not_130_out, not_131_out, not_132_out, not_133_out, not_134_out,
       not_135_out, not_136_out, not_137_out, not_138_out, not_139_out, not_140_out, not_141_out,
       not_142_out, not_143_out, not_144_out, not_145_out, not_146_out, not_147_out, not_148_out,
       not_149_out, not_150_out, not_151_out, not_152_out, not_153_out, not_154_out, not_155_out,
       not_156_out, not_157_out, not_158_out, not_159_out, not_160_out;
  wire [31:0] undriven, undriven_2, undriven_3, undriven_4, undriven_5, undriven_6, undriven_7, undriven_8,
       undriven_9, undriven_10, x0_2_q, x0_q, x1_2_q, x1_q, x3_2_q, x3_q, x4_2_q, x4_3_q, x4_4_q, x4_5_q,
       x4_6_q, x4_q, x6_2_q, x6_q, x7_2_q, x7_q, x8_2_q, x8_q, x9_2_q, x9_3_q, x9_4_q, x9_q, x11_2_q, x11_q,
       x12_2_q, x12_q, x13_2_q, x13_q, x14_2_q, x14_q, x15_2_q, x15_q, x16_2_q, x16_q, x17_2_q, x17_q,
       x18_2_q, x18_q, x19_2_q, x19_q, x20_2_q, x20_q, x21_2_q, x21_3_q, x21_4_q, x21_q, x23_2_q, x23_3_q,
       x23_4_q, x23_q, x25_2_q, x25_q, x26_2_q, x26_q, x27_2_q, x27_q, x28_2_q, x28_q, x29_2_q, x29_q,
       x30_2_q, x30_q, x31_2_q, x31_q;

  not not_1 (not_1_out, _1);
  not not_2 (not_2_out, _2);
  not not_3 (not_3_out, _3);
  not not_4 (not_4_out, _4);
  not not_5 (not_5_out, _0);
  not not_6 (not_6_out, _2);
  not not_7 (not_7_out, _3);
  not not_8 (not_8_out, _4);
  not not_9 (not_9_out, _2);
  not not_10 (not_10_out, _3);
  not not_11 (not_11_out, _4);
  not not_12 (not_12_out, _0);
  not not_13 (not_13_out, _1);
  not not_14 (not_14_out, _3);
  not not_15 (not_15_out, _4);
  not not_16 (not_16_out, _1);
  not not_17 (not_17_out, _3);
  not not_18 (not_18_out, _4);
  not not_19 (not_19_out, _0);
  not not_20 (not_20_out, _3);
  not not_21 (not_21_out, _4);
  not not_22 (not_22_out, _3);
  not not_23 (not_23_out, _4);
  not not_24 (not_24_out, _0);
  not not_25 (not_25_out, _1);
  not not_26 (not_26_out, _2);
  not not_27 (not_27_out, _4);
  not not_28 (not_28_out, _1);
  not not_29 (not_29_out, _2);
  not not_30 (not_30_out, _4);
  not not_31 (not_31_out, _0);
  not not_32 (not_32_out, _2);
  not not_33 (not_33_out, _4);
  not not_34 (not_34_out, _2);
  not not_35 (not_35_out, _4);
  not not_36 (not_36_out, _0);
  not not_37 (not_37_out, _1);
  not not_38 (not_38_out, _4);
  not not_39 (not_39_out, _1);
  not not_40 (not_40_out, _4);
  not not_41 (not_41_out, _0);
  not not_42 (not_42_out, _4);
  not not_43 (not_43_out, _4);
  not not_44 (not_44_out, _0);
  not not_45 (not_45_out, _1);
  not not_46 (not_46_out, _2);
  not not_47 (not_47_out, _3);
  not not_48 (not_48_out, _1);
  not not_49 (not_49_out, _2);
  not not_50 (not_50_out, _3);
  not not_51 (not_51_out, _0);
  not not_52 (not_52_out, _2);
  not not_53 (not_53_out, _3);
  not not_54 (not_54_out, _2);
  not not_55 (not_55_out, _3);
  not not_56 (not_56_out, _0);
  not not_57 (not_57_out, _1);
  not not_58 (not_58_out, _3);
  not not_59 (not_59_out, _1);
  not not_60 (not_60_out, _3);
  not not_61 (not_61_out, _0);
  not not_62 (not_62_out, _3);
  not not_63 (not_63_out, _3);
  not not_64 (not_64_out, _0);
  not not_65 (not_65_out, _1);
  not not_66 (not_66_out, _2);
  not not_67 (not_67_out, _1);
  not not_68 (not_68_out, _2);
  not not_69 (not_69_out, _0);
  not not_70 (not_70_out, _2);
  not not_71 (not_71_out, _2);
  not not_72 (not_72_out, _0);
  not not_73 (not_73_out, _1);
  not not_74 (not_74_out, _1);
  not not_75 (not_75_out, _0);
  not not_76 (not_76_out, _0);
  not not_77 (not_77_out, _1);
  not not_78 (not_78_out, _2);
  not not_79 (not_79_out, _3);
  not not_80 (not_80_out, _4);
  not not_81 (not_81_out, _1_2);
  not not_82 (not_82_out, _2_2);
  not not_83 (not_83_out, _3_2);
  not not_84 (not_84_out, _4_2);
  not not_85 (not_85_out, _0_2);
  not not_86 (not_86_out, _2_2);
  not not_87 (not_87_out, _3_2);
  not not_88 (not_88_out, _4_2);
  not not_89 (not_89_out, _2_2);
  not not_90 (not_90_out, _3_2);
  not not_91 (not_91_out, _4_2);
  not not_92 (not_92_out, _0_2);
  not not_93 (not_93_out, _1_2);
  not not_94 (not_94_out, _3_2);
  not not_95 (not_95_out, _4_2);
  not not_96 (not_96_out, _1_2);
  not not_97 (not_97_out, _3_2);
  not not_98 (not_98_out, _4_2);
  not not_99 (not_99_out, _0_2);
  not not_100 (not_100_out, _3_2);
  not not_101 (not_101_out, _4_2);
  not not_102 (not_102_out, _3_2);
  not not_103 (not_103_out, _4_2);
  not not_104 (not_104_out, _0_2);
  not not_105 (not_105_out, _1_2);
  not not_106 (not_106_out, _2_2);
  not not_107 (not_107_out, _4_2);
  not not_108 (not_108_out, _1_2);
  not not_109 (not_109_out, _2_2);
  not not_110 (not_110_out, _4_2);
  not not_111 (not_111_out, _0_2);
  not not_112 (not_112_out, _2_2);
  not not_113 (not_113_out, _4_2);
  not not_114 (not_114_out, _2_2);
  not not_115 (not_115_out, _4_2);
  not not_116 (not_116_out, _0_2);
  not not_117 (not_117_out, _1_2);
  not not_118 (not_118_out, _4_2);
  not not_119 (not_119_out, _1_2);
  not not_120 (not_120_out, _4_2);
  not not_121 (not_121_out, _0_2);
  not not_122 (not_122_out, _4_2);
  not not_123 (not_123_out, _4_2);
  not not_124 (not_124_out, _0_2);
  not not_125 (not_125_out, _1_2);
  not not_126 (not_126_out, _2_2);
  not not_127 (not_127_out, _3_2);
  not not_128 (not_128_out, _1_2);
  not not_129 (not_129_out, _2_2);
  not not_130 (not_130_out, _3_2);
  not not_131 (not_131_out, _0_2);
  not not_132 (not_132_out, _2_2);
  not not_133 (not_133_out, _3_2);
  not not_134 (not_134_out, _2_2);
  not not_135 (not_135_out, _3_2);
  not not_136 (not_136_out, _0_2);
  not not_137 (not_137_out, _1_2);
  not not_138 (not_138_out, _3_2);
  not not_139 (not_139_out, _1_2);
  not not_140 (not_140_out, _3_2);
  not not_141 (not_141_out, _0_2);
  not not_142 (not_142_out, _3_2);
  not not_143 (not_143_out, _3_2);
  not not_144 (not_144_out, _0_2);
  not not_145 (not_145_out, _1_2);
  not not_146 (not_146_out, _2_2);
  not not_147 (not_147_out, _1_2);
  not not_148 (not_148_out, _2_2);
  not not_149 (not_149_out, _0_2);
  not not_150 (not_150_out, _2_2);
  not not_151 (not_151_out, _2_2);
  not not_152 (not_152_out, _0_2);
  not not_153 (not_153_out, _1_2);
  not not_154 (not_154_out, _1_2);
  not not_155 (not_155_out, _0_2);
  not not_156 (not_156_out, _0_2);
  not not_157 (not_157_out, _1_2);
  not not_158 (not_158_out, _2_2);
  not not_159 (not_159_out, _3_2);
  not not_160 (not_160_out, _4_2);
  and and_1 (and_1_out, _0, not_1_out, not_2_out, not_3_out, not_4_out);
  and and_2 (and_2_out, not_5_out, _1, not_6_out, not_7_out, not_8_out);
  and and_3 (and_3_out, _0, _1, not_9_out, not_10_out, not_11_out);
  and and_4 (and_4_out, not_12_out, not_13_out, _2, not_14_out, not_15_out);
  and and_5 (and_5_out, _0, not_16_out, _2, not_17_out, not_18_out);
  and and_6 (and_6_out, not_19_out, _1, _2, not_20_out, not_21_out);
  and and_7 (and_7_out, _0, _1, _2, not_22_out, not_23_out);
  and and_8 (and_8_out, not_24_out, not_25_out, not_26_out, _3, not_27_out);
  and and_9 (and_9_out, _0, not_28_out, not_29_out, _3, not_30_out);
  and and_10 (and_10_out, not_31_out, _1, not_32_out, _3, not_33_out);
  and and_11 (and_11_out, _0, _1, not_34_out, _3, not_35_out);
  and and_12 (and_12_out, not_36_out, not_37_out, _2, _3, not_38_out);
  and and_13 (and_13_out, _0, not_39_out, _2, _3, not_40_out);
  and and_14 (and_14_out, not_41_out, _1, _2, _3, not_42_out);
  and and_15 (and_15_out, _0, _1, _2, _3, not_43_out);
  and and_16 (and_16_out, not_44_out, not_45_out, not_46_out, not_47_out, _4);
  and and_17 (and_17_out, _0, not_48_out, not_49_out, not_50_out, _4);
  and and_18 (and_18_out, not_51_out, _1, not_52_out, not_53_out, _4);
  and and_19 (and_19_out, _0, _1, not_54_out, not_55_out, _4);
  and and_20 (and_20_out, not_56_out, not_57_out, _2, not_58_out, _4);
  and and_21 (and_21_out, _0, not_59_out, _2, not_60_out, _4);
  and and_22 (and_22_out, not_61_out, _1, _2, not_62_out, _4);
  and and_23 (and_23_out, _0, _1, _2, not_63_out, _4);
  and and_24 (and_24_out, not_64_out, not_65_out, not_66_out, _3, _4);
  and and_25 (and_25_out, _0, not_67_out, not_68_out, _3, _4);
  and and_26 (and_26_out, not_69_out, _1, not_70_out, _3, _4);
  and and_27 (and_27_out, _0, _1, not_71_out, _3, _4);
  and and_28 (and_28_out, not_72_out, not_73_out, _2, _3, _4);
  and and_29 (and_29_out, _0, not_74_out, _2, _3, _4);
  and and_30 (and_30_out, not_75_out, _1, _2, _3, _4);
  and and_31 (and_31_out, _0, _1, _2, _3, _4);
  and and_32 (and_32_out, not_76_out, not_77_out, not_78_out, not_79_out, not_80_out);
  and and_33 (and_33_out, _0_2, not_81_out, not_82_out, not_83_out, not_84_out);
  and and_34 (and_34_out, not_85_out, _1_2, not_86_out, not_87_out, not_88_out);
  and and_35 (and_35_out, _0_2, _1_2, not_89_out, not_90_out, not_91_out);
  and and_36 (and_36_out, not_92_out, not_93_out, _2_2, not_94_out, not_95_out);
  and and_37 (and_37_out, _0_2, not_96_out, _2_2, not_97_out, not_98_out);
  and and_38 (and_38_out, not_99_out, _1_2, _2_2, not_100_out, not_101_out);
  and and_39 (and_39_out, _0_2, _1_2, _2_2, not_102_out, not_103_out);
  and and_40 (and_40_out, not_104_out, not_105_out, not_106_out, _3_2, not_107_out);
  and and_41 (and_41_out, _0_2, not_108_out, not_109_out, _3_2, not_110_out);
  and and_42 (and_42_out, not_111_out, _1_2, not_112_out, _3_2, not_113_out);
  and and_43 (and_43_out, _0_2, _1_2, not_114_out, _3_2, not_115_out);
  and and_44 (and_44_out, not_116_out, not_117_out, _2_2, _3_2, not_118_out);
  and and_45 (and_45_out, _0_2, not_119_out, _2_2, _3_2, not_120_out);
  and and_46 (and_46_out, not_121_out, _1_2, _2_2, _3_2, not_122_out);
  and and_47 (and_47_out, _0_2, _1_2, _2_2, _3_2, not_123_out);
  and and_48 (and_48_out, not_124_out, not_125_out, not_126_out, not_127_out, _4_2);
  and and_49 (and_49_out, _0_2, not_128_out, not_129_out, not_130_out, _4_2);
  and and_50 (and_50_out, not_131_out, _1_2, not_132_out, not_133_out, _4_2);
  and and_51 (and_51_out, _0_2, _1_2, not_134_out, not_135_out, _4_2);
  and and_52 (and_52_out, not_136_out, not_137_out, _2_2, not_138_out, _4_2);
  and and_53 (and_53_out, _0_2, not_139_out, _2_2, not_140_out, _4_2);
  and and_54 (and_54_out, not_141_out, _1_2, _2_2, not_142_out, _4_2);
  and and_55 (and_55_out, _0_2, _1_2, _2_2, not_143_out, _4_2);
  and and_56 (and_56_out, not_144_out, not_145_out, not_146_out, _3_2, _4_2);
  and and_57 (and_57_out, _0_2, not_147_out, not_148_out, _3_2, _4_2);
  and and_58 (and_58_out, not_149_out, _1_2, not_150_out, _3_2, _4_2);
  and and_59 (and_59_out, _0_2, _1_2, not_151_out, _3_2, _4_2);
  and and_60 (and_60_out, not_152_out, not_153_out, _2_2, _3_2, _4_2);
  and and_61 (and_61_out, _0_2, not_154_out, _2_2, _3_2, _4_2);
  and and_62 (and_62_out, not_155_out, _1_2, _2_2, _3_2, _4_2);
  and and_63 (and_63_out, _0_2, _1_2, _2_2, _3_2, _4_2);
  and and_64 (and_64_out, not_156_out, not_157_out, not_158_out, not_159_out, not_160_out);
  Register #(.width(32)) x1 (.D(Input_high), .en(and_1_out), .Q(x1_q), .clk(clock));  // open: clr
  Register #(.width(32)) x4 (.D(Input_high), .en(and_2_out), .Q(x4_q), .clk(clock));  // open: clr
  Register #(.width(32)) x3 (.D(Input_high), .en(and_3_out), .Q(x3_q), .clk(clock));  // open: clr
  Register #(.width(32)) x4_2 (.D(Input_high), .en(and_4_out), .Q(x4_2_q), .clk(clock));  // open: clr
  Register #(.width(32)) x4_3 (.D(Input_high), .en(and_5_out), .Q(x4_3_q), .clk(clock));  // open: clr
  Register #(.width(32)) x6 (.D(Input_high), .en(and_6_out), .Q(x6_q), .clk(clock));  // open: clr
  Register #(.width(32)) x7 (.D(Input_high), .en(and_7_out), .Q(x7_q), .clk(clock));  // open: clr
  Register #(.width(32)) x8 (.D(Input_high), .en(and_8_out), .Q(x8_q), .clk(clock));  // open: clr
  Register #(.width(32)) x9 (.D(Input_high), .en(and_9_out), .Q(x9_q), .clk(clock));  // open: clr
  Register #(.width(32)) x9_2 (.D(Input_high), .en(and_10_out), .Q(x9_2_q), .clk(clock));  // open: clr
  Register #(.width(32)) x11 (.D(Input_high), .en(and_11_out), .Q(x11_q), .clk(clock));  // open: clr
  Register #(.width(32)) x12 (.D(Input_high), .en(and_12_out), .Q(x12_q), .clk(clock));  // open: clr
  Register #(.width(32)) x13 (.D(Input_high), .en(and_13_out), .Q(x13_q), .clk(clock));  // open: clr
  Register #(.width(32)) x14 (.D(Input_high), .en(and_14_out), .Q(x14_q), .clk(clock));  // open: clr
  Register #(.width(32)) x15 (.D(Input_high), .en(and_15_out), .Q(x15_q), .clk(clock));  // open: clr
  Register #(.width(32)) x16 (.D(undriven), .en(and_16_out), .Q(x16_q), .clk(clock));  // open: clr
  Register #(.width(32)) x17 (.D(undriven_2), .en(and_17_out), .Q(x17_q), .clk(clock));  // open: clr
  Register #(.width(32)) x18 (.D(Input_high), .en(and_18_out), .Q(x18_q), .clk(clock));  // open: clr
  Register #(.width(32)) x19 (.D(Input_high), .en(and_19_out), .Q(x19_q), .clk(clock));  // open: clr
  Register #(.width(32)) x20 (.D(Input_high), .en(and_20_out), .Q(x20_q), .clk(clock));  // open: clr
  Register #(.width(32)) x21 (.D(Input_high), .en(and_21_out), .Q(x21_q), .clk(clock));  // open: clr
  Register #(.width(32)) x21_2 (.D(Input_high), .en(and_22_out), .Q(x21_2_q), .clk(clock));  // open: clr
  Register #(.width(32)) x23 (.D(Input_high), .en(and_23_out), .Q(x23_q), .clk(clock));  // open: clr
  Register #(.width(32)) x23_2 (.D(Input_high), .en(and_24_out), .Q(x23_2_q), .clk(clock));  // open: clr
  Register #(.width(32)) x25 (.D(Input_high), .en(and_25_out), .Q(x25_q), .clk(clock));  // open: clr
  Register #(.width(32)) x26 (.D(Input_high), .en(and_26_out), .Q(x26_q), .clk(clock));  // open: clr
  Register #(.width(32)) x27 (.D(Input_high), .en(and_27_out), .Q(x27_q), .clk(clock));  // open: clr
  Register #(.width(32)) x28 (.D(Input_high), .en(and_28_out), .Q(x28_q), .clk(clock));  // open: clr
  Register #(.width(32)) x29 (.D(Input_high), .en(and_29_out), .Q(x29_q), .clk(clock));  // open: clr
  Register #(.width(32)) x30 (.D(Input_high), .en(and_30_out), .Q(x30_q), .clk(clock));  // open: clr
  Register #(.width(32)) x31 (.D(Input_high), .en(and_31_out), .Q(x31_q), .clk(clock));  // open: clr
  Register #(.width(32)) x0 (.D(Input_high), .en(and_32_out), .Q(x0_q), .clk(clock));  // open: clr
  Register #(.width(32)) x1_2 (.D(Input_low), .en(and_33_out), .Q(x1_2_q), .clk(clock));  // open: clr
  Register #(.width(32)) x4_4 (.D(Input_low), .en(and_34_out), .Q(x4_4_q), .clk(clock));  // open: clr
  Register #(.width(32)) x3_2 (.D(Input_low), .en(and_35_out), .Q(x3_2_q), .clk(clock));  // open: clr
  Register #(.width(32)) x4_5 (.D(Input_low), .en(and_36_out), .Q(x4_5_q), .clk(clock));  // open: clr
  Register #(.width(32)) x4_6 (.D(Input_low), .en(and_37_out), .Q(x4_6_q), .clk(clock));  // open: clr
  Register #(.width(32)) x6_2 (.D(Input_low), .en(and_38_out), .Q(x6_2_q), .clk(clock));  // open: clr
  Register #(.width(32)) x7_2 (.D(Input_low), .en(and_39_out), .Q(x7_2_q), .clk(clock));  // open: clr
  Register #(.width(32)) x8_2 (.D(Input_low), .en(and_40_out), .Q(x8_2_q), .clk(clock));  // open: clr
  Register #(.width(32)) x9_3 (.D(Input_low), .en(and_41_out), .Q(x9_3_q), .clk(clock));  // open: clr
  Register #(.width(32)) x9_4 (.D(Input_low), .en(and_42_out), .Q(x9_4_q), .clk(clock));  // open: clr
  Register #(.width(32)) x11_2 (.D(Input_low), .en(and_43_out), .Q(x11_2_q), .clk(clock));  // open: clr
  Register #(.width(32)) x12_2 (.D(Input_low), .en(and_44_out), .Q(x12_2_q), .clk(clock));  // open: clr
  Register #(.width(32)) x13_2 (.D(Input_low), .en(and_45_out), .Q(x13_2_q), .clk(clock));  // open: clr
  Register #(.width(32)) x14_2 (.D(Input_low), .en(and_46_out), .Q(x14_2_q), .clk(clock));  // open: clr
  Register #(.width(32)) x15_2 (.D(Input_low), .en(and_47_out), .Q(x15_2_q), .clk(clock));  // open: clr
  Register #(.width(32)) x16_2 (.D(undriven_4), .en(and_48_out), .Q(x16_2_q), .clk(clock));  // open: clr
  Register #(.width(32)) x17_2 (.D(undriven_3), .en(and_49_out), .Q(x17_2_q), .clk(clock));  // open: clr
  Register #(.width(32)) x18_2 (.D(Input_low), .en(and_50_out), .Q(x18_2_q), .clk(clock));  // open: clr
  Register #(.width(32)) x19_2 (.D(Input_low), .en(and_51_out), .Q(x19_2_q), .clk(clock));  // open: clr
  Register #(.width(32)) x20_2 (.D(Input_low), .en(and_52_out), .Q(x20_2_q), .clk(clock));  // open: clr
  Register #(.width(32)) x21_3 (.D(Input_low), .en(and_53_out), .Q(x21_3_q), .clk(clock));  // open: clr
  Register #(.width(32)) x21_4 (.D(Input_low), .en(and_54_out), .Q(x21_4_q), .clk(clock));  // open: clr
  Register #(.width(32)) x23_3 (.D(Input_low), .en(and_55_out), .Q(x23_3_q), .clk(clock));  // open: clr
  Register #(.width(32)) x23_4 (.D(Input_low), .en(and_56_out), .Q(x23_4_q), .clk(clock));  // open: clr
  Register #(.width(32)) x25_2 (.D(Input_low), .en(and_57_out), .Q(x25_2_q), .clk(clock));  // open: clr
  Register #(.width(32)) x26_2 (.D(Input_low), .en(and_58_out), .Q(x26_2_q), .clk(clock));  // open: clr
  Register #(.width(32)) x27_2 (.D(Input_low), .en(and_59_out), .Q(x27_2_q), .clk(clock));  // open: clr
  Register #(.width(32)) x28_2 (.D(Input_low), .en(and_60_out), .Q(x28_2_q), .clk(clock));  // open: clr
  Register #(.width(32)) x29_2 (.D(Input_low), .en(and_61_out), .Q(x29_2_q), .clk(clock));  // open: clr
  Register #(.width(32)) x30_2 (.D(Input_low), .en(and_62_out), .Q(x30_2_q), .clk(clock));  // open: clr
  Register #(.width(32)) x31_2 (.D(Input_low), .en(and_63_out), .Q(x31_2_q), .clk(clock));  // open: clr
  Register #(.width(32)) x0_2 (.D(Input_low), .en(and_64_out), .Q(x0_2_q), .clk(clock));  // open: clr
  Multiplexer #(.select(5), .width(32)) multiplexer_1 (
    .in0(x0_q), .in1(x1_q), .in2(undriven_7), .in3(undriven_8), .in4(x4_2_q), .in5(x4_3_q), .in6(x6_q),
    .in7(undriven_5), .in8(x8_q), .in9(x9_q), .in10(x9_2_q), .in11(x11_q), .in12(x12_q), .in13(x13_q),
    .in14(x14_q), .in15(x15_q), .in16(x16_q), .in17(x17_q), .in18(x18_q), .in19(x19_q), .in20(x20_q),
    .in21(x21_q), .in22(x21_2_q), .in23(x23_q), .in24(x23_2_q), .in25(x25_q), .in26(x26_q), .in27(x27_q),
    .in28(x28_q), .in29(x29_q), .in30(x30_q), .in31(x31_q), .out(Output_high), .sel({_4, _3, _2, _1, _0}));  // open: en
  Multiplexer #(.select(5), .width(32)) multiplexer_2 (
    .in0(x0_2_q), .in1(x1_2_q), .in2(undriven_9), .in3(undriven_10), .in4(x4_5_q), .in5(x4_6_q),
    .in6(x6_2_q), .in7(undriven_6), .in8(x8_2_q), .in9(x9_3_q), .in10(x9_4_q), .in11(x11_2_q),
    .in12(x12_2_q), .in13(x13_2_q), .in14(x14_2_q), .in15(x15_2_q), .in16(x16_2_q), .in17(x17_2_q),
    .in18(x18_2_q), .in19(x19_2_q), .in20(x20_2_q), .in21(x21_3_q), .in22(x21_4_q), .in23(x23_3_q),
    .in24(x23_4_q), .in25(x25_2_q), .in26(x26_2_q), .in27(x27_2_q), .in28(x28_2_q), .in29(x29_2_q),
    .in30(x30_2_q), .in31(x31_2_q), .out(Output_low), .sel({_4_2, _3_2, _2_2, _1_2, _0_2}));  // open: en
  Clock u_Clock (.out(clock));
endmodule

module Program_Counter (
  input  [31:0] Inmediato,
  input  offset_mux,
  input  clock,
  input  clear,
  output [31:0] OUTPUT
);

  wire [31:0] adder_1_out, adder_2_out, multiplexer_1_out;

  Adder #(.width(32)) adder_1 (.a(OUTPUT), .b(32'h1), .out(adder_1_out));  // open: cin, cout
  Adder #(.width(32)) adder_2 (.a(Inmediato), .b(OUTPUT), .out(adder_2_out));  // open: cin, cout
  Multiplexer #(.width(32), .enable("false")) multiplexer_1 (
    .in0(adder_1_out), .in1(adder_2_out), .out(multiplexer_1_out), .sel(offset_mux));
  Register #(.width(32)) PC (.D(multiplexer_1_out), .Q(OUTPUT), .clk(clock), .clr(clear));  // open: en
endmodule

// Decoder p1
module Decoder (
  input  [31:0] instruction,
  output Tipo_B,
  output Load_Store,
  output Tipo_R,
  output Tipo_I
);

  wire B__BL_out, B_cond_out, CBZ_out, I_Add__etc_out, not_1_out, not_2_out, not_3_out, not_4_out, not_5_out,
       not_6_out, not_7_out, not_8_out, not_9_out, not_10_out, not_11_out, not_12_out, not_13_out,
       not_14_out, not_15_out, not_16_out, not_17_out, not_18_out, not_19_out, not_20_out, not_21_out,
       not_22_out, not_23_out, not_24_out, not_25_out, not_26_out, not_27_out, not_28_out, not_29_out,
       not_30_out, R_add__etc_out, R_and__etc_out, R_load_out, R_mov_out, R_shifts_out, R_STR_out;

  not not_1 (not_1_out, instruction[27]);
  not not_2 (not_2_out, instruction[25]);
  not not_3 (not_3_out, instruction[26]);
  and I_Add__etc (I_Add__etc_out, instruction[28], not_1_out, not_3_out, not_2_out, instruction[24]);
  or or_1 (Tipo_I, I_Add__etc_out, CBZ_out);
  not not_4 (not_4_out, instruction[28]);
  not not_5 (not_5_out, instruction[26]);
  and R_add__etc (R_add__etc_out, not_4_out, instruction[27], not_5_out, instruction[25], instruction[24]);
  not not_6 (not_6_out, instruction[26]);
  not not_7 (not_7_out, instruction[24]);
  not not_8 (not_8_out, instruction[28]);
  and R_and__etc (R_and__etc_out, not_8_out, instruction[27], not_6_out, instruction[25], not_7_out);
  or or_2 (Tipo_R, R_add__etc_out, R_and__etc_out, R_shifts_out, R_mov_out);
  not not_9 (not_9_out, instruction[26]);
  and R_shifts (R_shifts_out, instruction[28], instruction[27], not_9_out, instruction[25], not_10_out);
  not not_10 (not_10_out, instruction[24]);
  not not_11 (not_11_out, instruction[24]);
  not not_12 (not_12_out, instruction[26]);
  not not_13 (not_13_out, instruction[27]);
  and R_mov (R_mov_out, instruction[28], not_13_out, not_12_out, instruction[25], not_11_out);
  not not_14 (not_14_out, instruction[22]);
  not not_15 (not_15_out, instruction[26]);
  not not_16 (not_16_out, instruction[23]);
  not not_17 (not_17_out, instruction[25]);
  and R_STR (R_STR_out, instruction[31], instruction[30], instruction[29], instruction[28], instruction[27], not_15_out, not_17_out, instruction[24], not_16_out, not_14_out);
  or or_3 (Load_Store, R_STR_out, R_load_out);
  not not_18 (not_18_out, instruction[30]);
  not not_19 (not_19_out, instruction[25]);
  not not_20 (not_20_out, instruction[31]);
  not not_21 (not_21_out, instruction[27]);
  and CBZ (CBZ_out, not_18_out, instruction[29], instruction[28], not_21_out, instruction[26], not_19_out);
  not not_22 (not_22_out, instruction[27]);
  not not_23 (not_23_out, instruction[25]);
  not not_24 (not_24_out, instruction[29]);
  and B_cond (B_cond_out, not_20_out, instruction[30], not_24_out, instruction[28], not_22_out, instruction[26], not_23_out);
  or or_4 (Tipo_B, B_cond_out, B__BL_out);
  not not_25 (not_25_out, instruction[27]);
  not not_26 (not_26_out, instruction[30]);
  not not_27 (not_27_out, instruction[29]);
  and B__BL (B__BL_out, not_26_out, not_27_out, instruction[28], not_25_out, instruction[26]);
  not not_28 (not_28_out, instruction[26]);
  and R_load (R_load_out, instruction[31], instruction[30], instruction[29], instruction[28], instruction[27], not_28_out, not_30_out, instruction[24], not_29_out, instruction[22]);
  not not_29 (not_29_out, instruction[23]);
  not not_30 (not_30_out, instruction[25]);
endmodule

module Jump_Controller (
  input  [3:0] ijc,
  output ojc
);

  wire not_1_out, not_2_out;

  and and_1 (ojc, ijc[3], ijc[2], not_1_out, not_2_out);
  not not_1 (not_1_out, ijc[1]);
  not not_2 (not_2_out, ijc[0]);
endmodule

module Shift_Left (
  input  [31:0] High,
  input  [31:0] Corrimiento,
  input  [31:0] Low,
  output [31:0] Salida_high,
  output [31:0] Salida_low
);

  wire [4:0] bit_extender_1_out, subtractor_1_out;
  wire [31:0] or_1_out, shifter_1_out, shifter_2_out;

  Bit_Extender #(.in_width(32), .out_width(5)) bit_extender_1 (.in(Corrimiento), .out(bit_extender_1_out));
  Subtractor #(.width(5)) subtractor_1 (
    .a({5{1'b1}}), .b(bit_extender_1_out), .out(subtractor_1_out));  // open: bin, bout
  Shifter #(.width(32)) shifter_1 (.in(High), .\dist (bit_extender_1_out), .out(shifter_1_out));
  assign or_1_out = Low | {32{1'b0}};  // OR_Gate or_1, 32 bits wide
  Shifter #(.width(32), .shift("lr")) shifter_2 (.in(or_1_out), .\dist (subtractor_1_out), .out(shifter_2_out));
  assign Salida_high = shifter_1_out | shifter_2_out;  // OR_Gate or_2, 32 bits wide
  Shifter #(.width(32)) shifter_3 (.in(Low), .\dist (bit_extender_1_out), .out(Salida_low));
endmodule

module Shift_right (
  input  [31:0] High,
  input  [31:0] Corrimiento,
  input  [31:0] Low,
  output [31:0] Salida_high,
  output [31:0] Salida_Low
);

  wire [4:0] bit_extender_1_out, subtractor_1_out;
  wire [31:0] or_1_out, shifter_1_out, shifter_3_out;

  Bit_Extender #(.in_width(32), .out_width(5)) bit_extender_1 (.in(Corrimiento), .out(bit_extender_1_out));
  Subtractor #(.width(5)) subtractor_1 (
    .a({5{1'b1}}), .b(bit_extender_1_out), .out(subtractor_1_out));  // open: bin, bout
  assign or_1_out = High | {32{1'b0}};  // OR_Gate or_1, 32 bits wide
  Shifter #(.width(32), .shift("lr")) shifter_1 (.in(Low), .\dist (bit_extender_1_out), .out(shifter_1_out));
  Shifter #(.width(32), .shift("lr")) shifter_2 (.in(High), .\dist (bit_extender_1_out), .out(Salida_high));
  Shifter #(.width(32)) shifter_3 (.in(or_1_out), .\dist (subtractor_1_out), .out(shifter_3_out));
  assign Salida_Low = shifter_3_out | shifter_1_out;  // OR_Gate or_2, 32 bits wide
endmodule

module Prueba_registro (
  input  [3:0] in_1,
  input  in_2,
  input  in_3,
  input  [1:0] in_4,
  input  in_5,
  output [3:0] out_6,
  output [1:0] out_7,
  output [1:0] out_8
);

  wire not_1_out, undriven;

  assign out_7 = in_2 ? in_4 : 2'bz;  // Controlled_Buffer controlled_buffer_1
  not not_1 (not_1_out, in_5);
  assign out_8 = in_5 ? 2'b11 : 2'bz;  // Controlled_Buffer controlled_buffer_2
  assign out_8 = not_1_out ? 2'b01 : 2'bz;  // Controlled_Buffer controlled_buffer_3
  Register #(.width(4)) register_1 (.D(in_1), .Q(out_6), .clk(in_3));  // open: en, clr
  Banderas banderas_1 (.on(undriven));  // open: input_z, input_n, input_c, input_v, clock, output_z, output_n, output_c, output_v
  Comparator comparator_1 ();  // open: a, b, gt, eq, lt
  Comparator comparator_2 ();  // open: a, b, gt, eq, lt
  Comparator comparator_3 ();  // open: a, b, gt, eq, lt
  Comparator comparator_4 ();  // open: a, b, gt, eq, lt
endmodule

module Decoder_R (
  input  [31:0] instruction,
  output [4:0] RN,
  output [4:0] RM,
  output [4:0] RD,
  output ADD_R,
  output ADDS_R,
  output SUB_R,
  output SUBS_R,
  output AND_R,
  output ORR_R,
  output EOR_R,
  output ANDS_R,
  output LSLV_R,
  output LSRV_R,
  output ASRV_R,
  output RORV_R
);

  wire and_4_p11, and_4_p12, and_4_p13, not_1_out, not_2_out, not_3_out, not_4_out, not_5_out, not_6_out,
       not_7_out, not_8_out, not_9_out, not_10_out, not_11_out, not_12_out, not_13_out, not_14_out,
       not_15_out, not_16_out, not_17_out, not_18_out, not_19_out, not_20_out, not_21_out, not_24_out,
       not_26_out, not_27_out, not_28_out, not_29_out, not_30_out, not_31_out, not_32_out, not_33_out,
       not_34_out, not_35_out, not_36_out, not_37_out, not_38_out, not_39_out, not_40_out, not_41_out,
       not_42_out, not_43_out, not_44_out, not_45_out, not_46_out, not_47_out, not_48_out, not_49_out,
       not_50_out, not_51_out, not_52_out, not_53_out, not_54_out, not_55_out, not_56_out, not_57_out,
       not_58_out, not_59_out, not_60_out, not_61_out, not_62_out, not_63_out, not_64_out, not_65_out,
       not_66_out, not_67_out, not_68_out, not_69_out, not_70_out, not_71_out, not_72_out, not_73_out,
       not_74_out, not_75_out, not_76_out, not_77_out, not_78_out, not_79_out, not_80_out, not_81_out,
       not_82_out, not_83_out, not_84_out, not_85_out, not_86_out, not_87_out, not_88_out;

  not not_1 (not_1_out, instruction[30]);
  not not_2 (not_2_out, instruction[29]);
  not not_3 (not_3_out, instruction[28]);
  not not_4 (not_4_out, instruction[22]);
  not not_5 (not_5_out, instruction[21]);
  not not_6 (not_6_out, instruction[23]);
  not not_7 (not_7_out, instruction[26]);
  and and_1 (ADD_R, instruction[31], not_1_out, not_2_out, not_3_out, instruction[27], not_7_out, instruction[25], instruction[24], not_6_out, not_4_out, not_5_out);
  not not_8 (not_8_out, instruction[30]);
  not not_9 (not_9_out, instruction[26]);
  not not_10 (not_10_out, instruction[28]);
  and and_2 (ADDS_R, instruction[31], not_8_out, instruction[29], not_10_out, instruction[27], not_9_out, instruction[25], instruction[24], not_13_out, not_11_out, not_14_out);
  not not_11 (not_11_out, instruction[22]);
  not not_12 (not_12_out, instruction[29]);
  not not_13 (not_13_out, instruction[23]);
  not not_14 (not_14_out, instruction[21]);
  not not_15 (not_15_out, instruction[26]);
  not not_16 (not_16_out, instruction[22]);
  not not_17 (not_17_out, instruction[28]);
  not not_18 (not_18_out, instruction[21]);
  not not_19 (not_19_out, instruction[23]);
  and and_3 (SUB_R, instruction[31], instruction[30], not_12_out, not_17_out, instruction[27], not_15_out, instruction[25], instruction[24], not_19_out, not_16_out, not_18_out);
  not not_20 (not_20_out, instruction[26]);
  not not_21 (not_21_out, instruction[28]);
  // AND_Gate and_4: pin names not known; wires that end beside it: instruction[31], instruction[30], instruction[29], not_21_out, instruction[27], not_20_out, SUBS_R, SUBS_R, instruction[25], instruction[24], and_4_p11, and_4_p12, and_4_p13
  not not_22 (and_4_p13, instruction[21]);
  not not_23 (and_4_p11, instruction[23]);
  not not_24 (not_24_out, instruction[29]);
  not not_25 (and_4_p12, instruction[22]);
  not not_26 (not_26_out, instruction[30]);
  not not_27 (not_27_out, instruction[26]);
  not not_28 (not_28_out, instruction[24]);
  not not_29 (not_29_out, instruction[21]);
  not not_30 (not_30_out, instruction[28]);
  not not_31 (not_31_out, instruction[23]);
  not not_32 (not_32_out, instruction[22]);
  and and_5 (AND_R, instruction[31], not_26_out, not_24_out, not_30_out, instruction[27], not_27_out, instruction[25], not_28_out, not_31_out, not_32_out, not_29_out);
  not not_33 (not_33_out, instruction[28]);
  not not_34 (not_34_out, instruction[30]);
  not not_35 (not_35_out, instruction[26]);
  and and_6 (ORR_R, instruction[31], not_34_out, instruction[29], not_33_out, instruction[27], not_35_out, instruction[25], not_39_out, not_36_out, not_38_out, not_40_out);
  not not_36 (not_36_out, instruction[23]);
  not not_37 (not_37_out, instruction[29]);
  not not_38 (not_38_out, instruction[22]);
  not not_39 (not_39_out, instruction[24]);
  not not_40 (not_40_out, instruction[21]);
  not not_41 (not_41_out, instruction[28]);
  not not_42 (not_42_out, instruction[22]);
  not not_43 (not_43_out, instruction[23]);
  not not_44 (not_44_out, instruction[24]);
  not not_45 (not_45_out, instruction[26]);
  not not_46 (not_46_out, instruction[21]);
  and and_7 (EOR_R, instruction[31], instruction[30], not_37_out, not_41_out, instruction[27], not_45_out, instruction[25], not_44_out, not_43_out, not_42_out, not_46_out);
  not not_47 (not_47_out, instruction[28]);
  not not_48 (not_48_out, instruction[26]);
  and and_8 (ANDS_R, instruction[31], instruction[30], instruction[29], not_47_out, instruction[27], not_48_out, instruction[25], not_52_out, not_49_out, not_53_out, not_54_out);
  not not_49 (not_49_out, instruction[23]);
  not not_50 (not_50_out, instruction[30]);
  not not_51 (not_51_out, instruction[29]);
  not not_52 (not_52_out, instruction[24]);
  not not_53 (not_53_out, instruction[22]);
  not not_54 (not_54_out, instruction[21]);
  not not_55 (not_55_out, instruction[21]);
  not not_56 (not_56_out, instruction[26]);
  not not_57 (not_57_out, instruction[24]);
  and and_9 (LSLV_R, instruction[31], not_50_out, not_51_out, instruction[28], instruction[27], not_56_out, instruction[25], not_57_out, instruction[23], instruction[22], not_55_out, not_62_out, not_58_out, instruction[13], not_59_out, not_61_out, not_60_out);
  not not_58 (not_58_out, instruction[14]);
  not not_59 (not_59_out, instruction[12]);
  not not_60 (not_60_out, instruction[10]);
  not not_61 (not_61_out, instruction[11]);
  not not_62 (not_62_out, instruction[15]);
  not not_63 (not_63_out, instruction[26]);
  not not_64 (not_64_out, instruction[30]);
  not not_65 (not_65_out, instruction[24]);
  not not_66 (not_66_out, instruction[29]);
  and and_10 (LSRV_R, instruction[31], not_64_out, not_66_out, instruction[28], instruction[27], not_63_out, instruction[25], not_65_out, instruction[23], instruction[22], not_68_out, not_67_out, not_70_out, instruction[13], not_69_out, not_71_out, instruction[10]);
  not not_67 (not_67_out, instruction[15]);
  not not_68 (not_68_out, instruction[21]);
  not not_69 (not_69_out, instruction[12]);
  not not_70 (not_70_out, instruction[14]);
  not not_71 (not_71_out, instruction[11]);
  not not_72 (not_72_out, instruction[30]);
  not not_73 (not_73_out, instruction[29]);
  not not_74 (not_74_out, instruction[26]);
  not not_75 (not_75_out, instruction[15]);
  not not_76 (not_76_out, instruction[21]);
  not not_77 (not_77_out, instruction[24]);
  not not_78 (not_78_out, instruction[12]);
  not not_79 (not_79_out, instruction[14]);
  and and_11 (ASRV_R, instruction[31], not_72_out, not_73_out, instruction[28], instruction[27], not_74_out, instruction[25], not_77_out, instruction[23], instruction[22], not_76_out, not_75_out, not_79_out, instruction[13], not_78_out, instruction[11], not_80_out);
  not not_80 (not_80_out, instruction[10]);
  not not_81 (not_81_out, instruction[29]);
  not not_82 (not_82_out, instruction[30]);
  not not_83 (not_83_out, instruction[24]);
  not not_84 (not_84_out, instruction[26]);
  not not_85 (not_85_out, instruction[14]);
  not not_86 (not_86_out, instruction[15]);
  not not_87 (not_87_out, instruction[21]);
  and and_12 (RORV_R, instruction[31], not_82_out, not_81_out, instruction[28], instruction[27], not_84_out, instruction[25], not_83_out, instruction[23], instruction[22], not_87_out, not_86_out, not_85_out, instruction[13], not_88_out, instruction[11], instruction[10]);
  not not_88 (not_88_out, instruction[12]);

  assign RD = instruction[4:0];
  assign RM = instruction[20:16];
  assign RN = instruction[9:5];
endmodule

module Decoder_I (
  input  [31:0] instruction,
  output [11:0] IMM,
  output [4:0] RN,
  output [4:0] RD,
  output ADD_I,
  output ADDS_I,
  output SUB_I,
  output SUBS_I,
  output MOVN_I,
  output MOV_I,
  output MOVK_I
);

  wire not_1_out, not_2_out, not_3_out, not_4_out, not_5_out, not_6_out, not_7_out, not_8_out, not_9_out,
       not_10_out, not_11_out, not_12_out, not_13_out, not_14_out, not_15_out, not_16_out, not_17_out,
       not_18_out, not_19_out, not_20_out, not_21_out, not_22_out, not_23_out, not_24_out, not_25_out,
       not_26_out, not_27_out, not_28_out, not_29_out, not_30_out, not_32_out, not_33_out, not_34_out,
       not_35_out, not_36_out, not_38_out, not_39_out, not_40_out, not_41_out;

  not not_1 (not_1_out, instruction[27]);
  not not_2 (not_2_out, instruction[29]);
  not not_3 (not_3_out, instruction[30]);
  not not_4 (not_4_out, instruction[25]);
  not not_5 (not_5_out, instruction[23]);
  not not_6 (not_6_out, instruction[22]);
  not not_7 (not_7_out, instruction[26]);
  and and_1 (ADD_I, instruction[31], not_3_out, not_2_out, instruction[28], not_1_out, not_7_out, not_4_out, instruction[24], not_5_out, not_6_out);
  not not_8 (not_8_out, instruction[25]);
  not not_9 (not_9_out, instruction[30]);
  not not_10 (not_10_out, instruction[27]);
  not not_11 (not_11_out, instruction[26]);
  and and_2 (ADDS_I, instruction[31], not_9_out, instruction[29], instruction[28], not_10_out, not_11_out, not_8_out, instruction[24], not_14_out, not_12_out);
  not not_12 (not_12_out, instruction[22]);
  not not_13 (not_13_out, instruction[27]);
  not not_14 (not_14_out, instruction[23]);
  not not_15 (not_15_out, instruction[29]);
  not not_16 (not_16_out, instruction[25]);
  not not_17 (not_17_out, instruction[22]);
  not not_18 (not_18_out, instruction[26]);
  not not_19 (not_19_out, instruction[23]);
  and and_3 (SUB_I, instruction[31], instruction[30], not_15_out, instruction[28], not_13_out, not_18_out, not_16_out, instruction[24], not_19_out, not_17_out);
  not not_20 (not_20_out, instruction[26]);
  not not_21 (not_21_out, instruction[25]);
  not not_22 (not_22_out, instruction[27]);
  and and_4 (SUBS_I, instruction[31], instruction[30], instruction[29], instruction[28], not_22_out, not_20_out, not_21_out, instruction[24], not_25_out, not_26_out);
  not not_23 (not_23_out, instruction[29]);
  not not_24 (not_24_out, instruction[27]);
  not not_25 (not_25_out, instruction[23]);
  not not_26 (not_26_out, instruction[22]);
  not not_27 (not_27_out, instruction[30]);
  not not_28 (not_28_out, instruction[26]);
  not not_29 (not_29_out, instruction[22]);
  not not_30 (not_30_out, instruction[24]);
  // NOT_Gate not_31 has open pins: in=instruction[21], out=open
  and and_5 (MOVN_I, instruction[31], not_27_out, not_23_out, instruction[28], not_24_out, not_28_out, instruction[25], not_30_out, instruction[23], not_29_out);
  not not_32 (not_32_out, instruction[24]);
  not not_33 (not_33_out, instruction[27]);
  not not_34 (not_34_out, instruction[26]);
  not not_35 (not_35_out, instruction[29]);
  and and_6 (MOV_I, instruction[31], instruction[30], not_35_out, instruction[28], not_33_out, not_34_out, instruction[25], not_32_out, instruction[23], not_36_out);
  not not_36 (not_36_out, instruction[22]);
  // NOT_Gate not_37 has open pins: in=instruction[21], out=open
  not not_38 (not_38_out, instruction[27]);
  not not_39 (not_39_out, instruction[22]);
  not not_40 (not_40_out, instruction[24]);
  not not_41 (not_41_out, instruction[26]);
  // NOT_Gate not_42 has open pins: in=instruction[21], out=open
  and and_7 (MOVK_I, instruction[31], instruction[30], instruction[29], instruction[28], not_38_out, not_41_out, instruction[25], not_40_out, instruction[23], not_39_out);

  assign IMM = instruction[21:10];
  assign RD = instruction[4:0];
  assign RN = instruction[9:5];
endmodule

module Registros_orden (
  input  [4:0] xd,
  input  [4:0] xm,
  input  [4:0] xn,
  input  [31:0] Input_h,
  input  [31:0] Input_l,
  input  clock,
  output [31:0] output_xn_low,
  output [31:0] output_xn_high,
  output [31:0] output_xm_low,
  output [31:0] output_xm_high
);

  wire not_1_out, not_2_out, not_3_out, not_4_out, not_5_out, not_6_out, not_7_out, not_8_out, not_9_out,
       not_10_out, not_11_out, not_12_out, not_13_out, not_14_out, not_15_out, not_16_out, not_17_out,
       not_18_out, not_19_out, not_20_out, not_21_out, not_22_out, not_23_out, not_24_out, not_25_out,
       not_26_out, not_27_out, not_28_out, not_29_out, not_30_out, not_31_out, not_32_out, not_33_out,
       not_34_out, not_35_out, not_36_out, not_37_out, not_38_out, not_39_out, not_40_out, not_41_out,
       not_42_out, not_43_out, not_44_out, not_45_out, not_46_out, not_47_out, not_48_out, not_49_out,
       not_50_out, not_51_out, not_52_out, not_53_out, not_54_out, not_55_out, not_56_out, not_57_out,
       not_58_out, not_59_out, not_60_out, not_61_out, not_62_out, not_63_out, not_64_out, not_65_out,
       not_66_out, not_67_out, not_69_out, not_70_out, not_71_out, not_72_out, not_73_out, not_74_out,
       not_75_out, not_76_out, not_77_out, not_78_out, not_79_out, not_80_out, not_81_out, on0, on1, on2,
       on3, on4, on5, on6, on7, on8, on9, on10, on11, on12, on13, on14, on15, on16, on17, on18, on19, on20,
       on21, on22, on23, on24, on25, on26, on27, on28, on29, on30, on31;
  wire [31:0] x0, x0h, x1, x1h, x2, x2h, x3, x3h, x4, x4h, x5, x5h, x6, x6h, x7, x7h, x8, x8h, x9, x9h, x10,
       x10h, x11, x11h, x12, x12h, x13, x13h, x14, x14h, x15, x15h, x16, x16h, x17, x17h, x18, x18h, x19,
       x19h, x20, x20h, x21, x21h, x22, x22h, x23, x23h, x24, x24h, x25, x25h, x26, x26h, x27, x27h, x28,
       x28h, x29, x29h, x30, x30h, x31, x31h;

  not not_1 (not_1_out, xd[1]);
  not not_2 (not_2_out, xd[2]);
  not not_3 (not_3_out, xd[0]);
  and and_1 (on0, not_3_out, not_1_out, not_2_out, not_5_out, not_6_out);
  not not_4 (not_4_out, xd[3]);
  not not_5 (not_5_out, xd[3]);
  not not_6 (not_6_out, xd[4]);
  not not_7 (not_7_out, xd[4]);
  not not_8 (not_8_out, xd[1]);
  not not_9 (not_9_out, xd[2]);
  and and_2 (on1, xd[0], not_8_out, not_9_out, not_4_out, not_7_out);
  Register #(.width(32)) u_x0 (.D(Input_h), .en(on0), .Q(x0h), .clk(clock));  // open: clr
  Register #(.width(32)) u_x1 (.D(Input_h), .en(on1), .Q(x1h), .clk(clock));  // open: clr
  Register #(.width(32)) u_x2 (.D(Input_h), .en(on2), .Q(x2h), .clk(clock));  // open: clr
  Register #(.width(32)) u_x3 (.D(Input_h), .en(on3), .Q(x3h), .clk(clock));  // open: clr
  Register #(.width(32)) u_x4 (.D(Input_h), .en(on4), .Q(x4h), .clk(clock));  // open: clr
  Register #(.width(32)) u_x5 (.D(Input_h), .en(on5), .Q(x5h), .clk(clock));  // open: clr
  Register #(.width(32)) u_x6 (.D(Input_h), .en(on6), .Q(x6h), .clk(clock));  // open: clr
  Register #(.width(32)) u_x7 (.D(Input_h), .en(on7), .Q(x7h), .clk(clock));  // open: clr
  not not_10 (not_10_out, xd[3]);
  not not_11 (not_11_out, xd[4]);
  not not_12 (not_12_out, xd[2]);
  not not_13 (not_13_out, xd[0]);
  and and_3 (on2, not_13_out, xd[1], not_12_out, not_10_out, not_11_out);
  not not_14 (not_14_out, xd[0]);
  not not_15 (not_15_out, xd[2]);
  not not_16 (not_16_out, xd[1]);
  not not_17 (not_17_out, xd[4]);
  not not_18 (not_18_out, xd[3]);
  and and_4 (on4, not_14_out, not_16_out, xd[2], not_19_out, not_21_out);
  and and_5 (on3, xd[0], xd[1], not_15_out, not_18_out, not_17_out);
  Register #(.width(32)) u_x8 (.D(Input_h), .en(on8), .Q(x8h));  // open: clk, clr
  Register #(.width(32)) u_x9 (.D(Input_h), .en(on9), .Q(x9h), .clk(clock));  // open: clr
  Register #(.width(32)) u_x10 (.D(Input_h), .en(on10), .Q(x10h), .clk(clock));  // open: clr
  Register #(.width(32)) u_x11 (.D(Input_h), .en(on11), .Q(x11h), .clk(clock));  // open: clr
  Register #(.width(32)) u_x12 (.D(Input_h), .en(on12), .Q(x12h), .clk(clock));  // open: clr
  Register #(.width(32)) u_x13 (.D(Input_h), .en(on13), .Q(x13h), .clk(clock));  // open: clr
  Register #(.width(32)) u_x14 (.D(Input_h), .en(on14), .Q(x14h), .clk(clock));  // open: clr
  Register #(.width(32)) u_x15 (.D(Input_h), .en(on15), .Q(x15h), .clk(clock));  // open: clr
  not not_19 (not_19_out, xd[3]);
  not not_20 (not_20_out, xd[4]);
  not not_21 (not_21_out, xd[4]);
  not not_22 (not_22_out, xd[3]);
  not not_23 (not_23_out, xd[1]);
  and and_6 (on5, xd[0], not_23_out, xd[2], not_22_out, not_20_out);
  not not_24 (not_24_out, xd[3]);
  not not_25 (not_25_out, xd[4]);
  not not_26 (not_26_out, xd[0]);
  and and_7 (on6, not_26_out, xd[1], xd[2], not_24_out, not_25_out);
  Register #(.width(32)) u_x16 (.D(Input_h), .en(on16), .Q(x16h));  // open: clk, clr
  Register #(.width(32)) u_x17 (.D(Input_h), .en(on17), .Q(x17h), .clk(clock));  // open: clr
  Register #(.width(32)) u_x18 (.D(Input_h), .en(on18), .Q(x18h), .clk(clock));  // open: clr
  Register #(.width(32)) u_x19 (.D(Input_h), .en(on19), .Q(x19h), .clk(clock));  // open: clr
  Register #(.width(32)) u_x20 (.D(Input_h), .en(on20), .Q(x20h), .clk(clock));  // open: clr
  Register #(.width(32)) u_x21 (.D(Input_h), .en(on21), .Q(x21h), .clk(clock));  // open: clr
  Register #(.width(32)) u_x22 (.D(Input_h), .en(on22), .Q(x22h), .clk(clock));  // open: clr
  Register #(.width(32)) u_x23 (.D(Input_h), .en(on23), .Q(x23h), .clk(clock));  // open: clr
  not not_27 (not_27_out, xd[0]);
  not not_28 (not_28_out, xd[4]);
  not not_29 (not_29_out, xd[1]);
  not not_30 (not_30_out, xd[2]);
  not not_31 (not_31_out, xd[3]);
  and and_8 (on8, not_27_out, not_29_out, not_30_out, xd[3], not_32_out);
  and and_9 (on7, xd[0], xd[1], xd[2], not_31_out, not_28_out);
  not not_32 (not_32_out, xd[4]);
  not not_33 (not_33_out, xd[2]);
  not not_34 (not_34_out, xd[4]);
  not not_35 (not_35_out, xd[1]);
  and and_10 (on9, xd[0], not_35_out, not_33_out, xd[3], not_34_out);
  Register #(.width(32)) u_x24 (.D(Input_h), .en(on24), .Q(x24h));  // open: clk, clr
  Register #(.width(32)) u_x25 (.D(Input_h), .en(on25), .Q(x25h), .clk(clock));  // open: clr
  Register #(.width(32)) u_x26 (.D(Input_h), .en(on26), .Q(x26h), .clk(clock));  // open: clr
  Register #(.width(32)) u_x27 (.D(Input_h), .en(on27), .Q(x27h), .clk(clock));  // open: clr
  Register #(.width(32)) u_x28 (.D(Input_h), .en(on28), .Q(x28h), .clk(clock));  // open: clr
  Register #(.width(32)) u_x29 (.D(Input_h), .en(on29), .Q(x29h), .clk(clock));  // open: clr
  Register #(.width(32)) u_x30 (.D(Input_h), .en(on30), .Q(x30h), .clk(clock));  // open: clr
  Register #(.width(32)) u_x31 (.D(Input_h), .en(on31), .Q(x31h), .clk(clock));  // open: clr
  not not_36 (not_36_out, xd[4]);
  not not_37 (not_37_out, xd[2]);
  not not_38 (not_38_out, xd[0]);
  and and_11 (on10, not_38_out, xd[1], not_37_out, xd[3], not_36_out);
  not not_39 (not_39_out, xd[4]);
  not not_40 (not_40_out, xd[1]);
  not not_41 (not_41_out, xd[2]);
  not not_42 (not_42_out, xd[0]);
  and and_12 (on11, xd[0], xd[1], not_41_out, xd[3], not_39_out);
  and and_13 (on12, not_42_out, not_40_out, xd[2], xd[3], not_44_out);
  not not_43 (not_43_out, xd[4]);
  not not_44 (not_44_out, xd[4]);
  not not_45 (not_45_out, xd[1]);
  and and_14 (on13, xd[0], not_45_out, xd[2], xd[3], not_43_out);
  not not_46 (not_46_out, xd[0]);
  not not_47 (not_47_out, xd[4]);
  and and_15 (on14, not_46_out, xd[1], xd[2], xd[3], not_47_out);
  not not_48 (not_48_out, xd[1]);
  not not_49 (not_49_out, xd[2]);
  not not_50 (not_50_out, xd[4]);
  not not_51 (not_51_out, xd[0]);
  and and_16 (on15, xd[0], xd[1], xd[2], xd[3], not_50_out);
  and and_17 (on16, not_51_out, not_48_out, not_49_out, not_53_out, xd[4]);
  Multiplexer #(.select(5), .width(32)) multiplexer_1 (
    .in0(x0h), .in1(x1h), .in2(x2h), .in3(x3h), .in4(x4h), .in5(x5h), .in6(x6h), .in7(x7h), .in8(x8h),
    .in9(x9h), .in10(x10h), .in11(x11h), .in12(x12h), .in13(x13h), .in14(x14h), .in15(x15h), .in16(x16h),
    .in17(x17h), .in18(x18h), .in19(x19h), .in20(x20h), .in21(x21h), .in22(x22h), .in23(x23h), .in24(x24h),
    .in25(x25h), .in26(x26h), .in27(x27h), .in28(x28h), .in29(x29h), .in30(x30h), .in31(x31h),
    .out(output_xn_high), .sel(xn), .en(1'b1));
  Multiplexer #(.select(5), .width(32)) multiplexer_2 (
    .in0(x0h), .in1(x1h), .in2(x2h), .in3(x3h), .in4(x4h), .in5(x5h), .in6(x6h), .in7(x7h), .in8(x8h),
    .in9(x9h), .in10(x10h), .in11(x11h), .in12(x12h), .in13(x13h), .in14(x14h), .in15(x15h), .in16(x16h),
    .in17(x17h), .in18(x18h), .in19(x19h), .in20(x20h), .in21(x21h), .in22(x22h), .in23(x23h), .in24(x24h),
    .in25(x25h), .in26(x26h), .in27(x27h), .in28(x28h), .in29(x29h), .in30(x30h), .in31(x31h),
    .out(output_xm_high), .sel(xm), .en(1'b1));
  not not_52 (not_52_out, xd[1]);
  not not_53 (not_53_out, xd[3]);
  not not_54 (not_54_out, xd[3]);
  not not_55 (not_55_out, xd[2]);
  and and_18 (on17, xd[0], not_52_out, not_55_out, not_54_out, xd[4]);
  not not_56 (not_56_out, xd[3]);
  not not_57 (not_57_out, xd[2]);
  not not_58 (not_58_out, xd[0]);
  and and_19 (on18, not_58_out, xd[1], not_57_out, not_56_out, xd[4]);
  not not_59 (not_59_out, xd[0]);
  not not_60 (not_60_out, xd[2]);
  not not_61 (not_61_out, xd[3]);
  not not_62 (not_62_out, xd[1]);
  and and_20 (on20, not_59_out, not_62_out, xd[2], not_65_out, xd[4]);
  and and_21 (on19, xd[0], xd[1], not_60_out, not_61_out, xd[4]);
  not not_63 (not_63_out, xd[3]);
  not not_64 (not_64_out, xd[1]);
  not not_65 (not_65_out, xd[3]);
  and and_22 (on21, xd[0], not_64_out, xd[2], not_63_out, xd[4]);
  Register #(.width(32)) x0_2 (.D(Input_l), .en(on0), .Q(x0), .clk(clock));  // open: clr
  Register #(.width(32)) x1_2 (.D(Input_l), .en(on1), .Q(x1), .clk(clock));  // open: clr
  Register #(.width(32)) x2_2 (.D(Input_l), .en(on2), .Q(x2), .clk(clock));  // open: clr
  Register #(.width(32)) x3_2 (.D(Input_l), .en(on3), .Q(x3), .clk(clock));  // open: clr
  Register #(.width(32)) x4_2 (.D(Input_l), .en(on4), .Q(x4), .clk(clock));  // open: clr
  Register #(.width(32)) x5_2 (.D(Input_l), .en(on5), .Q(x5), .clk(clock));  // open: clr
  Register #(.width(32)) x6_2 (.D(Input_l), .en(on6), .Q(x6), .clk(clock));  // open: clr
  Register #(.width(32)) x7_2 (.D(Input_l), .en(on7), .Q(x7), .clk(clock));  // open: clr
  not not_66 (not_66_out, xd[0]);
  not not_67 (not_67_out, xd[3]);
  and and_23 (on22, not_66_out, xd[1], xd[2], not_67_out, xd[4]);
  // NOT_Gate not_68 is placed but not wired
  not not_69 (not_69_out, xd[0]);
  not not_70 (not_70_out, xd[1]);
  not not_71 (not_71_out, xd[2]);
  not not_72 (not_72_out, xd[3]);
  and and_24 (on23, xd[0], xd[1], xd[2], not_72_out, xd[4]);
  and and_25 (on24, not_69_out, not_70_out, not_71_out, xd[3], xd[4]);
  Register #(.width(32)) x8_2 (.D(Input_l), .en(on8), .Q(x8), .clk(clock));  // open: clr
  Register #(.width(32)) x9_2 (.D(Input_l), .en(on9), .Q(x9), .clk(clock));  // open: clr
  Register #(.width(32)) x10_2 (.D(Input_l), .en(on10), .Q(x10), .clk(clock));  // open: clr
  Register #(.width(32)) x11_2 (.D(Input_l), .en(on11), .Q(x11), .clk(clock));  // open: clr
  Register #(.width(32)) x12_2 (.D(Input_l), .en(on12), .Q(x12), .clk(clock));  // open: clr
  Register #(.width(32)) x13_2 (.D(Input_l), .en(on13), .Q(x13), .clk(clock));  // open: clr
  Register #(.width(32)) x14_2 (.D(Input_l), .en(on14), .Q(x14), .clk(clock));  // open: clr
  Register #(.width(32)) x15_2 (.D(Input_l), .en(on15), .Q(x15), .clk(clock));  // open: clr
  not not_73 (not_73_out, xd[1]);
  not not_74 (not_74_out, xd[2]);
  and and_26 (on25, xd[0], not_73_out, not_74_out, xd[3], xd[4]);
  not not_75 (not_75_out, xd[2]);
  not not_76 (not_76_out, xd[0]);
  and and_27 (on26, not_76_out, xd[1], not_75_out, xd[3], xd[4]);
  Register #(.width(32)) x16_2 (.D(Input_l), .en(on16), .Q(x16), .clk(clock));  // open: clr
  Register #(.width(32)) x17_2 (.D(Input_l), .en(on17), .Q(x17), .clk(clock));  // open: clr
  Register #(.width(32)) x18_2 (.D(Input_l), .en(on18), .Q(x18), .clk(clock));  // open: clr
  Register #(.width(32)) x19_2 (.D(Input_l), .en(on19), .Q(x19), .clk(clock));  // open: clr
  Register #(.width(32)) x20_2 (.D(Input_l), .en(on20), .Q(x20), .clk(clock));  // open: clr
  Register #(.width(32)) x21_2 (.D(Input_l), .en(on21), .Q(x21), .clk(clock));  // open: clr
  Register #(.width(32)) x22_2 (.D(Input_l), .en(on22), .Q(x22), .clk(clock));  // open: clr
  Register #(.width(32)) x23_2 (.D(Input_l), .en(on23), .Q(x23), .clk(clock));  // open: clr
  not not_77 (not_77_out, xd[2]);
  not not_78 (not_78_out, xd[1]);
  not not_79 (not_79_out, xd[0]);
  and and_28 (on27, xd[0], xd[1], not_77_out, xd[3], xd[4]);
  and and_29 (on28, not_79_out, not_78_out, xd[2], xd[3], xd[4]);
  not not_80 (not_80_out, xd[1]);
  and and_30 (on29, xd[0], not_80_out, xd[2], xd[3], xd[4]);
  Register #(.width(32)) x24_2 (.D(Input_l), .en(on24), .Q(x24), .clk(clock));  // open: clr
  Register #(.width(32)) x25_2 (.D(Input_l), .en(on25), .Q(x25), .clk(clock));  // open: clr
  Register #(.width(32)) x26_2 (.D(Input_l), .en(on26), .Q(x26), .clk(clock));  // open: clr
  Register #(.width(32)) x27_2 (.D(Input_l), .en(on27), .Q(x27), .clk(clock));  // open: clr
  Register #(.width(32)) x28_2 (.D(Input_l), .en(on28), .Q(x28), .clk(clock));  // open: clr
  Register #(.width(32)) x29_2 (.D(Input_l), .en(on29), .Q(x29), .clk(clock));  // open: clr
  Register #(.width(32)) x30_2 (.D(Input_l), .en(on30), .Q(x30), .clk(clock));  // open: clr
  Register #(.width(32)) x31_2 (.D(Input_l), .en(on31), .Q(x31), .clk(clock));  // open: clr
  not not_81 (not_81_out, xd[0]);
  and and_31 (on30, not_81_out, xd[1], xd[2], xd[3], xd[4]);
  and and_32 (on31, xd[0], xd[1], xd[2], xd[3], xd[4]);
  Multiplexer #(.select(5), .width(32)) multiplexer_3 (
    .in0(x0), .in1(x1), .in2(x2), .in3(x3), .in4(x4), .in5(x5), .in6(x6), .in7(x7), .in8(x8), .in9(x9),
    .in10(x10), .in11(x11), .in12(x12), .in13(x13), .in14(x14), .in15(x15), .in16(x16), .in17(x17),
    .in18(x18), .in19(x19), .in20(x20), .in21(x21), .in22(x22), .in23(x23), .in24(x24), .in25(x25),
    .in26(x26), .in27(x27), .in28(x28), .in29(x29), .in30(x30), .in31(x31), .out(output_xn_low), .sel(xn),
    .en(1'b1));
  Multiplexer #(.select(5), .width(32)) multiplexer_4 (
    .in0(x0), .in1(x1), .in2(x2), .in3(x3), .in4(x4), .in5(x5), .in6(x6), .in7(x7), .in8(x8), .in9(x9),
    .in10(x10), .in11(x11), .in12(x12), .in13(x13), .in14(x14), .in15(x15), .in16(x16), .in17(x17),
    .in18(x18), .in19(x19), .in20(x20), .in21(x21), .in22(x22), .in23(x23), .in24(x24), .in25(x25),
    .in26(x26), .in27(x27), .in28(x28), .in29(x29), .in30(x30), .in31(x31), .out(output_xm_low), .sel(xm),
    .en(1'b1));
endmodule

module Banderas (
  input  input_z,
  input  input_n,
  input  input_c,
  input  input_v,
  input  clock,
  input  on,
  output output_z,
  output output_n,
  output output_c,
  output output_v
);

  Register #(.width(1)) Z (.D(input_z), .en(on), .Q(output_z), .clk(clock));  // open: clr
  Register #(.width(1)) C (.D(input_c), .en(on), .Q(output_c), .clk(clock));  // open: clr
  Register #(.width(1)) N (.D(input_n), .en(on), .Q(output_n), .clk(clock));  // open: clr
  Register #(.width(1)) V (.D(input_v), .en(on), .Q(output_v), .clk(clock));  // open: clr
endmodule

module Decoder_B (
  input  [31:0] instruction,
  output CBZ_B,
  output CBNZ_B,
  output B__EQ_B,
  output B__NE_B,
  output B__HS_B,
  output B__LO_B,
  output B__MI_B,
  output B__PL_B,
  output B__VS_B,
  output B__VC_B,
  output B__HI_B,
  output B__LS_B,
  output B__GE_B,
  output B__LT_B,
  output B__GT_B,
  output B__LE_B,
  output B,
  output BL
);

  wire not_1_out, not_2_out, not_3_out, not_4_out, not_5_out, not_6_out, not_7_out, not_8_out, not_9_out,
       not_10_out, not_11_out, not_12_out, not_13_out, not_14_out, not_15_out, not_16_out, not_17_out,
       not_18_out, not_19_out, not_20_out, not_21_out, not_22_out, not_23_out, not_24_out, not_25_out,
       not_26_out, not_27_out, not_28_out, not_29_out, not_30_out, not_31_out, not_32_out, not_33_out,
       not_34_out, not_35_out, not_36_out, not_37_out, not_38_out, not_39_out, not_40_out, not_41_out,
       not_42_out, not_43_out, not_44_out, not_45_out, not_46_out, not_47_out, not_48_out, not_49_out,
       not_50_out, not_51_out, not_52_out, not_53_out, not_54_out, not_55_out, not_56_out, not_57_out,
       not_58_out, not_59_out, not_60_out, not_61_out, not_62_out, not_63_out, not_64_out, not_65_out,
       not_66_out, not_67_out, not_68_out, not_69_out, not_70_out, not_71_out, not_72_out, not_73_out,
       not_74_out, not_75_out, not_76_out, not_77_out, not_78_out, not_79_out, not_80_out, not_81_out,
       not_82_out, not_83_out, not_84_out, not_85_out, not_86_out, not_87_out, not_88_out, not_89_out,
       not_90_out, not_91_out, not_92_out, not_93_out, not_94_out, not_95_out, not_96_out, not_97_out,
       not_98_out, not_99_out, not_100_out, not_101_out, not_102_out, not_103_out, not_104_out, not_105_out,
       not_106_out, not_107_out, not_108_out, not_109_out, not_110_out, not_111_out, not_112_out,
       not_113_out, not_114_out, not_115_out, not_116_out, not_117_out, not_118_out, not_119_out,
       not_120_out, not_121_out, not_122_out, not_123_out, not_124_out, not_125_out, not_126_out,
       not_127_out, not_128_out, not_129_out;

  not not_1 (not_1_out, instruction[30]);
  not not_2 (not_2_out, instruction[25]);
  not not_3 (not_3_out, instruction[24]);
  not not_4 (not_4_out, instruction[27]);
  and and_1 (CBZ_B, instruction[31], not_1_out, instruction[29], instruction[28], not_4_out, instruction[26], not_2_out, not_3_out);
  not not_5 (not_5_out, instruction[27]);
  not not_6 (not_6_out, instruction[25]);
  not not_7 (not_7_out, instruction[30]);
  and and_2 (CBNZ_B, instruction[31], not_7_out, instruction[29], instruction[28], not_5_out, instruction[26], not_6_out, instruction[24]);
  not not_8 (not_8_out, instruction[27]);
  not not_9 (not_9_out, instruction[29]);
  not not_10 (not_10_out, instruction[31]);
  not not_11 (not_11_out, instruction[3]);
  not not_12 (not_12_out, instruction[4]);
  not not_13 (not_13_out, instruction[24]);
  not not_14 (not_14_out, instruction[0]);
  not not_15 (not_15_out, instruction[25]);
  not not_16 (not_16_out, instruction[2]);
  not not_17 (not_17_out, instruction[1]);
  and and_3 (B__EQ_B, not_10_out, instruction[30], not_9_out, instruction[28], not_8_out, instruction[26], not_15_out, not_13_out, not_12_out, not_11_out, not_16_out, not_17_out, not_14_out);
  not not_18 (not_18_out, instruction[27]);
  not not_19 (not_19_out, instruction[24]);
  not not_20 (not_20_out, instruction[29]);
  not not_21 (not_21_out, instruction[25]);
  not not_22 (not_22_out, instruction[31]);
  and and_4 (B__NE_B, not_22_out, instruction[30], not_20_out, instruction[28], not_18_out, instruction[26], not_21_out, not_19_out, not_24_out, not_26_out, not_23_out, not_25_out, instruction[0]);
  not not_23 (not_23_out, instruction[2]);
  not not_24 (not_24_out, instruction[4]);
  not not_25 (not_25_out, instruction[1]);
  not not_26 (not_26_out, instruction[3]);
  not not_27 (not_27_out, instruction[31]);
  not not_28 (not_28_out, instruction[29]);
  not not_29 (not_29_out, instruction[27]);
  not not_30 (not_30_out, instruction[25]);
  not not_31 (not_31_out, instruction[3]);
  not not_32 (not_32_out, instruction[4]);
  not not_33 (not_33_out, instruction[24]);
  and and_5 (B__HS_B, not_27_out, instruction[30], not_28_out, instruction[28], not_29_out, instruction[26], not_30_out, not_33_out, not_32_out, not_31_out, not_37_out, instruction[1], not_34_out);
  not not_34 (not_34_out, instruction[0]);
  not not_35 (not_35_out, instruction[29]);
  not not_36 (not_36_out, instruction[31]);
  not not_37 (not_37_out, instruction[2]);
  not not_38 (not_38_out, instruction[24]);
  not not_39 (not_39_out, instruction[4]);
  not not_40 (not_40_out, instruction[2]);
  not not_41 (not_41_out, instruction[25]);
  not not_42 (not_42_out, instruction[27]);
  not not_43 (not_43_out, instruction[3]);
  and and_6 (B__LO_B, not_36_out, instruction[30], not_35_out, instruction[28], not_42_out, instruction[26], not_41_out, not_38_out, not_39_out, not_43_out, not_40_out, instruction[1], instruction[0]);
  not not_44 (not_44_out, instruction[31]);
  not not_45 (not_45_out, instruction[27]);
  not not_46 (not_46_out, instruction[29]);
  not not_47 (not_47_out, instruction[25]);
  not not_48 (not_48_out, instruction[4]);
  not not_49 (not_49_out, instruction[24]);
  not not_50 (not_50_out, instruction[1]);
  not not_51 (not_51_out, instruction[0]);
  not not_52 (not_52_out, instruction[3]);
  and and_7 (B__MI_B, not_44_out, instruction[30], not_46_out, instruction[28], not_45_out, instruction[26], not_47_out, not_49_out, not_48_out, not_52_out, instruction[2], not_50_out, not_51_out);
  not not_53 (not_53_out, instruction[25]);
  not not_54 (not_54_out, instruction[31]);
  not not_55 (not_55_out, instruction[29]);
  not not_56 (not_56_out, instruction[27]);
  not not_57 (not_57_out, instruction[24]);
  and and_8 (B__PL_B, not_54_out, instruction[30], not_55_out, instruction[28], not_56_out, instruction[26], not_53_out, not_57_out, not_61_out, not_59_out, instruction[2], not_60_out, instruction[0]);
  not not_58 (not_58_out, instruction[31]);
  not not_59 (not_59_out, instruction[3]);
  not not_60 (not_60_out, instruction[1]);
  not not_61 (not_61_out, instruction[4]);
  not not_62 (not_62_out, instruction[25]);
  not not_63 (not_63_out, instruction[4]);
  not not_64 (not_64_out, instruction[29]);
  not not_65 (not_65_out, instruction[27]);
  not not_66 (not_66_out, instruction[3]);
  not not_67 (not_67_out, instruction[24]);
  and and_9 (B__VS_B, not_58_out, instruction[30], not_64_out, instruction[28], not_65_out, instruction[26], not_62_out, not_67_out, not_63_out, not_66_out, instruction[2], instruction[1], not_70_out);
  not not_68 (not_68_out, instruction[31]);
  not not_69 (not_69_out, instruction[29]);
  not not_70 (not_70_out, instruction[0]);
  not not_71 (not_71_out, instruction[4]);
  not not_72 (not_72_out, instruction[27]);
  not not_73 (not_73_out, instruction[25]);
  not not_74 (not_74_out, instruction[3]);
  not not_75 (not_75_out, instruction[24]);
  and and_10 (B__VC_B, not_68_out, instruction[30], not_69_out, instruction[28], not_72_out, instruction[26], not_73_out, not_75_out, not_71_out, not_74_out, instruction[2], instruction[1], instruction[0]);
  not not_76 (not_76_out, instruction[29]);
  not not_77 (not_77_out, instruction[27]);
  not not_78 (not_78_out, instruction[31]);
  not not_79 (not_79_out, instruction[0]);
  not not_80 (not_80_out, instruction[1]);
  not not_81 (not_81_out, instruction[24]);
  not not_82 (not_82_out, instruction[2]);
  not not_83 (not_83_out, instruction[4]);
  not not_84 (not_84_out, instruction[25]);
  and and_11 (B__HI_B, not_78_out, instruction[30], not_76_out, instruction[28], not_77_out, instruction[26], not_84_out, not_81_out, not_83_out, instruction[3], not_82_out, not_80_out, not_79_out);
  not not_85 (not_85_out, instruction[24]);
  not not_86 (not_86_out, instruction[27]);
  not not_87 (not_87_out, instruction[31]);
  not not_88 (not_88_out, instruction[29]);
  not not_89 (not_89_out, instruction[25]);
  and and_12 (B__LS_B, not_87_out, instruction[30], not_88_out, instruction[28], not_86_out, instruction[26], not_89_out, not_85_out, not_91_out, instruction[3], not_92_out, not_93_out, instruction[0]);
  not not_90 (not_90_out, instruction[31]);
  not not_91 (not_91_out, instruction[4]);
  not not_92 (not_92_out, instruction[2]);
  not not_93 (not_93_out, instruction[1]);
  not not_94 (not_94_out, instruction[29]);
  not not_95 (not_95_out, instruction[25]);
  not not_96 (not_96_out, instruction[24]);
  not not_97 (not_97_out, instruction[27]);
  not not_98 (not_98_out, instruction[4]);
  and and_13 (B__GE_B, not_90_out, instruction[30], not_94_out, instruction[28], not_97_out, instruction[26], not_95_out, not_96_out, not_98_out, instruction[3], not_100_out, instruction[1], not_101_out);
  not not_99 (not_99_out, instruction[29]);
  not not_100 (not_100_out, instruction[2]);
  not not_101 (not_101_out, instruction[0]);
  not not_102 (not_102_out, instruction[31]);
  not not_103 (not_103_out, instruction[24]);
  not not_104 (not_104_out, instruction[25]);
  not not_105 (not_105_out, instruction[4]);
  not not_106 (not_106_out, instruction[27]);
  not not_107 (not_107_out, instruction[2]);
  and and_14 (B__LT_B, not_102_out, instruction[30], not_99_out, instruction[28], not_106_out, instruction[26], not_104_out, not_103_out, not_105_out, instruction[3], not_107_out, instruction[1], instruction[0]);
  not not_108 (not_108_out, instruction[27]);
  not not_109 (not_109_out, instruction[31]);
  not not_110 (not_110_out, instruction[29]);
  not not_111 (not_111_out, instruction[24]);
  not not_112 (not_112_out, instruction[1]);
  not not_113 (not_113_out, instruction[0]);
  not not_114 (not_114_out, instruction[25]);
  not not_115 (not_115_out, instruction[4]);
  and and_15 (B__GT_B, not_109_out, instruction[30], not_110_out, instruction[28], not_108_out, instruction[26], not_114_out, not_111_out, not_115_out, instruction[3], instruction[2], not_112_out, not_113_out);
  not not_116 (not_116_out, instruction[29]);
  not not_117 (not_117_out, instruction[31]);
  not not_118 (not_118_out, instruction[27]);
  not not_119 (not_119_out, instruction[24]);
  not not_120 (not_120_out, instruction[25]);
  and and_16 (B__LE_B, not_117_out, instruction[30], not_116_out, instruction[28], not_118_out, instruction[26], not_120_out, not_119_out, not_124_out, instruction[3], instruction[2], not_121_out, instruction[0]);
  not not_121 (not_121_out, instruction[1]);
  not not_122 (not_122_out, instruction[30]);
  not not_123 (not_123_out, instruction[31]);
  not not_124 (not_124_out, instruction[4]);
  not not_125 (not_125_out, instruction[27]);
  not not_126 (not_126_out, instruction[29]);
  not not_127 (not_127_out, instruction[30]);
  and and_17 (B, not_123_out, not_122_out, not_126_out, instruction[28], not_125_out, instruction[26]);
  not not_128 (not_128_out, instruction[29]);
  not not_129 (not_129_out, instruction[27]);
  and and_18 (BL, instruction[31], not_127_out, not_128_out, instruction[28], not_129_out, instruction[26]);
endmodule

// Decoder str ldr
module Decoder_STR_o_LDR (
  input  [31:0] instruction,
  output STR,
  output LDR
);

  wire not_1_out, not_2_out, not_3_out, not_4_out, not_5_out, not_6_out, not_7_out;

  not not_1 (not_1_out, instruction[25]);
  and and_1 (STR, instruction[30], instruction[29], instruction[28], instruction[27], instruction[26], not_1_out, not_4_out, instruction[23], not_2_out, not_3_out);
  not not_2 (not_2_out, instruction[22]);
  not not_3 (not_3_out, instruction[21]);
  not not_4 (not_4_out, instruction[24]);
  not not_5 (not_5_out, instruction[22]);
  not not_6 (not_6_out, instruction[25]);
  not not_7 (not_7_out, instruction[24]);
  and and_2 (LDR, instruction[30], instruction[29], instruction[28], instruction[27], instruction[26], not_6_out, not_7_out, instruction[23], not_5_out, instruction[21]);
endmodule

module RET (
  input  [31:0] instruction,
  output RET
);

  wire not_1_out, not_2_out, not_3_out, not_4_out, not_5_out, not_6_out, not_7_out, not_8_out, not_9_out,
       not_10_out, not_11_out, not_12_out, not_13_out, not_14_out, not_15_out, not_16_out, not_17_out;

  not not_1 (not_1_out, instruction[27]);
  not not_2 (not_2_out, instruction[29]);
  not not_3 (not_3_out, instruction[24]);
  not not_4 (not_4_out, instruction[23]);
  not not_5 (not_5_out, instruction[21]);
  not not_6 (not_6_out, instruction[14]);
  not not_7 (not_7_out, instruction[12]);
  not not_8 (not_8_out, instruction[13]);
  not not_9 (not_9_out, instruction[15]);
  and and_1 (RET, instruction[31], instruction[30], not_2_out, instruction[28], not_1_out, instruction[26], instruction[25], not_3_out, not_4_out, instruction[22], not_5_out, instruction[20], instruction[19], instruction[18], instruction[17], instruction[16], not_9_out, not_6_out, not_8_out, not_7_out, not_11_out, not_13_out, instruction[9], instruction[8], instruction[7], instruction[6], not_12_out, not_10_out, not_17_out, not_14_out, not_16_out, not_15_out);
  not not_10 (not_10_out, instruction[4]);
  not not_11 (not_11_out, instruction[11]);
  not not_12 (not_12_out, instruction[5]);
  not not_13 (not_13_out, instruction[10]);
  not not_14 (not_14_out, instruction[2]);
  not not_15 (not_15_out, instruction[0]);
  not not_16 (not_16_out, instruction[1]);
  not not_17 (not_17_out, instruction[3]);
endmodule

module R_menos_shift (
  input  [31:0] instruccion,
  input  [3:0] control,
  input  CLOCK
);

  wire registros_orden_1_p4, registros_orden_1_p5, registros_orden_1_p7, registros_orden_1_p8,
       registros_orden_1_p9, registros_orden_1_p10;
  wire [31:0] bit_extender_1_out;

  // Registros_orden registros_orden_1: pin names not known; wires that end beside it: instruccion[4:0], instruccion[20:16], instruccion[9:5], registros_orden_1_p4, registros_orden_1_p5, CLOCK, registros_orden_1_p7, registros_orden_1_p8, registros_orden_1_p9, registros_orden_1_p10
  assign bit_extender_1_out = {{30{1'b0}}, instruccion[23:22]};  // Bit_Extender bit_extender_1
  // ALU alu_1: pin names not known; wires that end beside it: registros_orden_1_p5, control, registros_orden_1_p4, bit_extender_1_out, registros_orden_1_p9, registros_orden_1_p10, registros_orden_1_p7, registros_orden_1_p8
endmodule

module ALU_I (
  input  [31:0] input1_high,
  input  [31:0] input2_high,
  input  [31:0] input1_low,
  input  [31:0] input2_low
);

  wire adder_2_cout, subtractor_2_bout;
  wire [31:0] adder_1_out, subtractor_1_out;

  Adder #(.width(32)) adder_1 (.a(input1_high), .b(input2_high), .out(adder_1_out), .cin(adder_2_cout));  // open: cout
  Subtractor #(.width(32)) subtractor_1 (
    .a(input1_high), .b(input2_high), .out(subtractor_1_out), .bin(subtractor_2_bout));  // open: bout
  Adder #(.width(32)) adder_2 (.a(input1_low), .b(input2_low), .cout(adder_2_cout));  // open: out, cin
  Subtractor #(.width(32)) subtractor_2 (.a(input1_low), .b(input2_low), .bout(subtractor_2_bout));  // open: out, bin
  Multiplexer #(.select(4), .width(32)) multiplexer_1 (
    .in0(adder_1_out), .in1(subtractor_1_out));  // open: in2, in3, in4, in5, in6, in7, in8, in9, in10, in11, in12, in13, in14, in15, out, sel, en
endmodule

module asrv (
  input  [31:0] r1h,
  input  [31:0] rl1,
  input  [31:0] rl2,
  input  [31:0] r2h,
  output [31:0] HIGHP,
  output [31:0] LowP,
  output [31:0] out_7
);

  wire comparator_1_gt, comparator_1_lt, comparator_2_gt, comparator_2_lt, \if , not_1_out, or_1_out;
  wire [4:0] subtractor_1_out;
  wire [31:0] multiplexer_1_out, multiplexer_2_out, shifter_1_out, shifter_3_out, shifter_4_out,
       shifter_5_out, xor_1_out;

  Comparator #(.width(26)) comparator_1 (
    .a(rl2[31:6]), .b({26{1'b0}}), .gt(comparator_1_gt), .lt(comparator_1_lt));  // open: eq
  Comparator #(.width(32)) comparator_2 (
    .a(r2h), .b({32{1'b0}}), .gt(comparator_2_gt), .lt(comparator_2_lt));  // open: eq
  Subtractor #(.width(5)) subtractor_1 (.a({5{1'b1}}), .b(rl2[4:0]), .out(subtractor_1_out));  // open: bin, bout
  Shifter #(.width(32)) shifter_1 (.in(r1h), .\dist (subtractor_1_out), .out(shifter_1_out));
  Comparator #(.width(6)) comparator_3 (.a(rl2[5:0]), .b({6{1'b0}}), .lt(\if ));  // open: gt, eq
  or or_1 (or_1_out, comparator_1_gt, comparator_1_lt, comparator_2_gt, comparator_2_lt);
  Shifter #(.width(32)) shifter_2 (.in(shifter_1_out), .\dist (5'b00001), .out(out_7));
  Shifter #(.width(32), .shift("lr")) shifter_3 (.in(rl1), .\dist (rl2[4:0]), .out(shifter_3_out));
  Shifter #(.width(32), .shift("ar")) shifter_4 (.in(r1h), .\dist (rl2[4:0]), .out(shifter_4_out));
  assign xor_1_out = shifter_3_out ^ out_7;  // XOR_Gate xor_1, 32 bits wide
  not not_1 (not_1_out, \if );
  Multiplexer #(.width(32), .enable("false")) multiplexer_1 (
    .in0(shifter_4_out), .in1(xor_1_out), .out(multiplexer_1_out), .sel(not_1_out));
  Shifter #(.width(32), .shift("ar")) shifter_5 (.in(r1h), .\dist (rl2[4:0]), .out(shifter_5_out));
  Multiplexer #(.width(32), .enable("false")) multiplexer_2 (
    .in0(shifter_5_out), .in1({32{1'b1}}), .out(multiplexer_2_out), .sel(\if ));
  Multiplexer #(.width(32), .enable("false")) multiplexer_3 (
    .in0(multiplexer_1_out), .in1({32{1'b0}}), .out(LowP), .sel(or_1_out));
  Multiplexer #(.width(32), .enable("false")) multiplexer_4 (
    .in0(multiplexer_2_out), .in1({32{1'b0}}), .out(HIGHP), .sel(or_1_out));

  // Other names for the same wires on the sheet: High[31:0] = r1h; HIGHP_t[31:0] = r1h; low[31:0] = rl1;
  //   ph2[31:0] = out_7; change[4:0] = rl2[4:0]; ph[4:0] = rl2[4:0]
endmodule

module rorv (
  input  [31:0] r1h,
  input  [31:0] rl1,
  input  [31:0] rl2,
  output [31:0] HIGHP,
  output [31:0] out_5,
  output [31:0] out_6,
  output [31:0] out_7
);

  wire \if , not_1_out;
  wire [4:0] subtractor_1_out, subtractor_2_out;
  wire [31:0] multiplexer_2_out, shifter_1_out, shifter_3_out, shifter_4_out, shifter_5_out, shifter_7_out,
       xor_1_out;

  Subtractor #(.width(5)) subtractor_1 (.a({5{1'b1}}), .b(rl2[4:0]), .out(subtractor_1_out));  // open: bin, bout
  Shifter #(.width(32)) shifter_1 (.in(r1h), .\dist (subtractor_1_out), .out(shifter_1_out));
  Comparator #(.width(6)) comparator_1 (.a(rl2[5:0]), .b({6{1'b0}}), .lt(\if ));  // open: gt, eq
  Shifter #(.width(32)) shifter_2 (.in(shifter_1_out), .\dist (5'b00001), .out(out_5));
  Shifter #(.width(32), .shift("lr")) shifter_3 (.in(rl1), .\dist (rl2[4:0]), .out(shifter_3_out));
  Subtractor #(.width(5)) subtractor_2 (.a({5{1'b1}}), .b(rl2[4:0]), .out(subtractor_2_out));  // open: bin, bout
  Shifter #(.width(32), .shift("lr")) shifter_4 (.in(r1h), .\dist (rl2[4:0]), .out(shifter_4_out));
  Shifter #(.width(32)) shifter_5 (.in(rl1), .\dist (subtractor_2_out), .out(shifter_5_out));
  assign xor_1_out = shifter_3_out ^ out_5;  // XOR_Gate xor_1, 32 bits wide
  Multiplexer #(.width(32), .enable("false")) multiplexer_1 (
    .in0(shifter_4_out), .in1(xor_1_out), .out(out_6), .sel(not_1_out));
  not not_1 (not_1_out, \if );
  Shifter #(.width(32)) shifter_6 (.in(shifter_5_out), .\dist (5'b00001), .out(out_7));
  Shifter #(.width(32), .shift("ar")) shifter_7 (.in(r1h), .\dist (rl2[4:0]), .out(shifter_7_out));
  Multiplexer #(.width(32), .enable("false")) multiplexer_2 (
    .in0(shifter_7_out), .in1(rl1), .out(multiplexer_2_out), .sel(\if ));
  assign HIGHP = multiplexer_2_out ^ out_7;  // XOR_Gate xor_2, 32 bits wide

  // Other names for the same wires on the sheet: High[31:0] = r1h; HIGHP_t[31:0] = r1h; low[31:0] = rl1;
  //   ph2[31:0] = out_5; ph3[31:0] = out_7; change[4:0] = rl2[4:0]; ph[4:0] = rl2[4:0]
endmodule

module EXTENDER_32_64 (
  input  [31:0] INPUT,
  output [31:0] LOW,
  output [31:0] HIGH
);

  Bit_Extender #(.in_width(32), .out_width(32)) bit_extender_1 (.in(INPUT), .out(LOW));

  assign HIGH = {32{1'b0}};
endmodule
